// Logisim project Projet.circ as structural Verilog
module main (
);

  A a_1 ();  // open: Sous_systeme, CLK, out_3, out_4, out_5, out_6
endmodule

module A (
  input  Sous_systeme,
  input  CLK,
  output [22:0] out_3,
  output [6:0] out_4,
  output [2:0] out_5,
  output [3:0] out_6
);

  wire alarme_1_sous_systeme, chronometre_1_sous_systeme, clock_1_out, or_1_out;
  wire [1:0] button_1_out;
  wire [3:0] a_boutons_1_bc1;
  wire [7:0] alarme_1_seg0, alarme_1_seg1, alarme_1_seg2, alarme_1_seg3, alarme_1_seg4, alarme_1_seg5,
       chronometre_1_seg0, chronometre_1_seg1, chronometre_1_seg2, chronometre_1_seg3, chronometre_1_seg4,
       chronometre_1_seg5, heure_1_seg0, heure_1_seg1, heure_1_seg2, heure_1_seg3, heure_1_seg4,
       heure_1_seg5, undriven, undriven_2, undriven_3, undriven_4, undriven_5, undriven_6;
  wire [23:0] Debut_7seg, Fin_7seg;

  Button button_1 (.out(button_1_out[0]));
  Button button_2 (.out(button_1_out[1]));
  Clock clock_1 (.out(clock_1_out));
  A_temps a_temps_1 (.TempsIN(out_3), .CLK(clock_1_out), .TEMPSOUT(out_3));
  A_Boutons a_boutons_1 (
    .Bouton1(button_1_out[0]), .Bouton2(button_1_out[1]), .CLK(clock_1_out), .BC1(a_boutons_1_bc1[0]),
    .BL1(a_boutons_1_bc1[1]), .BC2(a_boutons_1_bc1[2]), .BL2(a_boutons_1_bc1[3]));
  A_def_etat a_def_etat_1 (
    .Boutons_IN(a_boutons_1_bc1), .Etat_IN(out_5), .sous_Etat(or_1_out), .CLK(clock_1_out), .Etat_OUT(out_5),
    .Boutons_OUT(out_6));
  or or_1 (or_1_out, alarme_1_sous_systeme, chronometre_1_sous_systeme);
  Heure heure_1 (
    .Boutons(out_6), .Temps(out_3), .Etat(out_5), .Seg0(heure_1_seg0), .Seg1(heure_1_seg1),
    .Seg2(heure_1_seg2), .Seg3(heure_1_seg3), .Seg4(heure_1_seg4), .Seg5(heure_1_seg5));
  Alarme alarme_1 (
    .Temps(out_3), .Boutons(out_6), .Etat(out_5), .LEDs(out_4), .Seg0(alarme_1_seg0), .Seg1(alarme_1_seg1),
    .Seg2(alarme_1_seg2), .Seg3(alarme_1_seg3), .Seg4(alarme_1_seg4), .Seg5(alarme_1_seg5),
    .Sous_systeme(alarme_1_sous_systeme));  // open: Sonne
  Chronometre chronometre_1 (
    .Temps(out_3), .Boutons(out_6), .Etat(out_5), .Seg0(chronometre_1_seg0), .Seg1(chronometre_1_seg1),
    .Seg2(chronometre_1_seg2), .Seg3(chronometre_1_seg3), .Seg4(chronometre_1_seg4),
    .Seg5(chronometre_1_seg5), .Sous_systeme(chronometre_1_sous_systeme));
  Multiplexer #(.select(3), .width(24), .enable("false")) multiplexer_1 (
    .in0({heure_1_seg2, heure_1_seg1, heure_1_seg0}), .in1({alarme_1_seg2, alarme_1_seg1, alarme_1_seg0}),
    .in2({chronometre_1_seg2, chronometre_1_seg1, chronometre_1_seg0}),
    .in3({undriven_6, undriven_5, undriven_4}), .out(Fin_7seg), .sel(out_5));  // open: in4, in5, in6, in7
  Multiplexer #(.select(3), .width(24), .enable("false")) multiplexer_2 (
    .in0({heure_1_seg5, heure_1_seg4, heure_1_seg3}), .in1({alarme_1_seg5, alarme_1_seg4, alarme_1_seg3}),
    .in2({chronometre_1_seg5, chronometre_1_seg4, chronometre_1_seg3}),
    .in3({undriven_3, undriven_2, undriven}), .out(Debut_7seg), .sel(out_5));  // open: in4, in5, in6, in7
  _7_Segment_Display u_7_segment_display_1 (
    .g(Fin_7seg[3]), .f(Fin_7seg[2]), .a(Fin_7seg[1]), .b(Fin_7seg[0]), .e(Fin_7seg[7]), .d(Fin_7seg[6]),
    .c(Fin_7seg[5]), .dp(Fin_7seg[4]));
  _7_Segment_Display u_7_segment_display_2 (
    .g(Fin_7seg[11]), .f(Fin_7seg[10]), .a(Fin_7seg[9]), .b(Fin_7seg[8]), .e(Fin_7seg[15]), .d(Fin_7seg[14]),
    .c(Fin_7seg[13]), .dp(Fin_7seg[12]));
  _7_Segment_Display u_7_segment_display_3 (
    .g(Fin_7seg[19]), .f(Fin_7seg[18]), .a(Fin_7seg[17]), .b(Fin_7seg[16]), .e(Fin_7seg[23]),
    .d(Fin_7seg[22]), .c(Fin_7seg[21]), .dp(Fin_7seg[20]));
  _7_Segment_Display u_7_segment_display_4 (
    .g(Debut_7seg[3]), .f(Debut_7seg[2]), .a(Debut_7seg[1]), .b(Debut_7seg[0]), .e(Debut_7seg[7]),
    .d(Debut_7seg[6]), .c(Debut_7seg[5]), .dp(Debut_7seg[4]));
  _7_Segment_Display u_7_segment_display_5 (
    .g(Debut_7seg[11]), .f(Debut_7seg[10]), .a(Debut_7seg[9]), .b(Debut_7seg[8]), .e(Debut_7seg[15]),
    .d(Debut_7seg[14]), .c(Debut_7seg[13]), .dp(Debut_7seg[12]));
  _7_Segment_Display u_7_segment_display_6 (
    .g(Debut_7seg[19]), .f(Debut_7seg[18]), .a(Debut_7seg[17]), .b(Debut_7seg[16]), .e(Debut_7seg[23]),
    .d(Debut_7seg[22]), .c(Debut_7seg[21]), .dp(Debut_7seg[20]));
  LED led_1 (.in(out_4[0]));
  LED led_2 (.in(out_4[1]));
  LED led_3 (.in(out_4[2]));
  LED led_4 (.in(out_4[3]));
  LED led_5 (.in(out_4[5]));
  LED led_6 (.in(out_4[4]));
  LED led_7 (.in(out_4[6]));
endmodule

module A_Boutons (
  input  Bouton1,
  input  Bouton2,
  input  CLK,
  output BC1,
  output BL1,
  output BC2,
  output BL2
);

  wire and_1_out, and_2_out, and_3_out, and_4_out, d_ff_1_q, d_ff_2_q, d_ff_3_q, d_ff_4_q, d_ff_5_q,
       d_ff_6_q, d_ff_7_q, d_ff_8_q, d_ff_9_q, d_ff_10_q, d_ff_11_q, d_ff_12_q, d_ff_13_q, d_ff_14_q,
       d_ff_15_q, d_ff_16_q, undriven, undriven_2;

  D_Flip_Flop d_ff_1 (.D(Bouton1), .clk(CLK), .Q(d_ff_1_q));  // open: Qn, preset, reset
  D_Flip_Flop d_ff_2 (.D(Bouton2), .clk(CLK), .Q(d_ff_2_q));  // open: Qn, preset, reset
  D_Flip_Flop d_ff_3 (.D(d_ff_1_q), .clk(CLK), .Q(d_ff_3_q));  // open: Qn, preset, reset
  D_Flip_Flop d_ff_4 (.D(d_ff_2_q), .clk(CLK), .Q(d_ff_4_q));  // open: Qn, preset, reset
  D_Flip_Flop d_ff_5 (.D(d_ff_3_q), .clk(CLK), .Q(d_ff_5_q));  // open: Qn, preset, reset
  D_Flip_Flop d_ff_6 (.D(d_ff_4_q), .clk(CLK), .Q(d_ff_6_q));  // open: Qn, preset, reset
  and and_1 (and_1_out, ~d_ff_1_q, d_ff_3_q);  // AND_Gate
  D_Flip_Flop d_ff_7 (.D(d_ff_5_q), .clk(CLK), .Q(d_ff_7_q));  // open: Qn, preset, reset
  and and_2 (and_2_out, ~d_ff_2_q, d_ff_4_q);  // AND_Gate
  D_Flip_Flop d_ff_8 (.D(d_ff_6_q), .clk(CLK), .Q(d_ff_8_q));  // open: Qn, preset, reset
  D_Flip_Flop d_ff_9 (.D(d_ff_7_q), .clk(CLK), .Q(d_ff_9_q));  // open: Qn, preset, reset
  D_Flip_Flop d_ff_10 (.D(d_ff_8_q), .clk(CLK), .Q(d_ff_10_q));  // open: Qn, preset, reset
  D_Flip_Flop d_ff_11 (.D(d_ff_9_q), .clk(CLK), .Q(d_ff_11_q));  // open: Qn, preset, reset
  D_Flip_Flop d_ff_12 (.D(d_ff_10_q), .clk(CLK), .Q(d_ff_12_q));  // open: Qn, preset, reset
  D_Flip_Flop d_ff_13 (.D(d_ff_11_q), .clk(CLK), .Q(d_ff_13_q));  // open: Qn, preset, reset
  D_Flip_Flop d_ff_14 (.D(d_ff_12_q), .clk(CLK), .Q(d_ff_14_q));  // open: Qn, preset, reset
  D_Flip_Flop d_ff_15 (.D(d_ff_13_q), .clk(CLK), .Q(d_ff_15_q), .reset(undriven));  // open: Qn, preset
  D_Flip_Flop d_ff_16 (.D(d_ff_14_q), .clk(CLK), .Q(d_ff_16_q), .reset(undriven_2));  // open: Qn, preset
  and and_3 (and_3_out, d_ff_5_q, d_ff_7_q, d_ff_9_q, d_ff_11_q, d_ff_13_q, d_ff_15_q);
  and and_4 (and_4_out, d_ff_6_q, d_ff_8_q, d_ff_10_q, d_ff_12_q, d_ff_14_q, d_ff_16_q);
  and and_5 (BC1, ~and_3_out, and_1_out);  // AND_Gate
  and and_6 (BL1, and_3_out, and_1_out);
  and and_7 (BC2, ~and_4_out, and_2_out);  // AND_Gate
  and and_8 (BL2, and_4_out, and_2_out);
endmodule

module A_temps (
  input  [22:0] TempsIN,
  input  CLK,
  output [22:0] TEMPSOUT
);

  wire comparator_1_eq;
  wire [22:0] adder_1_out, register_1_q;

  Adder #(.width(23)) adder_1 (.a(TempsIN), .b(23'h1), .out(adder_1_out));  // open: cin, cout
  Register #(.width(23)) register_1 (.D(adder_1_out), .clk(CLK), .Q(register_1_q));  // open: en, clr
  Comparator #(.width(23), .mode("unsigned")) comparator_1 (
    .a(register_1_q), .b(23'h5c4900), .eq(comparator_1_eq));  // open: gt, lt
  Multiplexer #(.width(23), .enable("false")) multiplexer_1 (
    .in0(register_1_q), .in1({23{1'b0}}), .out(TEMPSOUT), .sel(comparator_1_eq));
endmodule

module A_def_etat (
  input  [3:0] Boutons_IN,
  input  [2:0] Etat_IN,
  input  sous_Etat,
  input  CLK,
  output [2:0] Etat_OUT,
  output [3:0] Boutons_OUT
);

  wire and_2_out, and_3_out, not_1_out, not_2_out, not_3_out, not_4_out, not_5_out, not_6_out, or_1_out;
  wire [1:0] and_4_out;
  wire [2:0] multiplexer_1_out;

  not not_1 (not_1_out, Etat_IN[2]);
  not not_2 (not_2_out, Etat_IN[1]);
  not not_3 (not_3_out, Etat_IN[2]);
  not not_4 (not_4_out, Etat_IN[0]);
  not not_5 (not_5_out, Etat_IN[2]);
  not not_6 (not_6_out, Etat_IN[0]);
  or or_1 (or_1_out, sous_Etat, ~Boutons_IN[0]);  // OR_Gate
  and and_1 (Boutons_OUT[0], sous_Etat, Boutons_IN[0]);
  and and_2 (and_2_out, not_1_out, not_2_out, Etat_IN[0]);
  or or_2 (and_4_out[1], and_2_out, and_3_out);
  and and_3 (and_3_out, not_3_out, Etat_IN[1], not_4_out);
  and and_4 (and_4_out[0], not_5_out, not_6_out);
  Register #(.width(3)) register_1 (.D(multiplexer_1_out), .clk(CLK), .Q(Etat_OUT));  // open: en, clr
  Multiplexer #(.width(3), .enable("false")) multiplexer_1 (
    .in0({1'b0, and_4_out}), .in1(Etat_IN), .out(multiplexer_1_out), .sel(or_1_out));

  assign Boutons_OUT[3:1] = Boutons_IN[3:1];
endmodule

module Heure (
  input  [3:0] Boutons,
  input  [22:0] Temps,
  input  [2:0] Etat,
  output [7:0] Seg0,
  output [7:0] Seg1,
  output [7:0] Seg2,
  output [7:0] Seg3,
  output [7:0] Seg4,
  output [7:0] Seg5
);

  H_affiche h_affiche_1 (
    .Temps(Temps), .out_2(Seg0), .out_3(Seg1), .out_4(Seg2), .out_5(Seg3), .out_6(Seg4), .out_7(Seg5));
endmodule

module Conv_temps (
  input  [22:0] Temps,
  output [2:0] Jours,
  output [4:0] Heures,
  output [5:0] Minutes,
  output [5:0] Secondes,
  output [3:0] dixiemes
);

  wire [9:4] divider_4_rem;
  wire [9:6] divider_4_out;
  wire [15:0] divider_3_rem;
  wire [15:6] divider_3_out;
  wire [19:0] divider_2_rem;
  wire [19:5] divider_2_out;
  wire [22:0] divider_1_rem;
  wire [22:3] divider_1_out;

  Divider #(.width(23)) divider_1 (
    .a(Temps), .b(23'hd2f00), .out({divider_1_out, Jours}), .rem(divider_1_rem));  // open: upper
  Divider #(.width(20)) divider_2 (
    .a(divider_1_rem[19:0]), .b(20'h8ca0), .out({divider_2_out, Heures}), .rem(divider_2_rem));  // open: upper
  Divider #(.width(16)) divider_3 (
    .a(divider_2_rem[15:0]), .b(16'h258), .out({divider_3_out, Minutes}), .rem(divider_3_rem));  // open: upper
  Divider #(.width(10)) divider_4 (
    .a(divider_3_rem[9:0]), .b(10'ha), .out({divider_4_out, Secondes}), .rem({divider_4_rem, dixiemes}));  // open: upper
endmodule

module Chronometre (
  input  [22:0] Temps,
  input  [3:0] Boutons,
  input  [2:0] Etat,
  output [7:0] Seg0,
  output [7:0] Seg1,
  output [7:0] Seg2,
  output [7:0] Seg3,
  output [7:0] Seg4,
  output [7:0] Seg5,
  output Sous_systeme
);

  wire and_1_out, and_2_out, and_3_out, and_4_out, comparator_1_gt, not_1_out, not_2_out, or_1_out, t_ff_1_q,
       t_ff_2_q;
  wire [22:0] adder_1_out, conteur_tours_1_temps_sortie, Debut_q, FIn_q, multiplexer_1_out,
       multiplexer_2_out, register_1_q, subtractor_1_out;

  and and_1 (and_1_out, ~Etat[0], Etat[1], ~Etat[2]);  // AND_Gate
  T_Flip_Flop t_ff_1 (.T(and_2_out), .clk(Boutons[2]), .Q(t_ff_1_q), .reset(not_1_out));  // open: Qn, preset
  and and_2 (and_2_out, not_2_out, and_1_out);
  not not_1 (not_1_out, and_1_out);
  Register #(.width(23)) Debut (.D(Temps), .clk(t_ff_1_q), .Q(Debut_q), .clr(and_4_out));  // open: en
  and and_3 (and_3_out, ~t_ff_1_q, and_1_out);  // AND_Gate
  not not_2 (not_2_out, t_ff_2_q);
  and and_4 (and_4_out, Boutons[3], and_1_out, ~t_ff_1_q);  // AND_Gate
  T_Flip_Flop t_ff_2 (.T(and_3_out), .clk(Boutons[1]), .Q(t_ff_2_q));  // open: Qn, reset, preset
  Register #(.width(23), .trigger("falling")) FIn (.D(Temps), .clk(t_ff_1_q), .Q(FIn_q), .clr(and_4_out));  // open: en
  Comparator #(.width(23), .mode("unsigned")) comparator_1 (
    .a(FIn_q), .b(Debut_q), .gt(comparator_1_gt));  // open: eq, lt
  Multiplexer #(.width(23), .enable("false")) multiplexer_1 (
    .in0(Temps), .in1(FIn_q), .out(multiplexer_1_out), .sel(or_1_out));
  or or_1 (or_1_out, comparator_1_gt, ~t_ff_1_q);  // OR_Gate
  Multiplexer #(.width(23), .enable("false")) multiplexer_2 (
    .in0(multiplexer_1_out), .in1(conteur_tours_1_temps_sortie), .out(multiplexer_2_out), .sel(t_ff_2_q));
  Conteur_tours conteur_tours_1 (
    .B1L(Boutons[1]), .B1C(Boutons[0]), .Sous_syst(t_ff_1_q), .Lect_tours(t_ff_2_q), .Reset(and_4_out),
    .Temps(Temps), .Debut(Debut_q), .temps_sortie(conteur_tours_1_temps_sortie));
  or or_2 (Sous_systeme, t_ff_1_q, t_ff_2_q);
  Subtractor #(.width(23)) subtractor_1 (
    .a(multiplexer_2_out), .b(Debut_q), .out(subtractor_1_out));  // open: bin, bout
  Register #(.width(23)) register_1 (.D(adder_1_out), .clk(t_ff_1_q), .Q(register_1_q));  // open: en, clr
  Adder #(.width(23)) adder_1 (.a(register_1_q), .b(subtractor_1_out), .out(adder_1_out));  // open: cin, cout
  C_affiche c_affiche_1 (
    .Temps(adder_1_out), .Seg_0(Seg0), .Seg_1(Seg1), .Seg_2(Seg2), .Seg_3(Seg3), .Seg_4(Seg4), .Seg_5(Seg5));
endmodule

module Conteur_tours (
  input  B1L,
  input  B1C,
  input  Sous_syst,
  input  Lect_tours,
  input  Reset,
  input  [22:0] Temps,
  input  [22:0] Debut,
  output [22:0] temps_sortie
);

  wire and_1_out, and_2_out, and_3_out, and_4_out, and_5_out, and_6_out, and_7_out, and_8_out,
       comparator_1_lt, comparator_8_lt, comparator_9_lt, comparator_10_lt, comparator_11_lt,
       comparator_12_lt, comparator_13_lt, comparator_14_lt, d_ff_8_q, nor_1_out, not_1_out, or_1_out,
       or_2_out, or_3_out, or_4_out, or_5_out, or_6_out, or_7_out, or_8_out, or_9_out, or_10_out, undriven_8,
       undriven_9, undriven_10, undriven_11, undriven_12, undriven_13, undriven_14;
  wire [1:0] d_ff_1_q;
  wire [2:2] d_ff_3_q;
  wire [3:3] d_ff_4_q;
  wire [4:4] d_ff_5_q;
  wire [5:5] d_ff_6_q;
  wire [6:6] d_ff_7_q;
  wire [22:0] controlled_buffer_1_out, controlled_buffer_2_out, controlled_buffer_3_out,
       controlled_buffer_4_out, controlled_buffer_5_out, controlled_buffer_6_out, controlled_buffer_7_out,
       controlled_buffer_8_out, register_1_q, register_2_q, register_3_q, register_4_q, register_5_q,
       register_6_q, register_7_q, undriven, undriven_2, undriven_3, undriven_4, undriven_5, undriven_6,
       undriven_7, undriven_15;

  or or_1 (or_1_out, Sous_syst, Lect_tours);
  and and_1 (and_1_out, or_1_out, B1C);
  D_Flip_Flop d_ff_1 (.D(1'b1), .clk(and_1_out), .Q(d_ff_1_q[0]), .reset(or_3_out));  // open: Qn, preset
  D_Flip_Flop d_ff_2 (.D(d_ff_1_q[0]), .clk(and_1_out), .Q(d_ff_1_q[1]), .reset(or_4_out));  // open: Qn, preset
  D_Flip_Flop d_ff_3 (.D(d_ff_1_q[1]), .clk(and_1_out), .Q(d_ff_3_q[2]), .reset(or_5_out));  // open: Qn, preset
  D_Flip_Flop d_ff_4 (.D(d_ff_3_q[2]), .clk(and_1_out), .Q(d_ff_4_q[3]), .reset(or_6_out));  // open: Qn, preset
  D_Flip_Flop d_ff_5 (.D(d_ff_4_q[3]), .clk(and_1_out), .Q(d_ff_5_q[4]), .reset(or_7_out));  // open: Qn, preset
  D_Flip_Flop d_ff_6 (.D(d_ff_5_q[4]), .clk(and_1_out), .Q(d_ff_6_q[5]), .reset(or_8_out));  // open: Qn, preset
  D_Flip_Flop d_ff_7 (.D(d_ff_6_q[5]), .clk(and_1_out), .Q(d_ff_7_q[6]), .reset(or_9_out));  // open: Qn, preset
  D_Flip_Flop d_ff_8 (.D(or_2_out), .clk(and_1_out), .Q(d_ff_8_q), .reset(or_10_out));  // open: Qn, preset
  or or_2 (or_2_out, d_ff_7_q[6], d_ff_8_q);
  or or_3 (or_3_out, d_ff_1_q[1], or_4_out);
  or or_4 (or_4_out, d_ff_3_q[2], or_5_out);
  or or_5 (or_5_out, d_ff_4_q[3], or_6_out);
  or or_6 (or_6_out, d_ff_5_q[4], or_7_out);
  or or_7 (or_7_out, d_ff_6_q[5], or_8_out);
  or or_8 (or_8_out, d_ff_7_q[6], or_9_out);
  or or_9 (or_9_out, d_ff_8_q, or_10_out);
  or or_10 (or_10_out, Reset, B1L);
  Register #(.width(23)) register_1 (.D(Temps), .en(not_1_out), .clk(d_ff_1_q[0]), .Q(register_1_q), .clr(Reset));
  not not_1 (not_1_out, Lect_tours);
  Register #(.width(23)) register_2 (.D(Temps), .en(not_1_out), .clk(d_ff_1_q[1]), .Q(register_2_q), .clr(Reset));
  Register #(.width(23)) register_3 (.D(Temps), .en(not_1_out), .clk(d_ff_3_q[2]), .Q(register_3_q), .clr(Reset));
  Register #(.width(23)) register_4 (.D(Temps), .en(not_1_out), .clk(d_ff_4_q[3]), .Q(register_4_q), .clr(Reset));
  Register #(.width(23)) register_5 (.D(Temps), .en(not_1_out), .clk(d_ff_5_q[4]), .Q(register_5_q), .clr(Reset));
  Register #(.width(23)) register_6 (.D(Temps), .en(not_1_out), .clk(d_ff_6_q[5]), .Q(register_6_q), .clr(Reset));
  Register #(.width(23)) register_7 (.D(Temps), .en(not_1_out), .clk(d_ff_7_q[6]), .Q(register_7_q), .clr(Reset));
  Comparator #(.width(23), .mode("unsigned")) comparator_1 (
    .a(Debut), .b(register_1_q), .lt(comparator_1_lt));  // open: gt, eq
  Comparator #(.width(23), .mode("unsigned")) comparator_2 (.a(Debut), .b(register_2_q));  // open: gt, eq, lt
  Comparator #(.width(23), .mode("unsigned")) comparator_3 (.a(Debut), .b(register_3_q));  // open: gt, eq, lt
  Comparator #(.width(23), .mode("unsigned")) comparator_4 (.a(Debut), .b(register_4_q));  // open: gt, eq, lt
  Comparator #(.width(23), .mode("unsigned")) comparator_5 (.a(Debut), .b(register_5_q));  // open: gt, eq, lt
  Comparator #(.width(23), .mode("unsigned")) comparator_6 (.a(Debut), .b(register_6_q));  // open: gt, eq, lt
  Comparator #(.width(23), .mode("unsigned")) comparator_7 (.a(Debut), .b(register_7_q));  // open: gt, eq, lt
  Multiplexer #(.select(3), .width(23), .enable("false")) multiplexer_1 (
    .in0(register_1_q), .in1(register_2_q), .in2(register_3_q), .in3(register_4_q), .in4(register_5_q),
    .in5(register_6_q), .in6(register_7_q), .in7(Debut));  // open: out, sel
  assign controlled_buffer_1_out = undriven_8 ? undriven : 23'bz;  // Controlled_Buffer controlled_buffer_1
  assign controlled_buffer_2_out = undriven_9 ? undriven_2 : 23'bz;  // Controlled_Buffer controlled_buffer_2
  assign controlled_buffer_3_out = undriven_10 ? undriven_7 : 23'bz;  // Controlled_Buffer controlled_buffer_3
  assign controlled_buffer_4_out = undriven_11 ? undriven_3 : 23'bz;  // Controlled_Buffer controlled_buffer_4
  assign controlled_buffer_5_out = undriven_12 ? undriven_4 : 23'bz;  // Controlled_Buffer controlled_buffer_5
  assign controlled_buffer_6_out = undriven_13 ? undriven_5 : 23'bz;  // Controlled_Buffer controlled_buffer_6
  assign controlled_buffer_7_out = undriven_14 ? undriven_6 : 23'bz;  // Controlled_Buffer controlled_buffer_7
  Comparator #(.width(23), .mode("unsigned")) comparator_8 (
    .a(undriven_15), .b(undriven), .lt(comparator_8_lt));  // open: gt, eq
  Comparator #(.width(23), .mode("unsigned")) comparator_9 (
    .a(undriven_15), .b(undriven_2), .lt(comparator_9_lt));  // open: gt, eq
  Comparator #(.width(23), .mode("unsigned")) comparator_10 (
    .a(undriven_15), .b(undriven_7), .lt(comparator_10_lt));  // open: gt, eq
  Comparator #(.width(23), .mode("unsigned")) comparator_11 (
    .a(undriven_15), .b(undriven_3), .lt(comparator_11_lt));  // open: gt, eq
  Comparator #(.width(23), .mode("unsigned")) comparator_12 (
    .a(undriven_15), .b(undriven_4), .lt(comparator_12_lt));  // open: gt, eq
  Comparator #(.width(23), .mode("unsigned")) comparator_13 (
    .a(undriven_15), .b(undriven_5), .lt(comparator_13_lt));  // open: gt, eq
  Comparator #(.width(23), .mode("unsigned")) comparator_14 (
    .a(undriven_15), .b(undriven_6), .lt(comparator_14_lt));  // open: gt, eq
  assign controlled_buffer_8_out = comparator_8_lt ? controlled_buffer_1_out : 23'bz;  // Controlled_Buffer controlled_buffer_8
  assign controlled_buffer_8_out = comparator_9_lt ? controlled_buffer_2_out : 23'bz;  // Controlled_Buffer controlled_buffer_9
  assign controlled_buffer_8_out = comparator_10_lt ? controlled_buffer_3_out : 23'bz;  // Controlled_Buffer controlled_buffer_10
  assign controlled_buffer_8_out = comparator_11_lt ? controlled_buffer_4_out : 23'bz;  // Controlled_Buffer controlled_buffer_11
  assign controlled_buffer_8_out = comparator_12_lt ? controlled_buffer_5_out : 23'bz;  // Controlled_Buffer controlled_buffer_12
  assign controlled_buffer_8_out = comparator_13_lt ? controlled_buffer_6_out : 23'bz;  // Controlled_Buffer controlled_buffer_13
  assign controlled_buffer_8_out = comparator_14_lt ? controlled_buffer_7_out : 23'bz;  // Controlled_Buffer controlled_buffer_14
  and and_2 (and_2_out, comparator_8_lt, undriven_8);
  and and_3 (and_3_out, comparator_9_lt, undriven_9);
  and and_4 (and_4_out, comparator_10_lt, undriven_10);
  and and_5 (and_5_out, comparator_11_lt, undriven_11);
  and and_6 (and_6_out, comparator_12_lt, undriven_12);
  and and_7 (and_7_out, comparator_13_lt, undriven_13);
  and and_8 (and_8_out, comparator_14_lt, undriven_14);
  nor nor_1 (nor_1_out, and_2_out, and_3_out, and_4_out, and_5_out, and_6_out, and_7_out, and_8_out);
endmodule

module Alarme (
  input  [22:0] Temps,
  input  [3:0] Boutons,
  input  [2:0] Etat,
  output [6:0] LEDs,
  output [7:0] Seg0,
  output [7:0] Seg1,
  output [7:0] Seg2,
  output [7:0] Seg3,
  output [7:0] Seg4,
  output [7:0] Seg5,
  output Sonne,
  output Sous_systeme
);

  wire and_1_out, and_2_out, and_3_out, and_4_out, and_5_out, and_6_out, or_1_out, or_2_out, or_3_out,
       or_4_out, or_5_out;
  wire [2:0] a_detect_jour_1_j_3b, and_7_out;
  wire [5:0] J1_out;
  wire [6:6] J7_q;
  wire [22:0] controlled_buffer_1_out, multiplexer_1_out, set_alarme_1_valeur, set_alarme_2_valeur,
       set_alarme_3_valeur, set_alarme_4_valeur, set_alarme_5_valeur, set_alarme_6_valeur,
       set_alarme_7_valeur;

  and and_1 (and_1_out, Etat[0], ~Etat[1], ~Etat[2]);  // AND_Gate
  and and_2 (and_2_out, Boutons[2], and_1_out, ~Sous_systeme);  // AND_Gate
  and and_3 (and_3_out, Boutons[2], Sous_systeme);
  T_Flip_Flop t_ff_1 (.T(1'b1), .clk(and_4_out), .Q(Sous_systeme));  // open: Qn, reset, preset
  and and_4 (and_4_out, Boutons[1], and_1_out);
  D_Flip_Flop J2 (.D(1'b1), .clk(and_2_out), .Q(J1_out[1]), .reset(or_1_out));  // open: Qn, preset
  D_Flip_Flop J3 (.D(J1_out[1]), .clk(and_2_out), .Q(J1_out[2]), .reset(or_2_out));  // open: Qn, preset
  D_Flip_Flop J4 (.D(J1_out[2]), .clk(and_2_out), .Q(J1_out[3]), .reset(or_3_out));  // open: Qn, preset
  D_Flip_Flop J5 (.D(J1_out[3]), .clk(and_2_out), .Q(J1_out[4]), .reset(or_4_out));  // open: Qn, preset
  D_Flip_Flop J6 (.D(J1_out[4]), .clk(and_2_out), .Q(J1_out[5]), .reset(J7_q[6]));  // open: Qn, preset
  D_Flip_Flop J7 (.D(J1_out[5]), .clk(and_2_out), .Q(J7_q[6]));  // open: Qn, preset, reset
  and J1 (J1_out[0], ~or_1_out, ~J1_out[1]);  // AND_Gate
  or or_1 (or_1_out, J1_out[2], or_2_out);
  or or_2 (or_2_out, J1_out[3], or_3_out);
  or or_3 (or_3_out, J1_out[4], or_4_out);
  or or_4 (or_4_out, J1_out[5], J7_q[6]);
  and and_5 (and_5_out, Boutons[0], Sous_systeme);
  and and_6 (and_6_out, Boutons[3], and_1_out);
  D_Flip_Flop d_ff_1 (.D(1'b1), .clk(and_3_out), .Q(and_7_out[1]), .reset(or_5_out));  // open: Qn, preset
  D_Flip_Flop d_ff_2 (.D(and_7_out[1]), .clk(and_3_out), .Q(and_7_out[2]), .reset(and_4_out));  // open: Qn, preset
  or or_5 (or_5_out, and_7_out[2], and_4_out);
  and and_7 (and_7_out[0], ~and_7_out[1], ~and_7_out[2]);  // AND_Gate
  Set_alarme set_alarme_1 (
    .add(and_5_out), .E(J1_out[0]), .Valeur(set_alarme_1_valeur), .set_actif(and_6_out), .est_actif(LEDs[0]),
    .Nbr_a_ajouter(controlled_buffer_1_out));
  Set_alarme set_alarme_2 (
    .add(and_5_out), .E(J1_out[1]), .Valeur(set_alarme_2_valeur), .set_actif(and_6_out), .est_actif(LEDs[1]),
    .Nbr_a_ajouter(controlled_buffer_1_out));
  Set_alarme set_alarme_3 (
    .add(and_5_out), .E(J1_out[2]), .Valeur(set_alarme_3_valeur), .set_actif(and_6_out), .est_actif(LEDs[2]),
    .Nbr_a_ajouter(controlled_buffer_1_out));
  Set_alarme set_alarme_4 (
    .add(and_5_out), .E(J1_out[3]), .Valeur(set_alarme_4_valeur), .set_actif(and_6_out), .est_actif(LEDs[3]),
    .Nbr_a_ajouter(controlled_buffer_1_out));
  Set_alarme set_alarme_5 (
    .add(and_5_out), .E(J1_out[4]), .Valeur(set_alarme_5_valeur), .set_actif(and_6_out), .est_actif(LEDs[4]),
    .Nbr_a_ajouter(controlled_buffer_1_out));
  Set_alarme set_alarme_6 (
    .add(and_5_out), .E(J1_out[5]), .Valeur(set_alarme_6_valeur), .set_actif(and_6_out), .est_actif(LEDs[5]),
    .Nbr_a_ajouter(controlled_buffer_1_out));
  Set_alarme set_alarme_7 (
    .add(and_5_out), .E(J7_q[6]), .Valeur(set_alarme_7_valeur), .set_actif(and_6_out), .est_actif(LEDs[6]),
    .Nbr_a_ajouter(controlled_buffer_1_out));
  assign controlled_buffer_1_out = and_7_out[0] ? 23'h8ca0 : 23'bz;  // Controlled_Buffer controlled_buffer_1
  assign controlled_buffer_1_out = and_7_out[1] ? 23'h1770 : 23'bz;  // Controlled_Buffer controlled_buffer_2
  assign controlled_buffer_1_out = and_7_out[2] ? 23'h258 : 23'bz;  // Controlled_Buffer controlled_buffer_3
  detect_sonne detect_sonne_1 (
    .Temps(Temps), .J1(set_alarme_1_valeur), .J2(set_alarme_2_valeur), .J3(set_alarme_3_valeur),
    .J4(set_alarme_4_valeur), .J5(set_alarme_5_valeur), .J6(set_alarme_6_valeur), .J7(set_alarme_7_valeur),
    .Sonne(Sonne));
  Multiplexer #(.select(3), .width(23), .enable("false")) multiplexer_1 (
    .in1(set_alarme_1_valeur), .in2(set_alarme_2_valeur), .in3(set_alarme_3_valeur),
    .in4(set_alarme_4_valeur), .in5(set_alarme_5_valeur), .in6(set_alarme_6_valeur),
    .in7(set_alarme_7_valeur), .out(multiplexer_1_out), .sel(a_detect_jour_1_j_3b));  // open: in0
  A_detect_jour a_detect_jour_1 (.J_7b({J7_q[6], J1_out}), .J_3b(a_detect_jour_1_j_3b));
  A_affiche a_affiche_1 (
    .Clignot_activation(Sous_systeme), .Jour(a_detect_jour_1_j_3b), .Regle(and_7_out),
    .Clignotement(Temps[2]), .Temps(multiplexer_1_out), .Seg0(Seg0), .Seg1(Seg1), .Seg2(Seg2), .Seg3(Seg3),
    .Seg4(Seg4), .Seg5(Seg5));
endmodule

module Set_alarme (
  input  E,
  input  add,
  input  set_actif,
  input  [22:0] Nbr_a_ajouter,
  output [22:0] Valeur,
  output est_actif
);

  wire and_1_out, and_2_out;
  wire [22:0] adder_1_out;

  and and_1 (and_1_out, add, E);
  and and_2 (and_2_out, E, set_actif);
  Register #(.width(23)) register_1 (.D(adder_1_out), .clk(and_1_out), .Q(Valeur));  // open: en, clr
  T_Flip_Flop t_ff_1 (.T(1'b1), .clk(and_2_out), .Q(est_actif));  // open: Qn, reset, preset
  Adder #(.width(23)) adder_1 (.a(Nbr_a_ajouter), .b(Valeur), .out(adder_1_out));  // open: cin, cout
endmodule

module detect_sonne (
  input  [22:0] Temps,
  input  [22:0] J1,
  input  [22:0] J2,
  input  [22:0] J3,
  input  [22:0] J4,
  input  [22:0] J5,
  input  [22:0] J6,
  input  [22:0] J7,
  output Sonne
);

  wire comparator_1_eq, comparator_2_eq, comparator_3_eq, comparator_4_eq, comparator_5_eq, comparator_6_eq,
       comparator_7_eq;
  wire [22:0] subtractor_1_out, subtractor_2_out, subtractor_3_out, subtractor_4_out, subtractor_5_out,
       subtractor_6_out;

  Subtractor #(.width(23)) subtractor_1 (.a(Temps), .b(23'hd2f00), .out(subtractor_1_out));  // open: bin, bout
  Subtractor #(.width(23)) subtractor_2 (
    .a(subtractor_1_out), .b(23'hd2f00), .out(subtractor_2_out));  // open: bin, bout
  Subtractor #(.width(23)) subtractor_3 (
    .a(subtractor_2_out), .b(23'hd2f00), .out(subtractor_3_out));  // open: bin, bout
  Subtractor #(.width(23)) subtractor_4 (
    .a(subtractor_3_out), .b(23'hd2f00), .out(subtractor_4_out));  // open: bin, bout
  Subtractor #(.width(23)) subtractor_5 (
    .a(subtractor_4_out), .b(23'hd2f00), .out(subtractor_5_out));  // open: bin, bout
  Subtractor #(.width(23)) subtractor_6 (
    .a(subtractor_5_out), .b(23'hd2f00), .out(subtractor_6_out));  // open: bin, bout
  Comparator #(.width(23), .mode("unsigned")) comparator_1 (.a(Temps), .b(J1), .eq(comparator_1_eq));  // open: gt, lt
  Comparator #(.width(23), .mode("unsigned")) comparator_2 (
    .a(subtractor_1_out), .b(J2), .eq(comparator_2_eq));  // open: gt, lt
  Comparator #(.width(23), .mode("unsigned")) comparator_3 (
    .a(subtractor_2_out), .b(J3), .eq(comparator_3_eq));  // open: gt, lt
  Comparator #(.width(23), .mode("unsigned")) comparator_4 (
    .a(subtractor_3_out), .b(J4), .eq(comparator_4_eq));  // open: gt, lt
  Comparator #(.width(23), .mode("unsigned")) comparator_5 (
    .a(subtractor_4_out), .b(J5), .eq(comparator_5_eq));  // open: gt, lt
  Comparator #(.width(23), .mode("unsigned")) comparator_6 (
    .a(subtractor_5_out), .b(J6), .eq(comparator_6_eq));  // open: gt, lt
  Comparator #(.width(23), .mode("unsigned")) comparator_7 (
    .a(subtractor_6_out), .b(J7), .eq(comparator_7_eq));  // open: gt, lt
  or or_1 (Sonne, comparator_1_eq, comparator_2_eq, comparator_3_eq, comparator_4_eq, comparator_5_eq, comparator_6_eq, comparator_7_eq);
endmodule

module C_affiche (
  input  [22:0] Temps,
  output [7:0] Seg_0,
  output [7:0] Seg_1,
  output [7:0] Seg_2,
  output [7:0] Seg_3,
  output [7:0] Seg_4,
  output [7:0] Seg_5
);

  wire comparator_1_lt, not_1_out, not_2_out;
  wire [3:0] conv_temps_1_dixiemes, conv_unit_dizaines_1_dizaines, conv_unit_dizaines_1_unites,
       conv_unit_dizaines_2_dizaines, conv_unit_dizaines_2_unites, conv_unit_dizaines_3_dizaines,
       conv_unit_dizaines_3_unites, multiplexer_1_out, multiplexer_2_out, multiplexer_3_out,
       multiplexer_4_out, multiplexer_5_out;
  wire [4:0] conv_temps_1_heures;
  wire [5:0] conv_temps_1_minutes, conv_temps_1_secondes;
  wire [7:0] chiffre_7seg_1_sortie;

  Conv_temps conv_temps_1 (
    .Temps(Temps), .Heures(conv_temps_1_heures), .Minutes(conv_temps_1_minutes),
    .Secondes(conv_temps_1_secondes), .dixiemes(conv_temps_1_dixiemes));  // open: Jours
  Comparator #(.width(5), .mode("unsigned")) comparator_1 (
    .a({5{1'b0}}), .b(conv_temps_1_heures), .lt(comparator_1_lt));  // open: gt, eq
  conv_unit_dizaines conv_unit_dizaines_1 (
    .Entree({1'b0, conv_temps_1_heures}), .Dizaines(conv_unit_dizaines_1_dizaines),
    .Unites(conv_unit_dizaines_1_unites));
  conv_unit_dizaines conv_unit_dizaines_2 (
    .Entree(conv_temps_1_minutes), .Dizaines(conv_unit_dizaines_2_dizaines),
    .Unites(conv_unit_dizaines_2_unites));
  conv_unit_dizaines conv_unit_dizaines_3 (
    .Entree(conv_temps_1_secondes), .Dizaines(conv_unit_dizaines_3_dizaines),
    .Unites(conv_unit_dizaines_3_unites));
  Multiplexer #(.width(4), .enable("false")) multiplexer_1 (
    .in0(conv_unit_dizaines_2_dizaines), .in1(conv_unit_dizaines_1_unites), .out(multiplexer_1_out),
    .sel(comparator_1_lt));
  Multiplexer #(.width(4), .enable("false")) multiplexer_2 (
    .in0(conv_unit_dizaines_2_unites), .in1(conv_unit_dizaines_2_dizaines), .out(multiplexer_2_out),
    .sel(comparator_1_lt));
  not not_1 (not_1_out, comparator_1_lt);
  Multiplexer #(.width(4), .enable("false")) multiplexer_3 (
    .in0(conv_unit_dizaines_3_dizaines), .in1(conv_unit_dizaines_2_unites), .out(multiplexer_3_out),
    .sel(comparator_1_lt));
  Multiplexer #(.width(4), .enable("false")) multiplexer_4 (
    .in0(conv_unit_dizaines_3_unites), .in1(conv_unit_dizaines_3_dizaines), .out(multiplexer_4_out),
    .sel(comparator_1_lt));
  not not_2 (not_2_out, comparator_1_lt);
  Multiplexer #(.width(4), .enable("false")) multiplexer_5 (
    .in0(conv_temps_1_dixiemes), .in1(conv_unit_dizaines_3_unites), .out(multiplexer_5_out),
    .sel(comparator_1_lt));
  Multiplexer #(.width(8), .enable("false")) multiplexer_6 (
    .in0({8{1'b0}}), .in1(chiffre_7seg_1_sortie), .out(Seg_0), .sel(comparator_1_lt));
  Chiffre_7seg chiffre_7seg_1 (.Sortie(chiffre_7seg_1_sortie), .Point(1'b0), .Entree(conv_unit_dizaines_1_dizaines));
  Chiffre_7seg chiffre_7seg_2 (.Sortie(Seg_1), .Point(comparator_1_lt), .Entree(multiplexer_1_out));
  Chiffre_7seg chiffre_7seg_3 (.Sortie(Seg_2), .Point(not_1_out), .Entree(multiplexer_2_out));
  Chiffre_7seg chiffre_7seg_4 (.Sortie(Seg_3), .Point(comparator_1_lt), .Entree(multiplexer_3_out));
  Chiffre_7seg chiffre_7seg_5 (.Sortie(Seg_4), .Point(not_2_out), .Entree(multiplexer_4_out));
  Chiffre_7seg chiffre_7seg_6 (.Sortie(Seg_5), .Point(1'b0), .Entree(multiplexer_5_out));
endmodule

module Chiffre_7seg (
  input  [3:0] Entree,
  input  Point,
  output [7:0] Sortie
);

  Dec_b dec_b_1 (.in_1(Entree[3]), .in_2(Entree[2]), .in_3(Entree[1]), .in_4(Entree[0]), .out_5(Sortie[0]));
  Dec_a dec_a_1 (.in_1(Entree[3]), .in_2(Entree[2]), .in_3(Entree[1]), .in_4(Entree[0]), .out_5(Sortie[1]));
  Dec_f dec_f_1 (.in_1(Entree[3]), .in_2(Entree[2]), .in_3(Entree[1]), .in_4(Entree[0]), .out_5(Sortie[2]));
  Dec_g dec_g_1 (.in_1(Entree[3]), .in_2(Entree[2]), .in_3(Entree[1]), .in_4(Entree[0]), .out_5(Sortie[3]));
  Dec_c dec_c_1 (.in_1(Entree[3]), .in_2(Entree[2]), .in_3(Entree[1]), .in_4(Entree[0]), .out_5(Sortie[5]));
  Dec_d dec_d_1 (.in_1(Entree[3]), .in_2(Entree[2]), .in_3(Entree[1]), .in_4(Entree[0]), .out_5(Sortie[6]));
  Dec_e dec_e_1 (.in_1(Entree[3]), .in_2(Entree[2]), .in_3(Entree[1]), .in_4(Entree[0]), .out_5(Sortie[7]));
  _7_Segment_Display u_7_segment_display_1 (
    .g(Sortie[3]), .f(Sortie[2]), .a(Sortie[1]), .b(Sortie[0]), .e(Sortie[7]), .d(Sortie[6]), .c(Sortie[5]),
    .dp(Point));

  assign Sortie[4] = Point;
endmodule

module Dec_a (
  input  in_1,
  input  in_2,
  input  in_3,
  input  in_4,
  output out_5
);

  wire and_1_out, and_2_out, and_3_out, and_4_out, not_1_out, not_2_out, not_3_out, not_4_out, or_1_out;

  not not_1 (not_1_out, in_1);
  not not_2 (not_2_out, in_2);
  not not_3 (not_3_out, in_3);
  not not_4 (not_4_out, in_4);
  and and_1 (and_1_out, not_1_out, not_2_out, not_3_out, in_4);
  and and_2 (and_2_out, not_1_out, in_2, not_3_out, not_4_out);
  and and_3 (and_3_out, in_1, not_2_out, in_3, in_4);
  and and_4 (and_4_out, in_1, in_2, not_3_out, in_4);
  or or_1 (or_1_out, and_1_out, and_2_out, and_3_out, and_4_out);
  not not_5 (out_5, or_1_out);
endmodule

module Dec_b (
  input  in_1,
  input  in_2,
  input  in_3,
  input  in_4,
  output out_5
);

  wire and_1_out, and_2_out, and_3_out, and_4_out, and_5_out, not_1_out, not_2_out, not_3_out, not_4_out;

  not not_1 (not_1_out, in_1);
  not not_2 (not_2_out, in_2);
  not not_3 (not_3_out, in_3);
  not not_4 (not_4_out, in_4);
  and and_1 (and_1_out, not_1_out, not_2_out);
  and and_2 (and_2_out, not_2_out, not_4_out);
  and and_3 (and_3_out, not_1_out, not_3_out, not_4_out);
  and and_4 (and_4_out, not_1_out, in_3, in_4);
  and and_5 (and_5_out, in_1, not_3_out, in_4);
  or or_1 (out_5, and_1_out, and_2_out, and_3_out, and_4_out, and_5_out);
endmodule

module Dec_c (
  input  in_1,
  input  in_2,
  input  in_3,
  input  in_4,
  output out_5
);

  wire and_1_out, and_2_out, and_3_out, not_1_out, not_2_out, not_3_out, not_4_out, or_1_out;

  not not_1 (not_1_out, in_1);
  not not_2 (not_2_out, in_2);
  not not_3 (not_3_out, in_3);
  not not_4 (not_4_out, in_4);
  and and_1 (and_1_out, in_1, in_2, not_4_out);
  and and_2 (and_2_out, in_1, in_2, in_3);
  and and_3 (and_3_out, not_1_out, not_2_out, in_3, not_4_out);
  not not_5 (out_5, or_1_out);
  or or_1 (or_1_out, and_1_out, and_2_out, and_3_out);
endmodule

module Dec_d (
  input  in_1,
  input  in_2,
  input  in_3,
  input  in_4,
  output out_5
);

  wire and_1_out, and_2_out, and_3_out, and_4_out, and_5_out, not_1_out, not_2_out, not_3_out, not_4_out;

  not not_1 (not_1_out, in_1);
  not not_2 (not_2_out, in_2);
  not not_3 (not_3_out, in_3);
  not not_4 (not_4_out, in_4);
  and and_1 (and_1_out, in_1, not_3_out);
  and and_2 (and_2_out, in_2, in_3, not_4_out);
  and and_3 (and_3_out, not_2_out, in_3, in_4);
  and and_4 (and_4_out, not_1_out, not_2_out, not_4_out);
  and and_5 (and_5_out, in_2, not_3_out, in_4);
  or or_1 (out_5, and_1_out, and_2_out, and_3_out, and_4_out, and_5_out);
endmodule

module Dec_e (
  input  in_1,
  input  in_2,
  input  in_3,
  input  in_4,
  output out_5
);

  wire and_1_out, and_2_out, and_3_out, and_4_out, not_1_out, not_2_out, not_3_out, not_4_out;

  not not_1 (not_1_out, in_1);
  not not_2 (not_2_out, in_2);
  not not_3 (not_3_out, in_3);
  not not_4 (not_4_out, in_4);
  and and_1 (and_1_out, in_1, in_2);
  and and_2 (and_2_out, in_1, in_3);
  and and_3 (and_3_out, not_2_out, not_4_out);
  and and_4 (and_4_out, in_3, not_4_out);
  or or_1 (out_5, and_1_out, and_2_out, and_3_out, and_4_out);
endmodule

module Dec_f (
  input  in_1,
  input  in_2,
  input  in_3,
  input  in_4,
  output out_5
);

  wire and_1_out, and_2_out, and_3_out, and_4_out, not_1_out, not_2_out, not_3_out, not_4_out, or_1_out;

  not not_1 (not_1_out, in_1);
  not not_2 (not_2_out, in_2);
  not not_3 (not_3_out, in_3);
  not not_4 (not_4_out, in_4);
  and and_1 (and_1_out, in_1, in_2, not_3_out, in_4);
  and and_2 (and_2_out, not_1_out, in_3, in_4);
  and and_3 (and_3_out, not_1_out, not_2_out, in_3);
  and and_4 (and_4_out, not_1_out, not_2_out, in_4);
  or or_1 (or_1_out, and_1_out, and_2_out, and_3_out, and_4_out);
  not not_5 (out_5, or_1_out);
endmodule

module Dec_g (
  input  in_1,
  input  in_2,
  input  in_3,
  input  in_4,
  output out_5
);

  wire and_1_out, and_2_out, and_3_out, not_1_out, not_2_out, not_3_out, not_4_out, or_1_out;

  not not_1 (not_1_out, in_1);
  not not_2 (not_2_out, in_2);
  not not_3 (not_3_out, in_3);
  not not_4 (not_4_out, in_4);
  and and_1 (and_1_out, not_1_out, not_2_out, not_3_out);
  and and_2 (and_2_out, in_1, in_2, not_3_out, not_4_out);
  and and_3 (and_3_out, not_1_out, in_2, in_3, in_4);
  or or_1 (or_1_out, and_1_out, and_2_out, and_3_out);
  not not_5 (out_5, or_1_out);
endmodule

module conv_unit_dizaines (
  input  [5:0] Entree,
  output [3:0] Dizaines,
  output [3:0] Unites
);

  wire [5:4] divider_1_out, divider_1_rem;

  Divider #(.width(6)) divider_1 (
    .a(Entree), .b(6'b001010), .out({divider_1_out, Dizaines}), .rem({divider_1_rem, Unites}));  // open: upper
endmodule

module A_detect_jour (
  input  [6:0] J_7b,
  output [2:0] J_3b
);

  wire not_1_out, not_2_out, not_3_out, not_4_out, not_5_out, not_6_out, not_7_out, not_8_out, not_9_out;

  not not_1 (not_1_out, J_7b[0]);
  not not_2 (not_2_out, J_7b[1]);
  not not_3 (not_3_out, J_7b[2]);
  not not_4 (not_4_out, J_7b[0]);
  not not_5 (not_5_out, J_7b[3]);
  not not_6 (not_6_out, J_7b[4]);
  not not_7 (not_7_out, J_7b[1]);
  not not_8 (not_8_out, J_7b[3]);
  not not_9 (not_9_out, J_7b[5]);
  and and_1 (J_3b[2], not_1_out, not_2_out, not_3_out);
  and and_2 (J_3b[1], not_4_out, not_5_out, not_6_out);
  and and_3 (J_3b[0], not_7_out, not_8_out, not_9_out);
endmodule

module A_affiche (
  input  Clignot_activation,
  input  [2:0] Jour,
  input  [2:0] Regle,
  input  Clignotement,
  input  [22:0] Temps,
  output [7:0] Seg0,
  output [7:0] Seg1,
  output [7:0] Seg2,
  output [7:0] Seg3,
  output [7:0] Seg4,
  output [7:0] Seg5
);

  wire nand_1_out, nand_2_out, nand_3_out;
  wire [3:0] conv_unit_dizaines_1_dizaines, conv_unit_dizaines_1_unites, conv_unit_dizaines_2_dizaines,
       conv_unit_dizaines_2_unites;
  wire [4:0] conv_temps_1_heures;
  wire [5:0] conv_temps_1_minutes;
  wire [7:0] chiffre_7seg_1_sortie, chiffre_7seg_2_sortie, chiffre_7seg_3_sortie, chiffre_7seg_4_sortie;

  Conv_temps conv_temps_1 (
    .Temps(Temps), .Heures(conv_temps_1_heures), .Minutes(conv_temps_1_minutes));  // open: Jours, Secondes, dixiemes
  conv_unit_dizaines conv_unit_dizaines_1 (
    .Entree({1'b0, conv_temps_1_heures}), .Dizaines(conv_unit_dizaines_1_dizaines),
    .Unites(conv_unit_dizaines_1_unites));
  conv_unit_dizaines conv_unit_dizaines_2 (
    .Entree(conv_temps_1_minutes), .Dizaines(conv_unit_dizaines_2_dizaines),
    .Unites(conv_unit_dizaines_2_unites));
  Multiplexer #(.width(8), .enable("false")) multiplexer_1 (
    .in0({8{1'b0}}), .in1(chiffre_7seg_1_sortie), .out(Seg2), .sel(nand_1_out));
  Chiffre_7seg chiffre_7seg_1 (.Sortie(chiffre_7seg_1_sortie), .Point(1'b0), .Entree(conv_unit_dizaines_1_dizaines));
  Multiplexer #(.width(8), .enable("false")) multiplexer_2 (
    .in0({8{1'b0}}), .in1(chiffre_7seg_2_sortie), .out(Seg3), .sel(nand_1_out));
  Chiffre_7seg chiffre_7seg_2 (.Sortie(chiffre_7seg_2_sortie), .Point(1'b1), .Entree(conv_unit_dizaines_1_unites));
  Multiplexer #(.width(8), .enable("false")) multiplexer_3 (
    .in0({8{1'b0}}), .in1(chiffre_7seg_3_sortie), .out(Seg4), .sel(nand_2_out));
  Chiffre_7seg chiffre_7seg_3 (.Sortie(chiffre_7seg_3_sortie), .Point(1'b0), .Entree(conv_unit_dizaines_2_dizaines));
  Chiffre_7seg chiffre_7seg_4 (.Sortie(chiffre_7seg_4_sortie), .Point(1'b0), .Entree(conv_unit_dizaines_2_unites));
  Multiplexer #(.width(8), .enable("false")) multiplexer_4 (
    .in0({8{1'b0}}), .in1(chiffre_7seg_4_sortie), .out(Seg5), .sel(nand_3_out));
  nand nand_1 (nand_1_out, Regle[0], Clignot_activation, Clignotement);
  nand nand_2 (nand_2_out, Regle[1], Clignot_activation, Clignotement);
  nand nand_3 (nand_3_out, Regle[2], Clignot_activation, Clignotement);
  Chiffre_7seg chiffre_7seg_5 (.Sortie(Seg0), .Point(1'b0), .Entree({1'b0, Jour}));

  assign Seg1 = {8{1'b0}};
endmodule

module H_affiche (
  input  [22:0] Temps,
  output [7:0] out_2,
  output [7:0] out_3,
  output [7:0] out_4,
  output [7:0] out_5,
  output [7:0] out_6,
  output [7:0] out_7
);

  wire [3:0] conv_unit_dizaines_1_dizaines, conv_unit_dizaines_1_unites, conv_unit_dizaines_2_dizaines,
       conv_unit_dizaines_2_unites, conv_unit_dizaines_3_dizaines, conv_unit_dizaines_3_unites;
  wire [4:0] conv_temps_1_heures;
  wire [5:0] conv_temps_1_minutes, conv_temps_1_secondes;

  Conv_temps conv_temps_1 (
    .Temps(Temps), .Heures(conv_temps_1_heures), .Minutes(conv_temps_1_minutes),
    .Secondes(conv_temps_1_secondes));  // open: Jours, dixiemes
  conv_unit_dizaines conv_unit_dizaines_1 (
    .Entree({1'b0, conv_temps_1_heures}), .Dizaines(conv_unit_dizaines_1_dizaines),
    .Unites(conv_unit_dizaines_1_unites));
  conv_unit_dizaines conv_unit_dizaines_2 (
    .Entree(conv_temps_1_minutes), .Dizaines(conv_unit_dizaines_2_dizaines),
    .Unites(conv_unit_dizaines_2_unites));
  conv_unit_dizaines conv_unit_dizaines_3 (
    .Entree(conv_temps_1_secondes), .Dizaines(conv_unit_dizaines_3_dizaines),
    .Unites(conv_unit_dizaines_3_unites));
  Chiffre_7seg chiffre_7seg_1 (.Sortie(out_2), .Point(1'b0), .Entree(conv_unit_dizaines_1_dizaines));
  Chiffre_7seg chiffre_7seg_2 (.Sortie(out_3), .Point(1'b1), .Entree(conv_unit_dizaines_1_unites));
  Chiffre_7seg chiffre_7seg_3 (.Sortie(out_4), .Point(1'b0), .Entree(conv_unit_dizaines_2_dizaines));
  Chiffre_7seg chiffre_7seg_4 (.Sortie(out_5), .Point(1'b1), .Entree(conv_unit_dizaines_2_unites));
  Chiffre_7seg chiffre_7seg_5 (.Sortie(out_6), .Point(1'b0), .Entree(conv_unit_dizaines_3_dizaines));
  Chiffre_7seg chiffre_7seg_6 (.Sortie(out_7), .Point(1'b0), .Entree(conv_unit_dizaines_3_unites));
endmodule
