// Logisim project Projet Version Carte.circ as structural Verilog: 37 circuits, main circuit Principal
module Principal (
  output Pin_Buzzer
);

  wire Activation_sw1, Alarme_1_sonne, Alarme_1_sous_systeme, Chronometre_1_sous_systeme,
       CLK_Reelle_1_clk_10, CLK_Reelle_1_clk_1024, clock_1_out, Heure_1_modifier_temps, Heure_1_sous_systeme,
       not_1_out, or_1_out, or_2_out, Sonne_1_buzzer, Timer_1_sonne, Timer_1_sous_systeme;
  wire [1:0] Bouton_1_out, Choix_leds_1_sortie;
  wire [2:0] A_def_etat_1_etat_out;
  wire [3:0] A_Boutons_1_bc1, A_def_etat_1_boutons_out;
  wire [6:0] Alarme_1_leds, Chronometre_1_leds, multiplexer_4_out, Sonne_1_leds;
  wire [7:0] Alarme_1_seg0, Alarme_1_seg1, Alarme_1_seg2, Alarme_1_seg3, Alarme_1_seg4, Alarme_1_seg5,
       Chronometre_1_seg0, Chronometre_1_seg1, Chronometre_1_seg2, Chronometre_1_seg3, Chronometre_1_seg4,
       Chronometre_1_seg5, Heure_1_seg0, Heure_1_seg1, Heure_1_seg2, Heure_1_seg3, Heure_1_seg4,
       Heure_1_seg5, Sonne_1_seg0, Sonne_1_seg1, Sonne_1_seg2, Sonne_1_seg3, Sonne_1_seg4, Sonne_1_seg5,
       Timer_1_seg0, Timer_1_seg1, Timer_1_seg2, Timer_1_seg3, Timer_1_seg4, Timer_1_seg5;
  wire [22:0] A_temps_1_tempsout, Heure_1_temps_a_modifier, multiplexer_1_out;
  wire [23:0] Debut_7seg, Fin_7seg;

  Button Bouton_1 (.out(Bouton_1_out[0]));
  Button Bouton_2 (.out(Bouton_1_out[1]));
  Clock clock_1 (.out(clock_1_out));
  DipSwitch #(.number(2)) Activation (.sw1(Activation_sw1));  // open: sw2
  not not_1 (not_1_out, Activation_sw1);
  CLK_Reelle CLK_Reelle_1 (
    .CLK(clock_1_out), .E(not_1_out), .CLK_1024(CLK_Reelle_1_clk_1024), .CLK_10(CLK_Reelle_1_clk_10));  // open: CLK_512
  Multiplexer #(.width(23), .enable("false")) multiplexer_1 (
    .in0(A_temps_1_tempsout), .in1(Heure_1_temps_a_modifier), .out(multiplexer_1_out),
    .sel(Heure_1_modifier_temps));
  temps A_temps_1 (
    .TempsIN(multiplexer_1_out), .CLK(CLK_Reelle_1_clk_10), .E(not_1_out), .TEMPSOUT(A_temps_1_tempsout));
  Boutons A_Boutons_1 (
    .Bouton1(Bouton_1_out[0]), .Bouton2(Bouton_1_out[1]), .CLK(CLK_Reelle_1_clk_10), .E(not_1_out),
    .BC1(A_Boutons_1_bc1[0]), .BL1(A_Boutons_1_bc1[1]), .BC2(A_Boutons_1_bc1[2]), .BL2(A_Boutons_1_bc1[3]));
  Buzzer Buzzer_1 (
    .Active(Sonne_1_buzzer), .CLK_1024(CLK_Reelle_1_clk_1024), .CLK_10(CLK_Reelle_1_clk_10), .E(not_1_out),
    .Pin_Buzzer(Pin_Buzzer));
  def_etat A_def_etat_1 (
    .Boutons_IN(A_Boutons_1_bc1), .Etat_IN(A_def_etat_1_etat_out), .Sous_Etat(or_2_out),
    .CLK(CLK_Reelle_1_clk_10), .E(not_1_out), .Sonne(or_1_out), .Etat_OUT(A_def_etat_1_etat_out),
    .Boutons_OUT(A_def_etat_1_boutons_out));
  or or_1 (or_1_out, Timer_1_sonne, Alarme_1_sonne);
  or or_2 (or_2_out, Alarme_1_sous_systeme, Timer_1_sous_systeme, Chronometre_1_sous_systeme, Heure_1_sous_systeme);
  Chronometre Chronometre_1 (
    .Temps(A_temps_1_tempsout), .Boutons(A_def_etat_1_boutons_out), .Etat(A_def_etat_1_etat_out),
    .E(not_1_out), .Seg0(Chronometre_1_seg0), .Seg1(Chronometre_1_seg1), .Seg2(Chronometre_1_seg2),
    .Seg3(Chronometre_1_seg3), .Seg4(Chronometre_1_seg4), .Seg5(Chronometre_1_seg5),
    .Leds(Chronometre_1_leds), .Sous_systeme(Chronometre_1_sous_systeme));
  Timer Timer_1 (
    .Boutons(A_def_etat_1_boutons_out), .Etat(A_def_etat_1_etat_out), .Temps(A_temps_1_tempsout),
    .E(not_1_out), .Seg0(Timer_1_seg0), .Seg1(Timer_1_seg1), .Seg2(Timer_1_seg2), .Seg3(Timer_1_seg3),
    .Seg4(Timer_1_seg4), .Seg5(Timer_1_seg5), .Sonne(Timer_1_sonne), .sous_systeme(Timer_1_sous_systeme));
  Sonne Sonne_1 (
    .Etat(A_def_etat_1_etat_out), .Boutons(A_def_etat_1_boutons_out), .Temps(A_temps_1_tempsout),
    .E(not_1_out), .Buzzer(Sonne_1_buzzer), .Seg0(Sonne_1_seg0), .Seg1(Sonne_1_seg1), .Seg2(Sonne_1_seg2),
    .Seg3(Sonne_1_seg3), .Seg4(Sonne_1_seg4), .Seg5(Sonne_1_seg5), .Leds(Sonne_1_leds));
  Heure Heure_1 (
    .Temps(A_temps_1_tempsout), .Boutons(A_def_etat_1_boutons_out), .Etat(A_def_etat_1_etat_out),
    .E(not_1_out), .CLK(CLK_Reelle_1_clk_10), .Seg0(Heure_1_seg0), .Seg1(Heure_1_seg1), .Seg2(Heure_1_seg2),
    .Seg3(Heure_1_seg3), .Seg4(Heure_1_seg4), .Seg5(Heure_1_seg5),
    .Temps_a_modifier(Heure_1_temps_a_modifier), .Modifier_temps(Heure_1_modifier_temps),
    .sous_systeme(Heure_1_sous_systeme));
  Alarme Alarme_1 (
    .Temps(A_temps_1_tempsout), .Boutons(A_def_etat_1_boutons_out), .Etat(A_def_etat_1_etat_out),
    .E(not_1_out), .LEDs(Alarme_1_leds), .Seg0(Alarme_1_seg0), .Seg1(Alarme_1_seg1), .Seg2(Alarme_1_seg2),
    .Seg3(Alarme_1_seg3), .Seg4(Alarme_1_seg4), .Seg5(Alarme_1_seg5), .Sonne(Alarme_1_sonne),
    .Sous_systeme(Alarme_1_sous_systeme));
  Multiplexer #(.select(3), .width(24), .enable("false")) multiplexer_2 (
    .in0({Heure_1_seg2, Heure_1_seg1, Heure_1_seg0}), .in1({Alarme_1_seg2, Alarme_1_seg1, Alarme_1_seg0}),
    .in2({Chronometre_1_seg2, Chronometre_1_seg1, Chronometre_1_seg0}),
    .in3({Timer_1_seg2, Timer_1_seg1, Timer_1_seg0}), .in4({Sonne_1_seg2, Sonne_1_seg1, Sonne_1_seg0}),
    .out(Fin_7seg), .sel(A_def_etat_1_etat_out));  // open: in5, in6, in7
  Multiplexer #(.select(3), .width(24), .enable("false")) multiplexer_3 (
    .in0({Heure_1_seg5, Heure_1_seg4, Heure_1_seg3}), .in1({Alarme_1_seg5, Alarme_1_seg4, Alarme_1_seg3}),
    .in2({Chronometre_1_seg5, Chronometre_1_seg4, Chronometre_1_seg3}),
    .in3({Timer_1_seg5, Timer_1_seg4, Timer_1_seg3}), .in4({Sonne_1_seg5, Sonne_1_seg4, Sonne_1_seg3}),
    .out(Debut_7seg), .sel(A_def_etat_1_etat_out));  // open: in5, in6, in7
  Multiplexer #(.select(2), .width(7), .enable("false")) multiplexer_4 (
    .in0(Alarme_1_leds), .in1(Chronometre_1_leds), .in2(Sonne_1_leds), .in3({7{1'b0}}),
    .out(multiplexer_4_out), .sel(Choix_leds_1_sortie));
  _7_Segment_Display L_7_Segment_Display_1 (
    .g(Fin_7seg[3]), .f(Fin_7seg[2]), .a(Fin_7seg[1]), .b(Fin_7seg[0]), .e(Fin_7seg[7]), .d(Fin_7seg[6]),
    .c(Fin_7seg[5]), .dp(Fin_7seg[4]));
  _7_Segment_Display L_7_Segment_Display_2 (
    .g(Fin_7seg[11]), .f(Fin_7seg[10]), .a(Fin_7seg[9]), .b(Fin_7seg[8]), .e(Fin_7seg[15]), .d(Fin_7seg[14]),
    .c(Fin_7seg[13]), .dp(Fin_7seg[12]));
  Choix_leds Choix_leds_1 (.Entree(A_def_etat_1_etat_out), .Sortie(Choix_leds_1_sortie));
  _7_Segment_Display L_7_Segment_Display_4 (
    .g(Debut_7seg[3]), .f(Debut_7seg[2]), .a(Debut_7seg[1]), .b(Debut_7seg[0]), .e(Debut_7seg[7]),
    .d(Debut_7seg[6]), .c(Debut_7seg[5]), .dp(Debut_7seg[4]));
  _7_Segment_Display L_7_Segment_Display_3 (
    .g(Fin_7seg[19]), .f(Fin_7seg[18]), .a(Fin_7seg[17]), .b(Fin_7seg[16]), .e(Fin_7seg[23]),
    .d(Fin_7seg[22]), .c(Fin_7seg[21]), .dp(Fin_7seg[20]));
  _7_Segment_Display L_7_Segment_Display_5 (
    .g(Debut_7seg[11]), .f(Debut_7seg[10]), .a(Debut_7seg[9]), .b(Debut_7seg[8]), .e(Debut_7seg[15]),
    .d(Debut_7seg[14]), .c(Debut_7seg[13]), .dp(Debut_7seg[12]));
  _7_Segment_Display L_7_Segment_Display_6 (
    .g(Debut_7seg[19]), .f(Debut_7seg[18]), .a(Debut_7seg[17]), .b(Debut_7seg[16]), .e(Debut_7seg[23]),
    .d(Debut_7seg[22]), .c(Debut_7seg[21]), .dp(Debut_7seg[20]));
  LED LED_2 (.in(multiplexer_4_out[1]));
  LED LED_1 (.in(multiplexer_4_out[0]));
  LED LED_3 (.in(multiplexer_4_out[2]));
  LED LED_4 (.in(multiplexer_4_out[3]));
  LED LED_5 (.in(multiplexer_4_out[4]));
  LED LED_6 (.in(multiplexer_4_out[5]));
  LED LED_7 (.in(multiplexer_4_out[6]));

  // Notes on the sheet:
  //   Valeur qui va sur tous les resets de portes
endmodule

module Boutons (
  input  Bouton1,
  input  Bouton2,
  input  CLK,
  input  E,
  output BC1,
  output BL1,
  output BC2,
  output BL2
);

  wire and_1_out, and_2_out, and_3_out, and_4_out, d_ff_1_q, d_ff_2_q, d_ff_3_q, d_ff_4_q, d_ff_5_q,
       d_ff_6_q, d_ff_7_q, d_ff_8_q, d_ff_9_q, d_ff_10_q, d_ff_11_q, d_ff_12_q, d_ff_13_q, d_ff_14_q,
       d_ff_15_q, d_ff_16_q;

  D_Flip_Flop d_ff_1 (.D(Bouton1), .clk(CLK), .Q(d_ff_1_q), .reset(E));  // open: Qn, preset
  D_Flip_Flop d_ff_2 (.D(Bouton2), .clk(CLK), .Q(d_ff_2_q), .reset(E));  // open: Qn, preset
  D_Flip_Flop d_ff_3 (.D(d_ff_1_q), .clk(CLK), .Q(d_ff_3_q), .reset(E));  // open: Qn, preset
  D_Flip_Flop d_ff_4 (.D(d_ff_2_q), .clk(CLK), .Q(d_ff_4_q), .reset(E));  // open: Qn, preset
  D_Flip_Flop d_ff_5 (.D(d_ff_3_q), .clk(CLK), .Q(d_ff_5_q), .reset(E));  // open: Qn, preset
  D_Flip_Flop d_ff_6 (.D(d_ff_4_q), .clk(CLK), .Q(d_ff_6_q), .reset(E));  // open: Qn, preset
  and and_1 (and_1_out, ~d_ff_1_q, d_ff_3_q);  // AND_Gate
  D_Flip_Flop d_ff_7 (.D(d_ff_5_q), .clk(CLK), .Q(d_ff_7_q), .reset(E));  // open: Qn, preset
  and and_2 (and_2_out, ~d_ff_2_q, d_ff_4_q);  // AND_Gate
  D_Flip_Flop d_ff_8 (.D(d_ff_6_q), .clk(CLK), .Q(d_ff_8_q), .reset(E));  // open: Qn, preset
  D_Flip_Flop d_ff_9 (.D(d_ff_7_q), .clk(CLK), .Q(d_ff_9_q), .reset(E));  // open: Qn, preset
  D_Flip_Flop d_ff_10 (.D(d_ff_8_q), .clk(CLK), .Q(d_ff_10_q), .reset(E));  // open: Qn, preset
  D_Flip_Flop d_ff_11 (.D(d_ff_9_q), .clk(CLK), .Q(d_ff_11_q), .reset(E));  // open: Qn, preset
  D_Flip_Flop d_ff_12 (.D(d_ff_10_q), .clk(CLK), .Q(d_ff_12_q), .reset(E));  // open: Qn, preset
  D_Flip_Flop d_ff_13 (.D(d_ff_11_q), .clk(CLK), .Q(d_ff_13_q), .reset(E));  // open: Qn, preset
  D_Flip_Flop d_ff_14 (.D(d_ff_12_q), .clk(CLK), .Q(d_ff_14_q), .reset(E));  // open: Qn, preset
  D_Flip_Flop d_ff_15 (.D(d_ff_13_q), .clk(CLK), .Q(d_ff_15_q), .reset(E));  // open: Qn, preset
  D_Flip_Flop d_ff_16 (.D(d_ff_14_q), .clk(CLK), .Q(d_ff_16_q), .reset(E));  // open: Qn, preset
  and and_3 (and_3_out, d_ff_5_q, d_ff_7_q, d_ff_9_q, d_ff_11_q, d_ff_13_q, d_ff_15_q);
  and and_4 (and_4_out, d_ff_6_q, d_ff_8_q, d_ff_10_q, d_ff_12_q, d_ff_14_q, d_ff_16_q);
  and and_5 (BC1, ~and_3_out, and_1_out);  // AND_Gate
  and and_6 (BL1, and_3_out, and_1_out);
  and and_7 (BC2, ~and_4_out, and_2_out);  // AND_Gate
  and and_8 (BL2, and_4_out, and_2_out);
endmodule

module temps (
  input  [22:0] TempsIN,
  input  CLK,
  input  E,
  output [22:0] TEMPSOUT
);

  wire comparator_1_eq;
  wire [22:0] adder_1_out, register_1_q;

  Adder #(.width(23)) adder_1 (.a(TempsIN), .b(23'h1), .out(adder_1_out));  // open: cin, cout
  Register #(.width(23)) register_1 (.D(adder_1_out), .clk(CLK), .Q(register_1_q), .clr(E));  // open: en
  Comparator #(.width(23), .mode("unsigned")) comparator_1 (
    .a(register_1_q), .b(23'h5c4900), .eq(comparator_1_eq));  // open: gt, lt
  Multiplexer #(.width(23), .enable("false")) multiplexer_1 (
    .in0(register_1_q), .in1({23{1'b0}}), .out(TEMPSOUT), .sel(comparator_1_eq));
endmodule

module def_etat (
  input  [3:0] Boutons_IN,
  input  [2:0] Etat_IN,
  input  Sous_Etat,
  input  CLK,
  input  E,
  input  Sonne,
  output [2:0] Etat_OUT,
  output [3:0] Boutons_OUT
);

  wire and_1_out, and_2_out, not_1_out, not_2_out, not_3_out, not_4_out, not_5_out, not_6_out, or_1_out;
  wire [1:0] and_3_out;
  wire [2:0] multiplexer_1_out, multiplexer_2_out;

  Multiplexer #(.width(3), .enable("false")) multiplexer_1 (
    .in0(Etat_IN), .in1(3'b100), .out(multiplexer_1_out), .sel(Sonne));
  not not_1 (not_1_out, multiplexer_1_out[2]);
  and and_1 (and_1_out, not_1_out, not_2_out, multiplexer_1_out[0]);
  not not_2 (not_2_out, multiplexer_1_out[1]);
  not not_3 (not_3_out, multiplexer_1_out[2]);
  and and_2 (and_2_out, not_3_out, multiplexer_1_out[1], not_4_out);
  not not_4 (not_4_out, multiplexer_1_out[0]);
  not not_5 (not_5_out, multiplexer_1_out[2]);
  and and_3 (and_3_out[0], not_5_out, not_6_out);
  not not_6 (not_6_out, multiplexer_1_out[0]);
  or or_1 (or_1_out, Sous_Etat, ~Boutons_IN[0]);  // OR_Gate
  and and_4 (Boutons_OUT[0], Sous_Etat, Boutons_IN[0]);
  or or_2 (and_3_out[1], and_1_out, and_2_out);
  Multiplexer #(.width(3), .enable("false")) multiplexer_2 (
    .in0({1'b0, and_3_out}), .in1(multiplexer_1_out), .out(multiplexer_2_out), .sel(or_1_out));
  Register #(.width(3)) register_1 (.D(multiplexer_2_out), .clk(CLK), .Q(Etat_OUT), .clr(E));  // open: en

  assign Boutons_OUT[3:1] = Boutons_IN[3:1];
endmodule

module CLK_Reelle (
  input  CLK,
  input  E,
  output CLK_1024,
  output CLK_512,
  output CLK_10
);

  wire and_1_out, and_2_out, if_51_out, if_52_out, multiplexer_1_out, or_1_out, or_2_out, or_3_out, or_4_out,
       or_5_out, or_6_out, or_7_out, or_8_out, or_9_out, t_ff_2_q, t_ff_3_q, t_ff_4_q, t_ff_5_q, t_ff_6_q,
       t_ff_7_q, t_ff_8_q, t_ff_9_q;

  T_Flip_Flop t_ff_1 (.T(1'b1), .clk(CLK), .Q(CLK_512), .reset(or_1_out));  // open: Qn, preset
  or or_1 (or_1_out, E, multiplexer_1_out);
  T_Flip_Flop t_ff_2 (.T(1'b1), .clk(multiplexer_1_out), .Q(t_ff_2_q), .reset(or_2_out));  // open: Qn, preset
  or or_2 (or_2_out, E, and_2_out);
  T_Flip_Flop t_ff_3 (.T(1'b1), .clk(CLK_512), .Q(t_ff_3_q), .reset(or_3_out));  // open: Qn, preset
  or or_3 (or_3_out, E, multiplexer_1_out);
  T_Flip_Flop t_ff_4 (.T(1'b1), .clk(t_ff_2_q), .Q(t_ff_4_q), .reset(or_4_out));  // open: Qn, preset
  or or_4 (or_4_out, E, and_2_out);
  T_Flip_Flop t_ff_5 (.T(1'b1), .clk(t_ff_3_q), .Q(t_ff_5_q), .reset(or_5_out));  // open: Qn, preset
  and if_51 (if_51_out, CLK_512, ~t_ff_3_q, t_ff_5_q, t_ff_7_q, ~t_ff_8_q, ~t_ff_9_q);  // AND_Gate
  T_Flip_Flop t_ff_6 (.T(1'b1), .clk(t_ff_4_q), .Q(t_ff_6_q), .reset(or_6_out));  // open: Qn, preset
  or or_5 (or_5_out, E, multiplexer_1_out);
  or or_6 (or_6_out, E, and_2_out);
  T_Flip_Flop t_ff_7 (.T(1'b1), .clk(t_ff_5_q), .Q(t_ff_7_q), .reset(or_7_out));  // open: Qn, preset
  or or_7 (or_7_out, E, multiplexer_1_out);
  and if_52 (if_52_out, ~CLK_512, ~t_ff_3_q, t_ff_5_q, t_ff_7_q, ~t_ff_8_q, ~t_ff_9_q);  // AND_Gate
  T_Flip_Flop t_ff_8 (.T(1'b1), .clk(t_ff_7_q), .Q(t_ff_8_q), .reset(or_8_out));  // open: Qn, preset
  or or_8 (or_8_out, E, multiplexer_1_out);
  and and_1 (and_1_out, ~t_ff_2_q, ~t_ff_4_q, t_ff_6_q);  // AND_Gate
  T_Flip_Flop t_ff_9 (.T(1'b1), .clk(t_ff_8_q), .Q(t_ff_9_q), .reset(or_9_out));  // open: Qn, preset
  or or_9 (or_9_out, E, multiplexer_1_out);
  Multiplexer #(.enable("false")) multiplexer_1 (
    .in0(if_51_out), .in1(if_52_out), .out(multiplexer_1_out), .sel(and_1_out));
  and and_2 (and_2_out, and_1_out, if_52_out, multiplexer_1_out);
  T_Flip_Flop t_ff_10 (.T(1'b1), .clk(multiplexer_1_out), .Q(CLK_10), .reset(E));  // open: Qn, preset

  assign CLK_1024 = CLK;
endmodule

module Buzzer (
  input  Active,
  input  CLK_1024,
  input  CLK_10,
  input  E,
  output Pin_Buzzer
);

  wire and_1_out, d_ff_1_q, d_ff_2_q, d_ff_3_q, d_ff_4_q, or_1_out, t_ff_1_q, t_ff_2_q;

  T_Flip_Flop t_ff_1 (.T(1'b1), .clk(CLK_10), .Q(t_ff_1_q));  // open: Qn, reset, preset
  T_Flip_Flop t_ff_2 (.T(t_ff_1_q), .clk(CLK_10), .Q(t_ff_2_q));  // open: Qn, reset, preset
  D_Flip_Flop d_ff_1 (.D(1'b1), .clk(t_ff_2_q), .Q(d_ff_1_q), .reset(or_1_out));  // open: Qn, preset
  D_Flip_Flop d_ff_2 (.D(d_ff_1_q), .clk(t_ff_2_q), .Q(d_ff_2_q), .reset(or_1_out));  // open: Qn, preset
  D_Flip_Flop d_ff_3 (.D(d_ff_2_q), .clk(t_ff_2_q), .Q(d_ff_3_q), .reset(or_1_out));  // open: Qn, preset
  D_Flip_Flop d_ff_4 (.D(d_ff_3_q), .clk(t_ff_2_q), .Q(d_ff_4_q), .reset(or_1_out));  // open: Qn, preset
  and and_1 (and_1_out, d_ff_4_q, ~t_ff_2_q);  // AND_Gate
  or or_1 (or_1_out, and_1_out, E);
  and and_2 (Pin_Buzzer, Active, CLK_1024, t_ff_2_q, ~d_ff_4_q);  // AND_Gate
endmodule

module Choix_leds (
  input  [2:0] Entree,
  output [1:0] Sortie
);

  wire and_1_out;

  and and_1 (and_1_out, Entree[1], Entree[0]);
  or or_1 (Sortie[1], and_1_out, Entree[2]);

  assign Sortie[0] = Entree[1];
endmodule

module Heure (
  input  [22:0] Temps,
  input  [3:0] Boutons,
  input  [2:0] Etat,
  input  E,
  input  CLK,
  output [7:0] Seg0,
  output [7:0] Seg1,
  output [7:0] Seg2,
  output [7:0] Seg3,
  output [7:0] Seg4,
  output [7:0] Seg5,
  output [22:0] Temps_a_modifier,
  output Modifier_temps,
  output sous_systeme
);

  wire and_1_out, Lect_jours_q, nor_1_out, not_1_out, Set_Heure_q;
  wire [1:0] H_set_1_modifie;

  nor nor_1 (nor_1_out, Etat[0], Etat[1], Etat[2]);
  T_Flip_Flop Set_Heure (.T(nor_1_out), .clk(Boutons[1]), .Q(Set_Heure_q), .reset(E));  // open: Qn, preset
  and and_1 (and_1_out, ~Set_Heure_q, nor_1_out, Boutons[3]);  // AND_Gate
  T_Flip_Flop Lect_jours (.T(1'b1), .clk(and_1_out), .Q(Lect_jours_q), .reset(E));  // open: Qn, preset
  H_set H_set_1 (
    .Temps_actuel(Temps), .Set(Set_Heure_q), .B1C(Boutons[0]), .B2C(Boutons[2]), .CLK(CLK), .E(E),
    .Temps_a_set(Temps_a_modifier), .Modifie(H_set_1_modifie));
  not not_1 (not_1_out, Set_Heure_q);
  gen_impulsion_longue gen_impulsion_longue_1 (.Entree(not_1_out), .CLK(CLK), .E(E), .Output_1(Modifier_temps));
  H_affiche H_affiche_1 (
    .Temps(Temps), .Temps_Set(Temps_a_modifier), .Set(Set_Heure_q), .Modifie(H_set_1_modifie),
    .Clignote(Temps[2]), .Vue_jours(Lect_jours_q), .Output_bus_1(Seg0), .Output_bus_2(Seg1),
    .Output_bus_3(Seg2), .Output_bus_4(Seg3), .Output_bus_5(Seg4), .Output_bus_6(Seg5));
  and and_2 (sous_systeme, Set_Heure_q, nor_1_out);
endmodule

module H_affiche (
  input  [22:0] Temps,
  input  [22:0] Temps_Set,
  input  Set,
  input  [1:0] Modifie,
  input  Clignote,
  input  Vue_jours,
  output [7:0] Output_bus_1,
  output [7:0] Output_bus_2,
  output [7:0] Output_bus_3,
  output [7:0] Output_bus_4,
  output [7:0] Output_bus_5,
  output [7:0] Output_bus_6
);

  wire and_1_out, and_2_out, and_3_out, and_4_out, and_5_out, or_1_out, or_2_out, or_3_out, or_4_out;
  wire [2:0] Conv_temps_1_jours;
  wire [3:0] adder_1_out, conv_unit_dizaines_1_dizaines, conv_unit_dizaines_1_unites,
       conv_unit_dizaines_2_dizaines, conv_unit_dizaines_2_unites, conv_unit_dizaines_3_dizaines,
       conv_unit_dizaines_3_unites, multiplexer_2_out, multiplexer_3_out, multiplexer_4_out,
       multiplexer_5_out, multiplexer_6_out;
  wire [4:0] Conv_temps_1_heures;
  wire [5:0] Conv_temps_1_minutes, Conv_temps_1_secondes;
  wire [7:0] Chiffre_7seg_1_sortie, Chiffre_7seg_2_sortie, Chiffre_7seg_3_sortie, Chiffre_7seg_4_sortie,
       Chiffre_7seg_6_sortie, Chiffre_7seg_7_sortie;
  wire [22:0] multiplexer_1_out;

  Multiplexer #(.width(23), .enable("false")) multiplexer_1 (
    .in0(Temps), .in1(Temps_Set), .out(multiplexer_1_out), .sel(Set));
  and and_1 (and_1_out, Set, ~Modifie[0], ~Modifie[1], Clignote);  // AND_Gate
  and and_2 (and_2_out, Set, ~Modifie[1], Modifie[0], Clignote);  // AND_Gate
  and and_3 (and_3_out, Set, Modifie[1], ~Modifie[0], Clignote);  // AND_Gate
  and and_4 (and_4_out, Set, Modifie[1], Modifie[0], Clignote);
  Conv_temps Conv_temps_1 (
    .Temps(multiplexer_1_out), .Jours(Conv_temps_1_jours), .Heures(Conv_temps_1_heures),
    .Minutes(Conv_temps_1_minutes), .Secondes(Conv_temps_1_secondes));  // open: dixiemes
  Adder #(.width(4)) adder_1 (.a(4'b0001), .b({1'b0, Conv_temps_1_jours}), .out(adder_1_out));  // open: cin, cout
  conv_unit_dizaines conv_unit_dizaines_1 (
    .entree({1'b0, Conv_temps_1_heures}), .Dizaines(conv_unit_dizaines_1_dizaines),
    .Unites(conv_unit_dizaines_1_unites));
  conv_unit_dizaines conv_unit_dizaines_2 (
    .entree(Conv_temps_1_minutes), .Dizaines(conv_unit_dizaines_2_dizaines),
    .Unites(conv_unit_dizaines_2_unites));
  conv_unit_dizaines conv_unit_dizaines_3 (
    .entree(Conv_temps_1_secondes), .Dizaines(conv_unit_dizaines_3_dizaines),
    .Unites(conv_unit_dizaines_3_unites));
  or or_1 (or_1_out, Set, Vue_jours);
  and and_5 (and_5_out, and_1_out, ~Vue_jours);  // AND_Gate
  or or_2 (or_2_out, and_2_out, Vue_jours);
  or or_3 (or_3_out, and_3_out, Vue_jours);
  or or_4 (or_4_out, and_4_out, Vue_jours);
  Multiplexer #(.width(4), .enable("false")) multiplexer_2 (
    .in0(conv_unit_dizaines_1_dizaines), .in1(adder_1_out), .out(multiplexer_2_out), .sel(or_1_out));
  Multiplexer #(.width(4), .enable("false")) multiplexer_3 (
    .in0(conv_unit_dizaines_2_dizaines), .in1(conv_unit_dizaines_1_dizaines), .out(multiplexer_3_out),
    .sel(or_1_out));
  Multiplexer #(.width(4), .enable("false")) multiplexer_4 (
    .in0(conv_unit_dizaines_2_unites), .in1(conv_unit_dizaines_1_unites), .out(multiplexer_4_out),
    .sel(or_1_out));
  Multiplexer #(.width(4), .enable("false")) multiplexer_5 (
    .in0(conv_unit_dizaines_3_dizaines), .in1(conv_unit_dizaines_2_dizaines), .out(multiplexer_5_out),
    .sel(or_1_out));
  Multiplexer #(.width(4), .enable("false")) multiplexer_6 (
    .in0(conv_unit_dizaines_3_unites), .in1(conv_unit_dizaines_2_unites), .out(multiplexer_6_out),
    .sel(or_1_out));
  Chiffre_7seg Chiffre_7seg_1 (.Point(1'b0), .Sortie(Chiffre_7seg_1_sortie), .Entree(multiplexer_2_out));
  Chiffre_7seg Chiffre_7seg_2 (.Point(1'b1), .Sortie(Chiffre_7seg_2_sortie), .Entree(conv_unit_dizaines_1_unites));
  Chiffre_7seg Chiffre_7seg_3 (.Point(1'b0), .Sortie(Chiffre_7seg_3_sortie), .Entree(multiplexer_3_out));
  Chiffre_7seg Chiffre_7seg_4 (.Point(1'b1), .Sortie(Chiffre_7seg_4_sortie), .Entree(multiplexer_4_out));
  Chiffre_7seg Chiffre_7seg_7 (.Point(1'b0), .Sortie(Chiffre_7seg_7_sortie), .Entree(multiplexer_5_out));
  Chiffre_7seg Chiffre_7seg_6 (.Point(1'b0), .Sortie(Chiffre_7seg_6_sortie), .Entree(multiplexer_6_out));
  Multiplexer #(.width(8), .enable("false")) multiplexer_7 (
    .in0(Chiffre_7seg_1_sortie), .in1({8{1'b0}}), .out(Output_bus_1), .sel(and_5_out));
  Multiplexer #(.width(8), .enable("false")) multiplexer_8 (
    .in0(Chiffre_7seg_2_sortie), .in1({8{1'b0}}), .out(Output_bus_2), .sel(or_1_out));
  Multiplexer #(.width(8), .enable("false")) multiplexer_9 (
    .in0(Chiffre_7seg_3_sortie), .in1({8{1'b0}}), .out(Output_bus_3), .sel(or_2_out));
  Multiplexer #(.width(8), .enable("false")) multiplexer_10 (
    .in0(Chiffre_7seg_4_sortie), .in1({8{1'b0}}), .out(Output_bus_4), .sel(or_2_out));
  Multiplexer #(.width(8), .enable("false")) multiplexer_11 (
    .in0(Chiffre_7seg_7_sortie), .in1({8{1'b0}}), .out(Output_bus_5), .sel(or_3_out));
  Multiplexer #(.width(8), .enable("false")) multiplexer_12 (
    .in0(Chiffre_7seg_6_sortie), .in1({8{1'b0}}), .out(Output_bus_6), .sel(or_4_out));
endmodule

module H_set (
  input  [22:0] Temps_actuel,
  input  Set,
  input  B1C,
  input  B2C,
  input  CLK,
  input  E,
  output [22:0] Temps_a_set,
  output [1:0] Modifie
);

  wire and_1_out, comparator_1_eq, comparator_1_gt, d_ff_1_q, d_ff_2_q, d_ff_3_q, or_1_out, or_2_out;
  wire [1:0] adder_1_out;
  wire [22:0] adder_2_out, multiplexer_1_out, multiplexer_2_out, multiplexer_3_out, subtractor_1_out;

  D_Flip_Flop #(.trigger("falling")) d_ff_1 (.D(Set), .clk(CLK), .Q(d_ff_1_q), .reset(E));  // open: Qn, preset
  D_Flip_Flop d_ff_2 (.D(Set), .clk(CLK), .Q(d_ff_2_q), .reset(E));  // open: Qn, preset
  and and_1 (and_1_out, Set, ~d_ff_1_q, CLK);  // AND_Gate
  Register #(.width(2)) register_1 (.D(adder_1_out), .clk(B2C), .Q(Modifie), .clr(E));  // open: en
  Adder #(.width(2)) adder_1 (.a(Modifie), .b(2'b01), .out(adder_1_out));  // open: cin, cout
  D_Flip_Flop d_ff_3 (.D(d_ff_2_q), .clk(CLK), .Q(d_ff_3_q), .reset(E));  // open: Qn, preset
  or or_1 (or_1_out, and_1_out, B1C);
  Multiplexer #(.select(2), .width(23), .enable("false")) multiplexer_1 (
    .in0(23'hd2f00), .in1(23'h8ca0), .in2(23'h1770), .in3(23'h258), .out(multiplexer_1_out), .sel(Modifie));
  Adder #(.width(23)) adder_2 (.a(Temps_a_set), .b(multiplexer_1_out), .out(adder_2_out));  // open: cin, cout
  Multiplexer #(.width(23), .enable("false")) multiplexer_2 (
    .in0(Temps_actuel), .in1(adder_2_out), .out(multiplexer_2_out), .sel(d_ff_3_q));
  Subtractor #(.width(23)) subtractor_1 (
    .a(multiplexer_2_out), .b(23'h5c4900), .out(subtractor_1_out));  // open: bin, bout
  Comparator #(.width(23), .mode("unsigned")) comparator_1 (
    .a(multiplexer_2_out), .b(23'h5c4900), .gt(comparator_1_gt), .eq(comparator_1_eq));  // open: lt
  Multiplexer #(.width(23), .enable("false")) multiplexer_3 (
    .in0(multiplexer_2_out), .in1(subtractor_1_out), .out(multiplexer_3_out), .sel(or_2_out));
  or or_2 (or_2_out, comparator_1_gt, comparator_1_eq);
  Register #(.width(23)) register_2 (.D(multiplexer_3_out), .clk(or_1_out), .Q(Temps_a_set), .clr(E));  // open: en
endmodule

module Alarme (
  input  [22:0] Temps,
  input  [3:0] Boutons,
  input  [2:0] Etat,
  input  E,
  output [6:0] LEDs,
  output [7:0] Seg0,
  output [7:0] Seg1,
  output [7:0] Seg2,
  output [7:0] Seg3,
  output [7:0] Seg4,
  output [7:0] Seg5,
  output Sonne,
  output Sous_systeme
);

  wire and_1_out, and_2_out, and_3_out, and_4_out, and_5_out, and_6_out, or_1_out, or_2_out, or_3_out,
       or_4_out, or_5_out, or_6_out, or_7_out, t_ff_1_q;
  wire [1:0] A_detect_selection_1_s_out_2b;
  wire [2:0] A_detect_jour_1_j_3b, and_7_out;
  wire [5:0] J1_out;
  wire [6:6] J7_q;
  wire [22:0] multiplexer_1_out, multiplexer_2_out, Set_alarme_1_valeur, Set_alarme_2_valeur,
       Set_alarme_3_valeur, Set_alarme_4_valeur, Set_alarme_5_valeur, Set_alarme_6_valeur,
       Set_alarme_7_valeur;

  and and_1 (and_1_out, Etat[0], ~Etat[1], ~Etat[2]);  // AND_Gate
  and and_2 (and_2_out, Boutons[2], and_1_out, ~t_ff_1_q);  // AND_Gate
  and and_3 (and_3_out, Boutons[2], t_ff_1_q);
  D_Flip_Flop J2 (.D(1'b1), .clk(and_2_out), .Q(J1_out[1]), .reset(or_2_out));  // open: Qn, preset
  D_Flip_Flop J3 (.D(J1_out[1]), .clk(and_2_out), .Q(J1_out[2]), .reset(or_3_out));  // open: Qn, preset
  D_Flip_Flop J4 (.D(J1_out[2]), .clk(and_2_out), .Q(J1_out[3]), .reset(or_4_out));  // open: Qn, preset
  D_Flip_Flop J5 (.D(J1_out[3]), .clk(and_2_out), .Q(J1_out[4]), .reset(or_5_out));  // open: Qn, preset
  D_Flip_Flop J6 (.D(J1_out[4]), .clk(and_2_out), .Q(J1_out[5]), .reset(or_6_out));  // open: Qn, preset
  D_Flip_Flop J7 (.D(J1_out[5]), .clk(and_2_out), .Q(J7_q[6]));  // open: Qn, preset, reset
  T_Flip_Flop t_ff_1 (.T(1'b1), .clk(and_4_out), .Q(t_ff_1_q), .reset(E));  // open: Qn, preset
  and and_4 (and_4_out, Boutons[1], and_1_out);
  or or_1 (or_1_out, and_4_out, E);
  and J1 (J1_out[0], ~or_2_out, ~J1_out[1]);  // AND_Gate
  or or_2 (or_2_out, J1_out[2], or_3_out);
  or or_3 (or_3_out, J1_out[3], or_4_out);
  or or_4 (or_4_out, J1_out[4], or_5_out);
  or or_5 (or_5_out, J1_out[5], or_6_out);
  or or_6 (or_6_out, J7_q[6], E);
  and and_5 (and_5_out, Boutons[0], t_ff_1_q);
  and and_6 (and_6_out, Boutons[3], and_1_out);
  D_Flip_Flop d_ff_1 (.D(1'b1), .clk(and_3_out), .Q(and_7_out[1]), .reset(or_7_out));  // open: Qn, preset
  D_Flip_Flop d_ff_2 (.D(and_7_out[1]), .clk(and_3_out), .Q(and_7_out[2]), .reset(or_1_out));  // open: Qn, preset
  or or_7 (or_7_out, and_7_out[2], or_1_out);
  and and_7 (and_7_out[0], ~and_7_out[1], ~and_7_out[2]);  // AND_Gate
  A_set_alarme Set_alarme_1 (
    .est_actif(LEDs[0]), .Valeur(Set_alarme_1_valeur), .Nbr_a_ajouter(multiplexer_1_out),
    .set_actif(and_6_out), .E(J1_out[0]), .add(and_5_out), .reset(E));
  A_set_alarme Set_alarme_2 (
    .est_actif(LEDs[1]), .Valeur(Set_alarme_2_valeur), .Nbr_a_ajouter(multiplexer_1_out),
    .set_actif(and_6_out), .E(J1_out[1]), .add(and_5_out), .reset(E));
  A_set_alarme Set_alarme_3 (
    .est_actif(LEDs[2]), .Valeur(Set_alarme_3_valeur), .Nbr_a_ajouter(multiplexer_1_out),
    .set_actif(and_6_out), .E(J1_out[2]), .add(and_5_out), .reset(E));
  A_set_alarme Set_alarme_4 (
    .est_actif(LEDs[3]), .Valeur(Set_alarme_4_valeur), .Nbr_a_ajouter(multiplexer_1_out),
    .set_actif(and_6_out), .E(J1_out[3]), .add(and_5_out), .reset(E));
  A_set_alarme Set_alarme_5 (
    .est_actif(LEDs[4]), .Valeur(Set_alarme_5_valeur), .Nbr_a_ajouter(multiplexer_1_out),
    .set_actif(and_6_out), .E(J1_out[4]), .add(and_5_out), .reset(E));
  A_set_alarme Set_alarme_6 (
    .est_actif(LEDs[5]), .Valeur(Set_alarme_6_valeur), .Nbr_a_ajouter(multiplexer_1_out),
    .set_actif(and_6_out), .E(J1_out[5]), .add(and_5_out), .reset(E));
  A_set_alarme Set_alarme_7 (
    .est_actif(LEDs[6]), .Valeur(Set_alarme_7_valeur), .Nbr_a_ajouter(multiplexer_1_out),
    .set_actif(and_6_out), .E(J7_q[6]), .add(and_5_out), .reset(E));
  A_detect_selection A_detect_selection_1 (.S_IN_3b(and_7_out), .S_OUT_2b(A_detect_selection_1_s_out_2b));
  Multiplexer #(.select(2), .width(23), .enable("false")) multiplexer_1 (
    .in0(23'h8ca0), .in1(23'h1770), .in2(23'h258), .in3({23{1'b0}}), .out(multiplexer_1_out),
    .sel(A_detect_selection_1_s_out_2b));
  Multiplexer #(.select(3), .width(23), .enable("false")) multiplexer_2 (
    .in1(Set_alarme_1_valeur), .in2(Set_alarme_2_valeur), .in3(Set_alarme_3_valeur),
    .in4(Set_alarme_4_valeur), .in5(Set_alarme_5_valeur), .in6(Set_alarme_6_valeur),
    .in7(Set_alarme_7_valeur), .out(multiplexer_2_out), .sel(A_detect_jour_1_j_3b));  // open: in0
  A_detect_jour A_detect_jour_1 (.J_7b({J7_q[6], J1_out}), .J_3b(A_detect_jour_1_j_3b));
  A_detect_sonne detect_sonne_1 (
    .Temps(Temps), .Actif(LEDs), .J1(Set_alarme_1_valeur), .J2(Set_alarme_2_valeur),
    .J3(Set_alarme_3_valeur), .J4(Set_alarme_4_valeur), .J5(Set_alarme_5_valeur), .J6(Set_alarme_6_valeur),
    .J7(Set_alarme_7_valeur), .Sonne(Sonne));
  and and_8 (Sous_systeme, t_ff_1_q, and_1_out);
  A_affiche A_affiche_1 (
    .Clignot_activation(t_ff_1_q), .Jour(A_detect_jour_1_j_3b), .Regle(and_7_out), .Clignotement(Temps[2]),
    .Temps(multiplexer_2_out), .Seg0(Seg0), .Seg1(Seg1), .Seg2(Seg2), .Seg3(Seg3), .Seg4(Seg4), .Seg5(Seg5));
endmodule

module A_set_alarme (
  input  E,
  input  add,
  input  set_actif,
  input  reset,
  input  [22:0] Nbr_a_ajouter,
  output [22:0] Valeur,
  output est_actif
);

  wire and_1_out, and_2_out;
  wire [22:0] adder_1_out;

  and and_1 (and_1_out, add, E);
  and and_2 (and_2_out, E, set_actif);
  T_Flip_Flop t_ff_1 (.T(1'b1), .clk(and_2_out), .Q(est_actif), .reset(reset));  // open: Qn, preset
  Register #(.width(23)) register_1 (.D(adder_1_out), .clk(and_1_out), .Q(Valeur), .clr(reset));  // open: en
  Adder #(.width(23)) adder_1 (.a(Nbr_a_ajouter), .b(Valeur), .out(adder_1_out));  // open: cin, cout
endmodule

module A_detect_jour (
  input  [6:0] J_7b,
  output [2:0] J_3b
);

  wire not_1_out, not_2_out, not_3_out, not_4_out, not_5_out, not_6_out, not_7_out, not_8_out, not_9_out;

  not not_1 (not_1_out, J_7b[0]);
  not not_2 (not_2_out, J_7b[1]);
  not not_3 (not_3_out, J_7b[2]);
  not not_4 (not_4_out, J_7b[0]);
  not not_5 (not_5_out, J_7b[3]);
  not not_6 (not_6_out, J_7b[4]);
  not not_7 (not_7_out, J_7b[1]);
  not not_8 (not_8_out, J_7b[3]);
  not not_9 (not_9_out, J_7b[5]);
  and and_1 (J_3b[2], not_1_out, not_2_out, not_3_out);
  and and_2 (J_3b[1], not_4_out, not_5_out, not_6_out);
  and and_3 (J_3b[0], not_7_out, not_8_out, not_9_out);
endmodule

module A_detect_selection (
  input  [2:0] S_IN_3b,
  output [1:0] S_OUT_2b
);

  wire not_1_out, not_2_out, not_3_out, not_4_out;

  not not_1 (not_1_out, S_IN_3b[1]);
  not not_2 (not_2_out, S_IN_3b[0]);
  not not_3 (not_3_out, S_IN_3b[2]);
  not not_4 (not_4_out, S_IN_3b[0]);
  and and_1 (S_OUT_2b[1], not_1_out, not_2_out);
  and and_2 (S_OUT_2b[0], not_3_out, not_4_out);
endmodule

module A_detect_sonne (
  input  [22:0] Temps,
  input  [6:0] Actif,
  input  [22:0] J1,
  input  [22:0] J2,
  input  [22:0] J3,
  input  [22:0] J4,
  input  [22:0] J5,
  input  [22:0] J6,
  input  [22:0] J7,
  output Sonne
);

  wire and_1_out, and_2_out, and_3_out, and_4_out, and_5_out, and_6_out, and_7_out, comparator_1_eq,
       comparator_2_eq, comparator_3_eq, comparator_4_eq, comparator_5_eq, comparator_6_eq, comparator_7_eq;
  wire [22:0] subtractor_1_out, subtractor_2_out, subtractor_3_out, subtractor_4_out, subtractor_5_out,
       subtractor_6_out;

  Comparator #(.width(23), .mode("unsigned")) comparator_1 (.a(Temps), .b(J1), .eq(comparator_1_eq));  // open: gt, lt
  Subtractor #(.width(23)) subtractor_1 (.a(Temps), .b(23'hd2f00), .out(subtractor_1_out));  // open: bin, bout
  Subtractor #(.width(23)) subtractor_2 (
    .a(subtractor_1_out), .b(23'hd2f00), .out(subtractor_2_out));  // open: bin, bout
  Subtractor #(.width(23)) subtractor_3 (
    .a(subtractor_2_out), .b(23'hd2f00), .out(subtractor_3_out));  // open: bin, bout
  Subtractor #(.width(23)) subtractor_4 (
    .a(subtractor_3_out), .b(23'hd2f00), .out(subtractor_4_out));  // open: bin, bout
  Subtractor #(.width(23)) subtractor_5 (
    .a(subtractor_4_out), .b(23'hd2f00), .out(subtractor_5_out));  // open: bin, bout
  Subtractor #(.width(23)) subtractor_6 (
    .a(subtractor_5_out), .b(23'hd2f00), .out(subtractor_6_out));  // open: bin, bout
  Comparator #(.width(23), .mode("unsigned")) comparator_2 (
    .a(subtractor_1_out), .b(J2), .eq(comparator_2_eq));  // open: gt, lt
  Comparator #(.width(23), .mode("unsigned")) comparator_3 (
    .a(subtractor_2_out), .b(J3), .eq(comparator_3_eq));  // open: gt, lt
  Comparator #(.width(23), .mode("unsigned")) comparator_4 (
    .a(subtractor_3_out), .b(J4), .eq(comparator_4_eq));  // open: gt, lt
  Comparator #(.width(23), .mode("unsigned")) comparator_5 (
    .a(subtractor_4_out), .b(J5), .eq(comparator_5_eq));  // open: gt, lt
  Comparator #(.width(23), .mode("unsigned")) comparator_6 (
    .a(subtractor_5_out), .b(J6), .eq(comparator_6_eq));  // open: gt, lt
  Comparator #(.width(23), .mode("unsigned")) comparator_7 (
    .a(subtractor_6_out), .b(J7), .eq(comparator_7_eq));  // open: gt, lt
  and and_1 (and_1_out, comparator_3_eq, Actif[2]);
  and and_2 (and_2_out, Actif[3], comparator_4_eq);
  and and_3 (and_3_out, comparator_1_eq, Actif[0]);
  and and_4 (and_4_out, Actif[1], comparator_2_eq);
  and and_5 (and_5_out, comparator_5_eq, Actif[4]);
  and and_6 (and_6_out, Actif[5], comparator_6_eq);
  and and_7 (and_7_out, Actif[6], comparator_7_eq);
  or or_1 (Sonne, and_3_out, and_4_out, and_1_out, and_2_out, and_5_out, and_6_out, and_7_out);
endmodule

module A_affiche (
  input  Clignot_activation,
  input  [2:0] Jour,
  input  [2:0] Regle,
  input  Clignotement,
  input  [22:0] Temps,
  output [7:0] Seg0,
  output [7:0] Seg1,
  output [7:0] Seg2,
  output [7:0] Seg3,
  output [7:0] Seg4,
  output [7:0] Seg5
);

  wire nand_1_out, nand_2_out, nand_3_out;
  wire [3:0] conv_unit_dizaines_1_dizaines, conv_unit_dizaines_1_unites, conv_unit_dizaines_2_dizaines,
       conv_unit_dizaines_2_unites;
  wire [4:0] Conv_temps_1_heures;
  wire [5:0] Conv_temps_1_minutes;
  wire [7:0] Chiffre_7seg_2_sortie, Chiffre_7seg_3_sortie, Chiffre_7seg_4_sortie, Chiffre_7seg_5_sortie;

  Conv_temps Conv_temps_1 (
    .Temps(Temps), .Heures(Conv_temps_1_heures), .Minutes(Conv_temps_1_minutes));  // open: Jours, Secondes, dixiemes
  conv_unit_dizaines conv_unit_dizaines_1 (
    .entree({1'b0, Conv_temps_1_heures}), .Dizaines(conv_unit_dizaines_1_dizaines),
    .Unites(conv_unit_dizaines_1_unites));
  conv_unit_dizaines conv_unit_dizaines_2 (
    .entree(Conv_temps_1_minutes), .Dizaines(conv_unit_dizaines_2_dizaines),
    .Unites(conv_unit_dizaines_2_unites));
  Multiplexer #(.width(8), .enable("false")) multiplexer_1 (
    .in0({8{1'b0}}), .in1(Chiffre_7seg_2_sortie), .out(Seg2), .sel(nand_1_out));
  Chiffre_7seg Chiffre_7seg_2 (.Point(1'b0), .Sortie(Chiffre_7seg_2_sortie), .Entree(conv_unit_dizaines_1_dizaines));
  Chiffre_7seg Chiffre_7seg_3 (.Point(1'b1), .Sortie(Chiffre_7seg_3_sortie), .Entree(conv_unit_dizaines_1_unites));
  Multiplexer #(.width(8), .enable("false")) multiplexer_2 (
    .in0({8{1'b0}}), .in1(Chiffre_7seg_3_sortie), .out(Seg3), .sel(nand_1_out));
  Chiffre_7seg Chiffre_7seg_4 (.Point(1'b0), .Sortie(Chiffre_7seg_4_sortie), .Entree(conv_unit_dizaines_2_dizaines));
  Multiplexer #(.width(8), .enable("false")) multiplexer_3 (
    .in0({8{1'b0}}), .in1(Chiffre_7seg_4_sortie), .out(Seg4), .sel(nand_2_out));
  Multiplexer #(.width(8), .enable("false")) multiplexer_4 (
    .in0({8{1'b0}}), .in1(Chiffre_7seg_5_sortie), .out(Seg5), .sel(nand_3_out));
  Chiffre_7seg Chiffre_7seg_5 (.Point(1'b0), .Sortie(Chiffre_7seg_5_sortie), .Entree(conv_unit_dizaines_2_unites));
  nand nand_1 (nand_1_out, Regle[0], Clignot_activation, Clignotement);
  nand nand_2 (nand_2_out, Regle[1], Clignot_activation, Clignotement);
  nand nand_3 (nand_3_out, Regle[2], Clignot_activation, Clignotement);
  Chiffre_7seg Chiffre_7seg_1 (.Point(1'b0), .Sortie(Seg0), .Entree({1'b0, Jour}));

  assign Seg1 = {8{1'b0}};
endmodule

module Chronometre (
  input  [22:0] Temps,
  input  [3:0] Boutons,
  input  [2:0] Etat,
  input  E,
  output [7:0] Seg0,
  output [7:0] Seg1,
  output [7:0] Seg2,
  output [7:0] Seg3,
  output [7:0] Seg4,
  output [7:0] Seg5,
  output [6:0] Leds,
  output Sous_systeme
);

  wire and_1_out, and_2_out, and_3_out, and_4_out, and_5_out, comparator_1_gt, Conteur_tours_1_aucun_temps,
       Lecture_tours_q, not_1_out, not_2_out, or_1_out, or_2_out, or_3_out, or_5_out, t_ff_1_q;
  wire [22:0] Conteur_tours_1_temps_sortie, Debut_q, FIn_q, multiplexer_1_out, multiplexer_2_out,
       subtractor_1_out, subtractor_2_out, subtractor_3_out, Valeur_en_pause_q;

  and and_1 (and_1_out, ~t_ff_1_q, Boutons[1]);  // AND_Gate
  and and_2 (and_2_out, ~Etat[0], Etat[1], ~Etat[2]);  // AND_Gate
  T_Flip_Flop t_ff_1 (.T(and_3_out), .clk(Boutons[2]), .Q(t_ff_1_q), .reset(E));  // open: Qn, preset
  and and_3 (and_3_out, not_1_out, and_2_out);
  Subtractor #(.width(23)) subtractor_1 (.a(Temps), .b(Valeur_en_pause_q), .out(subtractor_1_out));  // open: bin, bout
  Register #(.width(23)) Debut (.D(subtractor_1_out), .clk(t_ff_1_q), .Q(Debut_q), .clr(or_1_out));  // open: en
  or or_1 (or_1_out, E, and_4_out);
  Register #(.width(23), .trigger("falling")) Valeur_en_pause (
    .D(multiplexer_2_out), .clk(t_ff_1_q), .Q(Valeur_en_pause_q), .clr(or_2_out));  // open: en
  not not_1 (not_1_out, Lecture_tours_q);
  and and_4 (and_4_out, Boutons[3], and_2_out, ~t_ff_1_q);  // AND_Gate
  and and_5 (and_5_out, ~t_ff_1_q, and_2_out);  // AND_Gate
  T_Flip_Flop Lecture_tours (.T(and_5_out), .clk(and_1_out), .Q(Lecture_tours_q), .reset(E));  // open: Qn, preset
  Register #(.width(23), .trigger("falling")) FIn (.D(Temps), .clk(t_ff_1_q), .Q(FIn_q), .clr(or_2_out));  // open: en
  Subtractor #(.width(23)) subtractor_2 (.a(Temps), .b(Debut_q), .out(subtractor_2_out));  // open: bin, bout
  or or_2 (or_2_out, E, and_4_out);
  or or_3 (or_3_out, and_4_out, E);
  Comparator #(.width(23), .mode("unsigned")) comparator_1 (
    .a(FIn_q), .b(Debut_q), .gt(comparator_1_gt));  // open: eq, lt
  Multiplexer #(.width(23), .enable("false")) multiplexer_1 (
    .in0(Temps), .in1(FIn_q), .out(multiplexer_1_out), .sel(not_2_out));
  not not_2 (not_2_out, t_ff_1_q);
  // OR_Gate or_4 has open pins: in0=comparator_1_gt, in1=t_ff_1_q, out=open
  Subtractor #(.width(23)) subtractor_3 (
    .a(multiplexer_1_out), .b(Debut_q), .out(subtractor_3_out));  // open: bin, bout
  C_conteur_tours Conteur_tours_1 (
    .B1L(and_1_out), .B1C(Boutons[0]), .Sous_syst(t_ff_1_q), .Lect_tours(Lecture_tours_q), .Reset(or_3_out),
    .Temps(subtractor_2_out), .temps_sortie(Conteur_tours_1_temps_sortie),
    .Aucun_temps(Conteur_tours_1_aucun_temps), .Leds(Leds));
  Multiplexer #(.width(23), .enable("false")) multiplexer_2 (
    .in0(subtractor_3_out), .in1(Conteur_tours_1_temps_sortie), .out(multiplexer_2_out), .sel(Lecture_tours_q));
  or or_5 (or_5_out, t_ff_1_q, Lecture_tours_q);
  C_affiche C_affiche_1 (
    .Lect_temps(Lecture_tours_q), .Temps(multiplexer_2_out), .Aucun_temps(Conteur_tours_1_aucun_temps),
    .Seg_0(Seg0), .Seg_1(Seg1), .Seg_2(Seg2), .Seg_3(Seg3), .Seg_4(Seg4), .Seg_5(Seg5));
  and and_6 (Sous_systeme, or_5_out, and_2_out);
endmodule

module C_conteur_tours (
  input  B1L,
  input  B1C,
  input  Sous_syst,
  input  Lect_tours,
  input  Reset,
  input  [22:0] Temps,
  output [22:0] temps_sortie,
  output Aucun_temps,
  output [6:0] Leds
);

  wire and_1_out, and_2_out, and_3_out, and_4_out, and_5_out, and_6_out, and_7_out, and_8_out, d_ff_8_q,
       gen_impulsion_delay_1_sortie, not_1_out, or_1_out, or_2_out, or_3_out, or_4_out, or_5_out, or_6_out,
       or_7_out, or_8_out, or_9_out, or_10_out, or_11_out;
  wire [1:0] d_ff_9_q;
  wire [2:0] C_detect_tour_1_t_3bits;
  wire [2:2] d_ff_11_q;
  wire [3:3] d_ff_12_q;
  wire [4:4] d_ff_13_q;
  wire [5:5] d_ff_14_q;
  wire [6:0] and_9_out, d_ff_1_q;
  wire [6:6] d_ff_15_q;
  wire [22:0] register_1_q, register_2_q, register_3_q, register_4_q, register_5_q, register_6_q,
       register_7_q;

  or or_1 (or_1_out, Sous_syst, Lect_tours);
  or or_2 (or_2_out, gen_impulsion_delay_1_sortie, and_1_out);
  and and_1 (and_1_out, or_1_out, B1C);
  or or_3 (or_3_out, d_ff_1_q[6], or_10_out);
  D_Flip_Flop d_ff_1 (.D(1'b1), .clk(or_2_out), .Q(d_ff_1_q[0]), .reset(or_4_out));  // open: Qn, preset
  D_Flip_Flop d_ff_2 (.D(d_ff_1_q[0]), .clk(or_2_out), .Q(d_ff_1_q[1]), .reset(or_5_out));  // open: Qn, preset
  D_Flip_Flop d_ff_3 (.D(d_ff_1_q[1]), .clk(or_2_out), .Q(d_ff_1_q[2]), .reset(or_6_out));  // open: Qn, preset
  D_Flip_Flop d_ff_4 (.D(d_ff_1_q[2]), .clk(or_2_out), .Q(d_ff_1_q[3]), .reset(or_7_out));  // open: Qn, preset
  D_Flip_Flop d_ff_5 (.D(d_ff_1_q[3]), .clk(or_2_out), .Q(d_ff_1_q[4]), .reset(or_8_out));  // open: Qn, preset
  D_Flip_Flop d_ff_6 (.D(d_ff_1_q[4]), .clk(or_2_out), .Q(d_ff_1_q[5]), .reset(or_9_out));  // open: Qn, preset
  D_Flip_Flop d_ff_7 (.D(d_ff_1_q[5]), .clk(or_2_out), .Q(d_ff_1_q[6]), .reset(or_10_out));  // open: Qn, preset
  D_Flip_Flop d_ff_8 (.D(or_3_out), .clk(or_2_out), .Q(d_ff_8_q), .reset(or_11_out));  // open: Qn, preset
  or or_4 (or_4_out, d_ff_1_q[1], or_5_out);
  or or_5 (or_5_out, d_ff_1_q[2], or_6_out);
  or or_6 (or_6_out, d_ff_1_q[3], or_7_out);
  or or_7 (or_7_out, d_ff_1_q[4], or_8_out);
  or or_8 (or_8_out, d_ff_1_q[5], or_9_out);
  or or_9 (or_9_out, d_ff_1_q[6], or_10_out);
  or or_10 (or_10_out, d_ff_8_q, or_11_out);
  or or_11 (or_11_out, Reset, B1L);
  not not_1 (not_1_out, Lect_tours);
  gen_impulsion_delay gen_impulsion_delay_1 (
    .Entree(Lect_tours), .CLK(Temps[0]), .E(Reset), .Sortie(gen_impulsion_delay_1_sortie));
  Register #(.width(23)) register_1 (.D(Temps), .en(not_1_out), .clk(d_ff_1_q[0]), .Q(register_1_q), .clr(Reset));
  Register #(.width(23)) register_2 (.D(Temps), .en(not_1_out), .clk(d_ff_1_q[1]), .Q(register_2_q), .clr(Reset));
  Register #(.width(23)) register_3 (.D(Temps), .en(not_1_out), .clk(d_ff_1_q[2]), .Q(register_3_q), .clr(Reset));
  Register #(.width(23)) register_4 (.D(Temps), .en(not_1_out), .clk(d_ff_1_q[3]), .Q(register_4_q), .clr(Reset));
  Register #(.width(23)) register_5 (.D(Temps), .en(not_1_out), .clk(d_ff_1_q[4]), .Q(register_5_q), .clr(Reset));
  Register #(.width(23)) register_6 (.D(Temps), .en(not_1_out), .clk(d_ff_1_q[5]), .Q(register_6_q), .clr(Reset));
  Register #(.width(23)) register_7 (.D(Temps), .en(not_1_out), .clk(d_ff_1_q[6]), .Q(register_7_q), .clr(Reset));
  and and_2 (and_2_out, not_1_out, d_ff_1_q[0]);
  and and_3 (and_3_out, not_1_out, d_ff_1_q[1]);
  and and_4 (and_4_out, not_1_out, d_ff_1_q[2]);
  and and_5 (and_5_out, not_1_out, d_ff_1_q[3]);
  and and_6 (and_6_out, not_1_out, d_ff_1_q[4]);
  and and_7 (and_7_out, not_1_out, d_ff_1_q[5]);
  and and_8 (and_8_out, not_1_out, d_ff_1_q[6]);
  D_Flip_Flop d_ff_9 (.D(1'b1), .clk(and_2_out), .Q(d_ff_9_q[0]), .reset(Reset));  // open: Qn, preset
  D_Flip_Flop d_ff_10 (.D(1'b1), .clk(and_3_out), .Q(d_ff_9_q[1]), .reset(Reset));  // open: Qn, preset
  D_Flip_Flop d_ff_11 (.D(1'b1), .clk(and_4_out), .Q(d_ff_11_q[2]), .reset(Reset));  // open: Qn, preset
  D_Flip_Flop d_ff_12 (.D(1'b1), .clk(and_5_out), .Q(d_ff_12_q[3]), .reset(Reset));  // open: Qn, preset
  D_Flip_Flop d_ff_13 (.D(1'b1), .clk(and_6_out), .Q(d_ff_13_q[4]), .reset(Reset));  // open: Qn, preset
  D_Flip_Flop d_ff_14 (.D(1'b1), .clk(and_7_out), .Q(d_ff_14_q[5]), .reset(Reset));  // open: Qn, preset
  D_Flip_Flop d_ff_15 (.D(1'b1), .clk(and_8_out), .Q(d_ff_15_q[6]), .reset(Reset));  // open: Qn, preset
  assign and_9_out = ~{d_ff_15_q[6], d_ff_14_q[5], d_ff_13_q[4], d_ff_12_q[3], d_ff_11_q[2], d_ff_9_q} & d_ff_1_q;  // AND_Gate and_9, 7 bits wide
  Multiplexer #(.select(3), .width(23), .enable("false")) multiplexer_1 (
    .in1(register_1_q), .in2(register_2_q), .in3(register_3_q), .in4(register_4_q), .in5(register_5_q),
    .in6(register_6_q), .in7(register_7_q), .out(temps_sortie), .sel(C_detect_tour_1_t_3bits));  // open: in0
  C_detect_tour C_detect_tour_1 (.T_7bits(d_ff_1_q), .T_3bits(C_detect_tour_1_t_3bits));
  C_leds C_leds_1 (.temps_actif(d_ff_1_q), .Lect_tours(not_1_out), .Clignotement(Temps[1]), .Output_bus_1(Leds));
  or or_12 (Aucun_temps, and_9_out[0], and_9_out[1], and_9_out[2], and_9_out[3], and_9_out[4], and_9_out[5], and_9_out[6], or_10_out);
endmodule

module C_detect_tour (
  input  [6:0] T_7bits,
  output [2:0] T_3bits
);

  or or_1 (T_3bits[2], T_7bits[3], T_7bits[4], T_7bits[5], T_7bits[6]);
  or or_2 (T_3bits[1], T_7bits[1], T_7bits[2], T_7bits[5], T_7bits[6]);
  or or_3 (T_3bits[0], T_7bits[0], T_7bits[2], T_7bits[4], T_7bits[6]);
endmodule

module C_affiche (
  input  Lect_temps,
  input  [22:0] Temps,
  input  Aucun_temps,
  output [7:0] Seg_0,
  output [7:0] Seg_1,
  output [7:0] Seg_2,
  output [7:0] Seg_3,
  output [7:0] Seg_4,
  output [7:0] Seg_5
);

  wire and_1_out, comparator_1_lt, not_1_out, not_2_out;
  wire [3:0] Conv_temps_1_dixiemes, conv_unit_dizaines_1_dizaines, conv_unit_dizaines_1_unites,
       conv_unit_dizaines_2_dizaines, conv_unit_dizaines_2_unites, conv_unit_dizaines_3_dizaines,
       conv_unit_dizaines_3_unites, multiplexer_1_out, multiplexer_2_out, multiplexer_3_out,
       multiplexer_4_out, multiplexer_5_out;
  wire [4:0] Conv_temps_1_heures;
  wire [5:0] Conv_temps_1_minutes, Conv_temps_1_secondes;
  wire [7:0] Chiffre_7seg_1_sortie, Chiffre_7seg_2_sortie, Chiffre_7seg_3_sortie, Chiffre_7seg_4_sortie,
       Chiffre_7seg_5_sortie, Chiffre_7seg_6_sortie, multiplexer_6_out;

  and and_1 (and_1_out, Lect_temps, Aucun_temps);
  Conv_temps Conv_temps_1 (
    .Temps(Temps), .Heures(Conv_temps_1_heures), .Minutes(Conv_temps_1_minutes),
    .Secondes(Conv_temps_1_secondes), .dixiemes(Conv_temps_1_dixiemes));  // open: Jours
  Comparator #(.width(5), .mode("unsigned")) comparator_1 (
    .a({5{1'b0}}), .b(Conv_temps_1_heures), .lt(comparator_1_lt));  // open: gt, eq
  conv_unit_dizaines conv_unit_dizaines_1 (
    .entree({1'b0, Conv_temps_1_heures}), .Dizaines(conv_unit_dizaines_1_dizaines),
    .Unites(conv_unit_dizaines_1_unites));
  conv_unit_dizaines conv_unit_dizaines_2 (
    .entree(Conv_temps_1_minutes), .Dizaines(conv_unit_dizaines_2_dizaines),
    .Unites(conv_unit_dizaines_2_unites));
  conv_unit_dizaines conv_unit_dizaines_3 (
    .entree(Conv_temps_1_secondes), .Dizaines(conv_unit_dizaines_3_dizaines),
    .Unites(conv_unit_dizaines_3_unites));
  Multiplexer #(.width(4), .enable("false")) multiplexer_1 (
    .in0(conv_unit_dizaines_2_dizaines), .in1(conv_unit_dizaines_1_unites), .out(multiplexer_1_out),
    .sel(comparator_1_lt));
  Multiplexer #(.width(4), .enable("false")) multiplexer_2 (
    .in0(conv_unit_dizaines_2_unites), .in1(conv_unit_dizaines_2_dizaines), .out(multiplexer_2_out),
    .sel(comparator_1_lt));
  not not_1 (not_1_out, comparator_1_lt);
  Multiplexer #(.width(4), .enable("false")) multiplexer_3 (
    .in0(conv_unit_dizaines_3_dizaines), .in1(conv_unit_dizaines_2_unites), .out(multiplexer_3_out),
    .sel(comparator_1_lt));
  Multiplexer #(.width(4), .enable("false")) multiplexer_4 (
    .in0(conv_unit_dizaines_3_unites), .in1(conv_unit_dizaines_3_dizaines), .out(multiplexer_4_out),
    .sel(comparator_1_lt));
  not not_2 (not_2_out, comparator_1_lt);
  Multiplexer #(.width(4), .enable("false")) multiplexer_5 (
    .in0(Conv_temps_1_dixiemes), .in1(conv_unit_dizaines_3_unites), .out(multiplexer_5_out),
    .sel(comparator_1_lt));
  Chiffre_7seg Chiffre_7seg_1 (.Point(1'b0), .Sortie(Chiffre_7seg_1_sortie), .Entree(conv_unit_dizaines_1_dizaines));
  Multiplexer #(.width(8), .enable("false")) multiplexer_6 (
    .in0({8{1'b0}}), .in1(Chiffre_7seg_1_sortie), .out(multiplexer_6_out), .sel(comparator_1_lt));
  Chiffre_7seg Chiffre_7seg_2 (.Point(comparator_1_lt), .Sortie(Chiffre_7seg_2_sortie), .Entree(multiplexer_1_out));
  Chiffre_7seg Chiffre_7seg_3 (.Point(not_1_out), .Sortie(Chiffre_7seg_3_sortie), .Entree(multiplexer_2_out));
  Chiffre_7seg Chiffre_7seg_4 (.Point(comparator_1_lt), .Sortie(Chiffre_7seg_4_sortie), .Entree(multiplexer_3_out));
  Chiffre_7seg Chiffre_7seg_5 (.Point(not_2_out), .Sortie(Chiffre_7seg_5_sortie), .Entree(multiplexer_4_out));
  Chiffre_7seg Chiffre_7seg_6 (.Point(1'b0), .Sortie(Chiffre_7seg_6_sortie), .Entree(multiplexer_5_out));
  Multiplexer #(.width(8), .enable("false")) multiplexer_7 (
    .in0(multiplexer_6_out), .in1(8'h40), .out(Seg_0), .sel(Lect_temps));
  Multiplexer #(.width(8), .enable("false")) multiplexer_8 (
    .in0(Chiffre_7seg_2_sortie), .in1(8'h8), .out(Seg_1), .sel(and_1_out));
  Multiplexer #(.width(8), .enable("false")) multiplexer_9 (
    .in0(Chiffre_7seg_3_sortie), .in1(8'h8), .out(Seg_2), .sel(and_1_out));
  Multiplexer #(.width(8), .enable("false")) multiplexer_10 (
    .in0(Chiffre_7seg_4_sortie), .in1(8'h8), .out(Seg_3), .sel(and_1_out));
  Multiplexer #(.width(8), .enable("false")) multiplexer_11 (
    .in0(Chiffre_7seg_5_sortie), .in1(8'h8), .out(Seg_4), .sel(and_1_out));
  Multiplexer #(.width(8), .enable("false")) multiplexer_12 (
    .in0(Chiffre_7seg_6_sortie), .in1(8'h8), .out(Seg_5), .sel(and_1_out));
endmodule

module C_leds (
  input  [6:0] temps_actif,
  input  Lect_tours,
  input  Clignotement,
  output [6:0] Output_bus_1
);

  wire and_1_out, and_2_out, and_3_out, and_4_out, and_5_out, and_6_out, and_7_out;
  wire [5:0] or_1_out;

  and and_1 (and_1_out, ~Lect_tours, Clignotement);  // AND_Gate
  or or_1 (or_1_out[0], temps_actif[0], and_2_out);
  and and_2 (and_2_out, Lect_tours, or_1_out[1]);
  or or_2 (or_1_out[1], temps_actif[1], and_3_out);
  and and_3 (and_3_out, Lect_tours, or_1_out[2]);
  or or_3 (or_1_out[2], temps_actif[2], and_4_out);
  and and_4 (and_4_out, Lect_tours, or_1_out[3]);
  or or_4 (or_1_out[3], temps_actif[3], and_5_out);
  and and_5 (and_5_out, Lect_tours, or_1_out[4]);
  or or_5 (or_1_out[4], temps_actif[4], and_6_out);
  and and_6 (and_6_out, Lect_tours, or_1_out[5]);
  or or_6 (or_1_out[5], temps_actif[5], and_7_out);
  and and_7 (and_7_out, Lect_tours, temps_actif[6]);
  Multiplexer #(.width(7), .enable("false")) multiplexer_1 (
    .in0({temps_actif[6], or_1_out}), .in1({7{1'b0}}), .out(Output_bus_1), .sel(and_1_out));
endmodule

module Timer (
  input  [3:0] Boutons,
  input  [2:0] Etat,
  input  [22:0] Temps,
  input  E,
  output [7:0] Seg0,
  output [7:0] Seg1,
  output [7:0] Seg2,
  output [7:0] Seg3,
  output [7:0] Seg4,
  output [7:0] Seg5,
  output Sonne,
  output sous_systeme
);

  wire Actif_q, and_1_out, and_2_out, and_3_out, and_5_out, and_6_out, and_9_out, and_10_out, and_11_out,
       and_13_out, comparator_1_eq, comparator_2_eq, comparator_2_lt, d_ff_1_q, d_ff_2_q, d_ff_3_q, d_ff_4_q,
       d_ff_5_q, d_ff_6_q, d_ff_7_q, not_1_out, or_1_out, or_2_out, or_3_out, or_4_out, or_7_out, or_8_out,
       subtractor_1_bout, t_ff_1_q;
  wire [1:0] or_5_out;
  wire [2:0] regle;
  wire [22:0] adder_1_out, adder_2_out, Duree_q, Fin_q, multiplexer_1_out, multiplexer_2_out,
       multiplexer_3_out, subtractor_1_out, subtractor_2_out, temps_prevu_q;

  Comparator #(.width(3), .mode("unsigned")) comparator_1 (.a(Etat), .b(3'b011), .eq(comparator_1_eq));  // open: gt, lt
  T_Flip_Flop t_ff_1 (.T(1'b1), .clk(and_1_out), .Q(t_ff_1_q), .reset(or_3_out));  // open: Qn, preset
  and and_1 (and_1_out, Boutons[1], ~Actif_q, comparator_1_eq);  // AND_Gate
  and and_2 (and_2_out, Boutons[2], ~t_ff_1_q, comparator_1_eq);  // AND_Gate
  and and_3 (and_3_out, t_ff_1_q, Boutons[1], comparator_1_eq, ~and_1_out);  // AND_Gate
  D_Flip_Flop d_ff_1 (.D(1'b1), .clk(Sonne), .Q(d_ff_1_q), .reset(or_1_out));  // open: Qn, preset
  or or_1 (or_1_out, E, d_ff_5_q);
  T_Flip_Flop Actif (.T(comparator_1_eq), .clk(and_2_out), .Q(Actif_q), .reset(or_3_out));  // open: Qn, preset
  D_Flip_Flop d_ff_2 (.D(d_ff_1_q), .clk(Temps[0]), .Q(d_ff_2_q), .reset(or_2_out));  // open: Qn, preset
  or or_2 (or_2_out, E, d_ff_5_q);
  and and_4 (regle[0], t_ff_1_q, ~d_ff_3_q);  // AND_Gate
  D_Flip_Flop d_ff_3 (.D(t_ff_1_q), .clk(and_5_out), .Q(d_ff_3_q), .reset(or_4_out));  // open: Qn, preset
  and and_5 (and_5_out, Boutons[2], comparator_1_eq);
  Register #(.width(23)) Duree (.D(temps_prevu_q), .clk(and_3_out), .Q(Duree_q), .clr(or_3_out));  // open: en
  and and_6 (and_6_out, Boutons[2], comparator_1_eq, Actif_q);
  D_Flip_Flop d_ff_4 (.D(Actif_q), .clk(Temps[0]), .Q(d_ff_4_q), .reset(or_3_out));  // open: Qn, preset
  D_Flip_Flop d_ff_5 (.D(d_ff_2_q), .clk(Temps[0]), .Q(d_ff_5_q), .reset(E));  // open: Qn, preset
  and and_7 (regle[1], d_ff_3_q, ~d_ff_6_q);  // AND_Gate
  D_Flip_Flop d_ff_6 (.D(d_ff_3_q), .clk(and_5_out), .Q(d_ff_6_q), .reset(or_4_out));  // open: Qn, preset
  Register #(.width(23)) Debut (.D(Temps), .clk(and_6_out), .clr(or_3_out));  // open: en, Q
  and and_8 (regle[2], d_ff_6_q, ~d_ff_7_q);  // AND_Gate
  D_Flip_Flop d_ff_7 (.D(d_ff_6_q), .clk(and_5_out), .Q(d_ff_7_q), .reset(or_4_out));  // open: Qn, preset
  Adder #(.width(23)) adder_1 (.a(Duree_q), .b(Temps), .out(adder_1_out));  // open: cin, cout
  or or_3 (or_3_out, E, d_ff_5_q);
  or or_4 (or_4_out, d_ff_7_q, or_3_out);
  Subtractor #(.width(23)) subtractor_1 (
    .a(adder_1_out), .b(23'h5c4900), .out(subtractor_1_out), .bout(subtractor_1_bout));  // open: bin
  Register #(.width(23)) Fin (.D(multiplexer_1_out), .clk(and_6_out), .Q(Fin_q), .clr(or_3_out));  // open: en
  Multiplexer #(.width(23), .enable("false")) multiplexer_1 (
    .in0(subtractor_1_out), .in1(adder_1_out), .out(multiplexer_1_out), .sel(subtractor_1_bout));
  and and_9 (and_9_out, regle[0], Boutons[0]);
  and and_10 (and_10_out, regle[1], Boutons[0]);
  and and_11 (and_11_out, regle[2], Boutons[0]);
  Comparator #(.width(23), .mode("unsigned")) comparator_2 (
    .a(Fin_q), .b(Temps), .eq(comparator_2_eq), .lt(comparator_2_lt));  // open: gt
  or or_5 (or_5_out[0], and_9_out, and_11_out);
  or or_6 (or_5_out[1], and_10_out, and_11_out);
  or or_7 (or_7_out, comparator_2_eq, comparator_2_lt);
  and and_12 (Sonne, or_7_out, d_ff_4_q);
  Multiplexer #(.select(2), .width(23), .enable("false")) multiplexer_2 (
    .in0({23{1'b0}}), .in1(23'h8ca0), .in2(23'h1770), .in3(23'h258), .out(multiplexer_2_out), .sel(or_5_out));
  Subtractor #(.width(23)) subtractor_2 (.a(Fin_q), .b(Temps), .out(subtractor_2_out));  // open: bin, bout
  Adder #(.width(23)) adder_2 (.a(multiplexer_2_out), .b(temps_prevu_q), .out(adder_2_out));  // open: cin, cout
  not not_1 (not_1_out, Boutons[0]);
  Multiplexer #(.width(23), .enable("false")) multiplexer_3 (
    .in0(Duree_q), .in1(subtractor_2_out), .out(multiplexer_3_out), .sel(Actif_q));
  Register #(.width(23)) temps_prevu (.D(adder_2_out), .clk(not_1_out), .Q(temps_prevu_q), .clr(or_8_out));  // open: en
  or or_8 (or_8_out, and_13_out, or_3_out);
  and and_13 (and_13_out, t_ff_1_q, and_1_out);
  and and_14 (sous_systeme, t_ff_1_q, comparator_1_eq);
  T_affiche T_affiche_1 (
    .regle(regle), .sous_systeme(t_ff_1_q), .temps_set(adder_2_out), .temps_restant(multiplexer_3_out),
    .clignotement(Temps[2]), .Output_bus_1(Seg0), .Output_bus_2(Seg1), .Output_bus_3(Seg2),
    .Output_bus_4(Seg3), .Output_bus_5(Seg4), .Output_bus_6(Seg5));
endmodule

module T_affiche (
  input  [2:0] regle,
  input  sous_systeme,
  input  [22:0] temps_set,
  input  [22:0] temps_restant,
  input  clignotement,
  output [7:0] Output_bus_1,
  output [7:0] Output_bus_2,
  output [7:0] Output_bus_3,
  output [7:0] Output_bus_4,
  output [7:0] Output_bus_5,
  output [7:0] Output_bus_6
);

  wire nand_1_out, nand_2_out, nand_3_out, not_1_out;
  wire [3:0] conv_unit_dizaines_1_dizaines, conv_unit_dizaines_1_unites, conv_unit_dizaines_2_dizaines,
       conv_unit_dizaines_2_unites, conv_unit_dizaines_3_dizaines, conv_unit_dizaines_3_unites;
  wire [4:0] Conv_temps_1_heures;
  wire [5:0] Conv_temps_1_minutes, Conv_temps_1_secondes;
  wire [7:0] Chiffre_7seg_1_sortie, Chiffre_7seg_2_sortie, Chiffre_7seg_3_sortie, Chiffre_7seg_4_sortie,
       Chiffre_7seg_5_sortie, Chiffre_7seg_6_sortie;
  wire [22:0] multiplexer_1_out;

  Multiplexer #(.width(23), .enable("false")) multiplexer_1 (
    .in0(temps_restant), .in1(temps_set), .out(multiplexer_1_out), .sel(sous_systeme));
  Conv_temps Conv_temps_1 (
    .Temps(multiplexer_1_out), .Heures(Conv_temps_1_heures), .Minutes(Conv_temps_1_minutes),
    .Secondes(Conv_temps_1_secondes));  // open: Jours, dixiemes
  conv_unit_dizaines conv_unit_dizaines_1 (
    .entree({1'b0, Conv_temps_1_heures}), .Dizaines(conv_unit_dizaines_1_dizaines),
    .Unites(conv_unit_dizaines_1_unites));
  conv_unit_dizaines conv_unit_dizaines_2 (
    .entree(Conv_temps_1_minutes), .Dizaines(conv_unit_dizaines_2_dizaines),
    .Unites(conv_unit_dizaines_2_unites));
  conv_unit_dizaines conv_unit_dizaines_3 (
    .entree(Conv_temps_1_secondes), .Dizaines(conv_unit_dizaines_3_dizaines),
    .Unites(conv_unit_dizaines_3_unites));
  not not_1 (not_1_out, sous_systeme);
  Chiffre_7seg Chiffre_7seg_1 (.Point(1'b0), .Sortie(Chiffre_7seg_1_sortie), .Entree(conv_unit_dizaines_1_dizaines));
  Chiffre_7seg Chiffre_7seg_2 (.Point(1'b1), .Sortie(Chiffre_7seg_2_sortie), .Entree(conv_unit_dizaines_1_unites));
  Chiffre_7seg Chiffre_7seg_3 (.Point(1'b0), .Sortie(Chiffre_7seg_3_sortie), .Entree(conv_unit_dizaines_2_dizaines));
  Chiffre_7seg Chiffre_7seg_4 (.Point(1'b1), .Sortie(Chiffre_7seg_4_sortie), .Entree(conv_unit_dizaines_2_unites));
  Chiffre_7seg Chiffre_7seg_5 (.Point(1'b0), .Sortie(Chiffre_7seg_5_sortie), .Entree(conv_unit_dizaines_3_dizaines));
  Chiffre_7seg Chiffre_7seg_6 (.Point(1'b0), .Sortie(Chiffre_7seg_6_sortie), .Entree(conv_unit_dizaines_3_unites));
  nand nand_1 (nand_1_out, sous_systeme, regle[0], clignotement);
  nand nand_2 (nand_2_out, sous_systeme, regle[1], clignotement);
  nand nand_3 (nand_3_out, sous_systeme, regle[2], clignotement);
  Multiplexer #(.width(8), .enable("false")) multiplexer_2 (
    .in0({8{1'b0}}), .in1(Chiffre_7seg_1_sortie), .out(Output_bus_1), .sel(nand_1_out));
  Multiplexer #(.width(8), .enable("false")) multiplexer_3 (
    .in0({8{1'b0}}), .in1(Chiffre_7seg_2_sortie), .out(Output_bus_2), .sel(nand_1_out));
  Multiplexer #(.width(8), .enable("false")) multiplexer_4 (
    .in0({8{1'b0}}), .in1(Chiffre_7seg_3_sortie), .out(Output_bus_3), .sel(nand_2_out));
  Multiplexer #(.width(8), .enable("false")) multiplexer_5 (
    .in0({8{1'b0}}), .in1(Chiffre_7seg_4_sortie), .out(Output_bus_4), .sel(nand_3_out));
  Multiplexer #(.width(8), .enable("false")) multiplexer_6 (
    .in0({8{1'b0}}), .in1(Chiffre_7seg_5_sortie), .out(Output_bus_5), .sel(not_1_out));
  Multiplexer #(.width(8), .enable("false")) multiplexer_7 (
    .in0({8{1'b0}}), .in1(Chiffre_7seg_6_sortie), .out(Output_bus_6), .sel(not_1_out));
endmodule

module Sonne (
  input  [2:0] Etat,
  input  [3:0] Boutons,
  input  [22:0] Temps,
  input  E,
  output Buzzer,
  output [7:0] Seg0,
  output [7:0] Seg1,
  output [7:0] Seg2,
  output [7:0] Seg3,
  output [7:0] Seg4,
  output [7:0] Seg5,
  output [6:0] Leds
);

  wire and_1_out, and_3_out, comparator_1_eq, comparator_2_eq, comparator_3_eq, or_1_out, Snooze_q,
       subtractor_1_bout;
  wire [22:0] adder_1_out, Fin_snooze_q, multiplexer_1_out, subtractor_1_out;

  Comparator #(.width(3), .mode("unsigned")) comparator_1 (.a(3'b100), .b(Etat), .eq(comparator_1_eq));  // open: gt, lt
  Comparator #(.width(4), .mode("unsigned")) comparator_2 (
    .a(4'b0100), .b(Boutons), .eq(comparator_2_eq));  // open: gt, lt
  and and_1 (and_1_out, comparator_1_eq, comparator_2_eq);
  D_Flip_Flop Snooze (.D(1'b1), .clk(and_1_out), .Q(Snooze_q), .reset(or_1_out));  // open: Qn, preset
  or or_1 (or_1_out, ~comparator_1_eq, comparator_3_eq, E);  // OR_Gate
  Adder #(.width(23)) adder_1 (.a(23'hbb8), .b(Temps), .out(adder_1_out));  // open: cin, cout
  Subtractor #(.width(23)) subtractor_1 (
    .a(adder_1_out), .b(23'h5c4900), .out(subtractor_1_out), .bout(subtractor_1_bout));  // open: bin
  Register #(.width(23)) Fin_snooze (.D(multiplexer_1_out), .clk(Snooze_q), .Q(Fin_snooze_q));  // open: en, clr
  Multiplexer #(.width(23), .enable("false")) multiplexer_1 (
    .in0(subtractor_1_out), .in1(adder_1_out), .out(multiplexer_1_out), .sel(subtractor_1_bout));
  and and_2 (Buzzer, comparator_1_eq, ~Snooze_q);  // AND_Gate
  and and_3 (and_3_out, Temps[1], Buzzer);
  Comparator #(.width(23), .mode("unsigned")) comparator_3 (
    .a(Fin_snooze_q), .b(Temps), .eq(comparator_3_eq));  // open: gt, lt
  Multiplexer #(.width(7), .enable("false")) multiplexer_2 (
    .in0({7{1'b0}}), .in1({7{1'b1}}), .out(Leds), .sel(and_3_out));
  Multiplexer #(.width(8), .enable("false")) multiplexer_3 (.in0(8'h88), .in1(8'h6e), .out(Seg0), .sel(Buzzer));
  Multiplexer #(.width(8), .enable("false")) multiplexer_4 (.in0(8'haf), .in1(8'he8), .out(Seg1), .sel(Buzzer));
  Multiplexer #(.width(8), .enable("false")) multiplexer_5 (.in0(8'h8f), .in1(8'ha8), .out(Seg2), .sel(Buzzer));
  Multiplexer #(.width(8), .enable("false")) multiplexer_6 (.in0(8'h8f), .in1(8'ha8), .out(Seg3), .sel(Buzzer));
  Multiplexer #(.width(8), .enable("false")) multiplexer_7 (.in0(8'hce), .in1(8'hce), .out(Seg4), .sel(Buzzer));
  Multiplexer #(.width(8), .enable("false")) multiplexer_8 (.in0(8'hc4), .in1({8{1'b0}}), .out(Seg5), .sel(Buzzer));
endmodule

module Conv_temps (
  input  [22:0] Temps,
  output [2:0] Jours,
  output [4:0] Heures,
  output [5:0] Minutes,
  output [5:0] Secondes,
  output [3:0] dixiemes
);

  wire [22:0] diviseur_1_reste, diviseur_2_reste, diviseur_3_reste;
  wire [22:3] diviseur_1_quotient;
  wire [22:4] diviseur_4_reste;
  wire [22:5] diviseur_2_quotient;
  wire [22:6] diviseur_3_quotient, diviseur_4_quotient;

  diviseur diviseur_1 (
    .dividende(Temps), .diviseur(23'hd2f00), .quotient({diviseur_1_quotient, Jours}), .reste(diviseur_1_reste));
  diviseur diviseur_2 (
    .dividende(diviseur_1_reste), .diviseur(23'h8ca0), .quotient({diviseur_2_quotient, Heures}),
    .reste(diviseur_2_reste));
  diviseur diviseur_3 (
    .dividende(diviseur_2_reste), .diviseur(23'h258), .quotient({diviseur_3_quotient, Minutes}),
    .reste(diviseur_3_reste));
  diviseur diviseur_4 (
    .dividende(diviseur_3_reste), .diviseur(23'ha), .quotient({diviseur_4_quotient, Secondes}),
    .reste({diviseur_4_reste, dixiemes}));
endmodule

module conv_unit_dizaines (
  input  [5:0] entree,
  output [3:0] Dizaines,
  output [3:0] Unites
);

  wire [22:4] diviseur_1_quotient, diviseur_1_reste;

  diviseur diviseur_1 (
    .dividende({{17{1'b0}}, entree}), .diviseur(23'ha), .quotient({diviseur_1_quotient, Dizaines}),
    .reste({diviseur_1_reste, Unites}));
endmodule

module diviseur (
  input  [22:0] dividende,
  input  [22:0] diviseur,
  output [22:0] quotient,
  output [22:0] reste
);

  wire subtractor_1_bout, subtractor_2_bout, subtractor_3_bout, subtractor_4_bout, subtractor_5_bout,
       subtractor_6_bout, subtractor_7_bout, subtractor_8_bout, subtractor_9_bout, subtractor_10_bout,
       subtractor_11_bout, subtractor_12_bout, subtractor_13_bout, subtractor_14_bout, subtractor_15_bout,
       subtractor_16_bout, subtractor_17_bout, subtractor_18_bout, subtractor_19_bout, subtractor_20_bout,
       subtractor_21_bout, subtractor_22_bout, subtractor_23_bout;
  wire [22:0] multiplexer_2_out, multiplexer_4_out, multiplexer_6_out, multiplexer_8_out, multiplexer_10_out,
       multiplexer_12_out, multiplexer_14_out, multiplexer_16_out, multiplexer_18_out, multiplexer_20_out,
       multiplexer_22_out, subtractor_1_out, subtractor_2_out, subtractor_3_out, subtractor_4_out,
       subtractor_5_out, subtractor_6_out, subtractor_7_out, subtractor_8_out, subtractor_9_out,
       subtractor_10_out, subtractor_11_out, subtractor_12_out, subtractor_13_out, subtractor_14_out,
       subtractor_15_out, subtractor_16_out, subtractor_17_out, subtractor_18_out, subtractor_19_out,
       subtractor_20_out, subtractor_21_out, subtractor_22_out, subtractor_23_out;
  wire [22:1] multiplexer_1_out, multiplexer_3_out, multiplexer_5_out, multiplexer_7_out, multiplexer_9_out,
       multiplexer_11_out, multiplexer_13_out, multiplexer_15_out, multiplexer_17_out, multiplexer_19_out,
       multiplexer_21_out;
  wire [22:22] multiplexer_1_out_2, multiplexer_3_out_2, multiplexer_5_out_2, multiplexer_7_out_2,
       multiplexer_9_out_2, multiplexer_11_out_2, multiplexer_13_out_2, multiplexer_15_out_2,
       multiplexer_17_out_2, multiplexer_19_out_2, multiplexer_21_out_2;

  Subtractor #(.width(23)) subtractor_1 (
    .a({{22{1'b0}}, dividende[22]}), .b(diviseur), .out(subtractor_1_out), .bout(subtractor_1_bout));  // open: bin
  not not_1 (quotient[22], subtractor_1_bout);
  Subtractor #(.width(23)) subtractor_2 (
    .a({multiplexer_1_out, dividende[21]}), .b(diviseur), .out(subtractor_2_out), .bout(subtractor_2_bout));  // open: bin
  not not_2 (quotient[21], subtractor_2_bout);
  Subtractor #(.width(23)) subtractor_3 (
    .a({multiplexer_2_out[21:0], dividende[20]}), .b(diviseur), .out(subtractor_3_out),
    .bout(subtractor_3_bout));  // open: bin
  not not_3 (quotient[20], subtractor_3_bout);
  Subtractor #(.width(23)) subtractor_4 (
    .a({multiplexer_3_out, dividende[19]}), .b(diviseur), .out(subtractor_4_out), .bout(subtractor_4_bout));  // open: bin
  not not_4 (quotient[19], subtractor_4_bout);
  Subtractor #(.width(23)) subtractor_5 (
    .a({multiplexer_4_out[21:0], dividende[18]}), .b(diviseur), .out(subtractor_5_out),
    .bout(subtractor_5_bout));  // open: bin
  not not_5 (quotient[18], subtractor_5_bout);
  Subtractor #(.width(23)) subtractor_6 (
    .a({multiplexer_5_out, dividende[17]}), .b(diviseur), .out(subtractor_6_out), .bout(subtractor_6_bout));  // open: bin
  not not_6 (quotient[17], subtractor_6_bout);
  Subtractor #(.width(23)) subtractor_7 (
    .a({multiplexer_6_out[21:0], dividende[16]}), .b(diviseur), .out(subtractor_7_out),
    .bout(subtractor_7_bout));  // open: bin
  not not_7 (quotient[16], subtractor_7_bout);
  Subtractor #(.width(23)) subtractor_8 (
    .a({multiplexer_7_out, dividende[15]}), .b(diviseur), .out(subtractor_8_out), .bout(subtractor_8_bout));  // open: bin
  not not_8 (quotient[15], subtractor_8_bout);
  Subtractor #(.width(23)) subtractor_9 (
    .a({multiplexer_8_out[21:0], dividende[14]}), .b(diviseur), .out(subtractor_9_out),
    .bout(subtractor_9_bout));  // open: bin
  not not_9 (quotient[14], subtractor_9_bout);
  Subtractor #(.width(23)) subtractor_10 (
    .a({multiplexer_9_out, dividende[13]}), .b(diviseur), .out(subtractor_10_out), .bout(subtractor_10_bout));  // open: bin
  not not_10 (quotient[13], subtractor_10_bout);
  Subtractor #(.width(23)) subtractor_11 (
    .a({multiplexer_10_out[21:0], dividende[12]}), .b(diviseur), .out(subtractor_11_out),
    .bout(subtractor_11_bout));  // open: bin
  not not_11 (quotient[12], subtractor_11_bout);
  Subtractor #(.width(23)) subtractor_12 (
    .a({multiplexer_11_out, dividende[11]}), .b(diviseur), .out(subtractor_12_out), .bout(subtractor_12_bout));  // open: bin
  not not_12 (quotient[11], subtractor_12_bout);
  Subtractor #(.width(23)) subtractor_13 (
    .a({multiplexer_12_out[21:0], dividende[10]}), .b(diviseur), .out(subtractor_13_out),
    .bout(subtractor_13_bout));  // open: bin
  not not_13 (quotient[10], subtractor_13_bout);
  Subtractor #(.width(23)) subtractor_14 (
    .a({multiplexer_13_out, dividende[9]}), .b(diviseur), .out(subtractor_14_out), .bout(subtractor_14_bout));  // open: bin
  not not_14 (quotient[9], subtractor_14_bout);
  Subtractor #(.width(23)) subtractor_15 (
    .a({multiplexer_14_out[21:0], dividende[8]}), .b(diviseur), .out(subtractor_15_out),
    .bout(subtractor_15_bout));  // open: bin
  not not_15 (quotient[8], subtractor_15_bout);
  Subtractor #(.width(23)) subtractor_16 (
    .a({multiplexer_15_out, dividende[7]}), .b(diviseur), .out(subtractor_16_out), .bout(subtractor_16_bout));  // open: bin
  not not_16 (quotient[7], subtractor_16_bout);
  Subtractor #(.width(23)) subtractor_17 (
    .a({multiplexer_16_out[21:0], dividende[6]}), .b(diviseur), .out(subtractor_17_out),
    .bout(subtractor_17_bout));  // open: bin
  not not_17 (quotient[6], subtractor_17_bout);
  Subtractor #(.width(23)) subtractor_18 (
    .a({multiplexer_17_out, dividende[5]}), .b(diviseur), .out(subtractor_18_out), .bout(subtractor_18_bout));  // open: bin
  not not_18 (quotient[5], subtractor_18_bout);
  Subtractor #(.width(23)) subtractor_19 (
    .a({multiplexer_18_out[21:0], dividende[4]}), .b(diviseur), .out(subtractor_19_out),
    .bout(subtractor_19_bout));  // open: bin
  not not_19 (quotient[4], subtractor_19_bout);
  Subtractor #(.width(23)) subtractor_20 (
    .a({multiplexer_19_out, dividende[3]}), .b(diviseur), .out(subtractor_20_out), .bout(subtractor_20_bout));  // open: bin
  not not_20 (quotient[3], subtractor_20_bout);
  Subtractor #(.width(23)) subtractor_21 (
    .a({multiplexer_20_out[21:0], dividende[2]}), .b(diviseur), .out(subtractor_21_out),
    .bout(subtractor_21_bout));  // open: bin
  not not_21 (quotient[2], subtractor_21_bout);
  Subtractor #(.width(23)) subtractor_22 (
    .a({multiplexer_21_out, dividende[1]}), .b(diviseur), .out(subtractor_22_out), .bout(subtractor_22_bout));  // open: bin
  not not_22 (quotient[1], subtractor_22_bout);
  Subtractor #(.width(23)) subtractor_23 (
    .a({multiplexer_22_out[21:0], dividende[0]}), .b(diviseur), .out(subtractor_23_out),
    .bout(subtractor_23_bout));  // open: bin
  not not_23 (quotient[0], subtractor_23_bout);
  Multiplexer #(.width(23), .enable("false")) multiplexer_1 (
    .in0({{22{1'b0}}, dividende[22]}), .in1(subtractor_1_out),
    .out({multiplexer_1_out_2[22], multiplexer_1_out}), .sel(quotient[22]));
  Multiplexer #(.width(23), .enable("false")) multiplexer_2 (
    .in0({multiplexer_1_out, dividende[21]}), .in1(subtractor_2_out), .out(multiplexer_2_out),
    .sel(quotient[21]));
  Multiplexer #(.width(23), .enable("false")) multiplexer_3 (
    .in0({multiplexer_2_out[21:0], dividende[20]}), .in1(subtractor_3_out),
    .out({multiplexer_3_out_2[22], multiplexer_3_out}), .sel(quotient[20]));
  Multiplexer #(.width(23), .enable("false")) multiplexer_4 (
    .in0({multiplexer_3_out, dividende[19]}), .in1(subtractor_4_out), .out(multiplexer_4_out),
    .sel(quotient[19]));
  Multiplexer #(.width(23), .enable("false")) multiplexer_5 (
    .in0({multiplexer_4_out[21:0], dividende[18]}), .in1(subtractor_5_out),
    .out({multiplexer_5_out_2[22], multiplexer_5_out}), .sel(quotient[18]));
  Multiplexer #(.width(23), .enable("false")) multiplexer_6 (
    .in0({multiplexer_5_out, dividende[17]}), .in1(subtractor_6_out), .out(multiplexer_6_out),
    .sel(quotient[17]));
  Multiplexer #(.width(23), .enable("false")) multiplexer_7 (
    .in0({multiplexer_6_out[21:0], dividende[16]}), .in1(subtractor_7_out),
    .out({multiplexer_7_out_2[22], multiplexer_7_out}), .sel(quotient[16]));
  Multiplexer #(.width(23), .enable("false")) multiplexer_8 (
    .in0({multiplexer_7_out, dividende[15]}), .in1(subtractor_8_out), .out(multiplexer_8_out),
    .sel(quotient[15]));
  Multiplexer #(.width(23), .enable("false")) multiplexer_9 (
    .in0({multiplexer_8_out[21:0], dividende[14]}), .in1(subtractor_9_out),
    .out({multiplexer_9_out_2[22], multiplexer_9_out}), .sel(quotient[14]));
  Multiplexer #(.width(23), .enable("false")) multiplexer_10 (
    .in0({multiplexer_9_out, dividende[13]}), .in1(subtractor_10_out), .out(multiplexer_10_out),
    .sel(quotient[13]));
  Multiplexer #(.width(23), .enable("false")) multiplexer_11 (
    .in0({multiplexer_10_out[21:0], dividende[12]}), .in1(subtractor_11_out),
    .out({multiplexer_11_out_2[22], multiplexer_11_out}), .sel(quotient[12]));
  Multiplexer #(.width(23), .enable("false")) multiplexer_12 (
    .in0({multiplexer_11_out, dividende[11]}), .in1(subtractor_12_out), .out(multiplexer_12_out),
    .sel(quotient[11]));
  Multiplexer #(.width(23), .enable("false")) multiplexer_13 (
    .in0({multiplexer_12_out[21:0], dividende[10]}), .in1(subtractor_13_out),
    .out({multiplexer_13_out_2[22], multiplexer_13_out}), .sel(quotient[10]));
  Multiplexer #(.width(23), .enable("false")) multiplexer_14 (
    .in0({multiplexer_13_out, dividende[9]}), .in1(subtractor_14_out), .out(multiplexer_14_out),
    .sel(quotient[9]));
  Multiplexer #(.width(23), .enable("false")) multiplexer_15 (
    .in0({multiplexer_14_out[21:0], dividende[8]}), .in1(subtractor_15_out),
    .out({multiplexer_15_out_2[22], multiplexer_15_out}), .sel(quotient[8]));
  Multiplexer #(.width(23), .enable("false")) multiplexer_16 (
    .in0({multiplexer_15_out, dividende[7]}), .in1(subtractor_16_out), .out(multiplexer_16_out),
    .sel(quotient[7]));
  Multiplexer #(.width(23), .enable("false")) multiplexer_17 (
    .in0({multiplexer_16_out[21:0], dividende[6]}), .in1(subtractor_17_out),
    .out({multiplexer_17_out_2[22], multiplexer_17_out}), .sel(quotient[6]));
  Multiplexer #(.width(23), .enable("false")) multiplexer_18 (
    .in0({multiplexer_17_out, dividende[5]}), .in1(subtractor_18_out), .out(multiplexer_18_out),
    .sel(quotient[5]));
  Multiplexer #(.width(23), .enable("false")) multiplexer_19 (
    .in0({multiplexer_18_out[21:0], dividende[4]}), .in1(subtractor_19_out),
    .out({multiplexer_19_out_2[22], multiplexer_19_out}), .sel(quotient[4]));
  Multiplexer #(.width(23), .enable("false")) multiplexer_20 (
    .in0({multiplexer_19_out, dividende[3]}), .in1(subtractor_20_out), .out(multiplexer_20_out),
    .sel(quotient[3]));
  Multiplexer #(.width(23), .enable("false")) multiplexer_21 (
    .in0({multiplexer_20_out[21:0], dividende[2]}), .in1(subtractor_21_out),
    .out({multiplexer_21_out_2[22], multiplexer_21_out}), .sel(quotient[2]));
  Multiplexer #(.width(23), .enable("false")) multiplexer_22 (
    .in0({multiplexer_21_out, dividende[1]}), .in1(subtractor_22_out), .out(multiplexer_22_out),
    .sel(quotient[1]));
  Multiplexer #(.width(23), .enable("false")) multiplexer_23 (
    .in0({multiplexer_22_out[21:0], dividende[0]}), .in1(subtractor_23_out), .out(reste), .sel(quotient[0]));
endmodule

module Chiffre_7seg (
  input  [3:0] Entree,
  input  Point,
  output [7:0] Sortie
);

  Dec_b Dec_b_1 (
    .Input_1(Entree[3]), .Input_2(Entree[2]), .Input_3(Entree[1]), .Input_4(Entree[0]), .Output_1(Sortie[0]));
  Dec_a Dec_a_1 (
    .Input_1(Entree[3]), .Input_2(Entree[2]), .Input_3(Entree[1]), .Input_4(Entree[0]), .Output_1(Sortie[1]));
  Dec_f Dec_f_1 (
    .Input_1(Entree[3]), .Input_2(Entree[2]), .Input_3(Entree[1]), .Input_4(Entree[0]), .Output_1(Sortie[2]));
  Dec_g Dec_g_1 (
    .Input_1(Entree[3]), .Input_2(Entree[2]), .Input_3(Entree[1]), .Input_4(Entree[0]), .Output_1(Sortie[3]));
  Dec_c Dec_c_1 (
    .Input_1(Entree[3]), .Input_2(Entree[2]), .Input_3(Entree[1]), .Input_4(Entree[0]), .Output_1(Sortie[5]));
  Dec_d Dec_d_1 (
    .Input_1(Entree[3]), .Input_2(Entree[2]), .Input_3(Entree[1]), .Input_4(Entree[0]), .Output_1(Sortie[6]));
  Dec_e Dec_e_1 (
    .Input_1(Entree[3]), .Input_2(Entree[2]), .Input_3(Entree[1]), .Input_4(Entree[0]), .Output_1(Sortie[7]));

  assign Sortie[4] = Point;
endmodule

module Dec_a (
  input  Input_1,
  input  Input_2,
  input  Input_3,
  input  Input_4,
  output Output_1
);

  wire and_1_out, and_2_out, and_3_out, and_4_out, not_1_out, not_2_out, not_3_out, not_4_out, or_1_out;

  not not_1 (not_1_out, Input_1);
  not not_2 (not_2_out, Input_2);
  not not_3 (not_3_out, Input_3);
  not not_4 (not_4_out, Input_4);
  and and_1 (and_1_out, not_1_out, not_2_out, not_3_out, Input_4);
  and and_2 (and_2_out, not_1_out, Input_2, not_3_out, not_4_out);
  and and_3 (and_3_out, Input_1, not_2_out, Input_3, Input_4);
  and and_4 (and_4_out, Input_1, Input_2, not_3_out, Input_4);
  or or_1 (or_1_out, and_1_out, and_2_out, and_3_out, and_4_out);
  not not_5 (Output_1, or_1_out);
endmodule

module Dec_b (
  input  Input_1,
  input  Input_2,
  input  Input_3,
  input  Input_4,
  output Output_1
);

  wire and_1_out, and_2_out, and_3_out, and_4_out, and_5_out, not_1_out, not_2_out, not_3_out, not_4_out;

  not not_1 (not_1_out, Input_1);
  not not_2 (not_2_out, Input_2);
  not not_3 (not_3_out, Input_3);
  not not_4 (not_4_out, Input_4);
  and and_1 (and_1_out, not_1_out, not_2_out);
  and and_2 (and_2_out, not_2_out, not_4_out);
  and and_3 (and_3_out, not_1_out, not_3_out, not_4_out);
  and and_4 (and_4_out, not_1_out, Input_3, Input_4);
  and and_5 (and_5_out, Input_1, not_3_out, Input_4);
  or or_1 (Output_1, and_1_out, and_2_out, and_3_out, and_4_out, and_5_out);
endmodule

module Dec_c (
  input  Input_1,
  input  Input_2,
  input  Input_3,
  input  Input_4,
  output Output_1
);

  wire and_1_out, and_2_out, and_3_out, not_1_out, not_2_out, not_3_out, not_4_out, or_1_out;

  not not_1 (not_1_out, Input_1);
  not not_2 (not_2_out, Input_2);
  not not_3 (not_3_out, Input_3);
  not not_4 (not_4_out, Input_4);
  and and_1 (and_1_out, Input_1, Input_2, not_4_out);
  and and_2 (and_2_out, Input_1, Input_2, Input_3);
  and and_3 (and_3_out, not_1_out, not_2_out, Input_3, not_4_out);
  or or_1 (or_1_out, and_1_out, and_2_out, and_3_out);
  not not_5 (Output_1, or_1_out);
endmodule

module Dec_d (
  input  Input_1,
  input  Input_2,
  input  Input_3,
  input  Input_4,
  output Output_1
);

  wire and_1_out, and_2_out, and_3_out, and_4_out, and_5_out, not_1_out, not_2_out, not_3_out, not_4_out;

  not not_1 (not_1_out, Input_1);
  not not_2 (not_2_out, Input_2);
  not not_3 (not_3_out, Input_3);
  not not_4 (not_4_out, Input_4);
  and and_1 (and_1_out, Input_1, not_3_out);
  and and_2 (and_2_out, Input_2, Input_3, not_4_out);
  and and_3 (and_3_out, not_2_out, Input_3, Input_4);
  and and_4 (and_4_out, not_1_out, not_2_out, not_4_out);
  and and_5 (and_5_out, Input_2, not_3_out, Input_4);
  or or_1 (Output_1, and_1_out, and_2_out, and_3_out, and_4_out, and_5_out);
endmodule

module Dec_e (
  input  Input_1,
  input  Input_2,
  input  Input_3,
  input  Input_4,
  output Output_1
);

  wire and_1_out, and_2_out, and_3_out, and_4_out, not_1_out, not_2_out, not_3_out, not_4_out;

  not not_1 (not_1_out, Input_1);
  not not_2 (not_2_out, Input_2);
  not not_3 (not_3_out, Input_3);
  not not_4 (not_4_out, Input_4);
  and and_1 (and_1_out, Input_1, Input_2);
  and and_2 (and_2_out, Input_1, Input_3);
  and and_3 (and_3_out, not_2_out, not_4_out);
  and and_4 (and_4_out, Input_3, not_4_out);
  or or_1 (Output_1, and_1_out, and_2_out, and_3_out, and_4_out);
endmodule

module Dec_f (
  input  Input_1,
  input  Input_2,
  input  Input_3,
  input  Input_4,
  output Output_1
);

  wire and_1_out, and_2_out, and_3_out, and_4_out, not_1_out, not_2_out, not_3_out, not_4_out, or_1_out;

  not not_1 (not_1_out, Input_1);
  not not_2 (not_2_out, Input_2);
  not not_3 (not_3_out, Input_3);
  not not_4 (not_4_out, Input_4);
  and and_1 (and_1_out, Input_1, Input_2, not_3_out, Input_4);
  and and_2 (and_2_out, not_1_out, Input_3, Input_4);
  and and_3 (and_3_out, not_1_out, not_2_out, Input_3);
  and and_4 (and_4_out, not_1_out, not_2_out, Input_4);
  or or_1 (or_1_out, and_1_out, and_2_out, and_3_out, and_4_out);
  not not_5 (Output_1, or_1_out);
endmodule

module Dec_g (
  input  Input_1,
  input  Input_2,
  input  Input_3,
  input  Input_4,
  output Output_1
);

  wire and_1_out, and_2_out, and_3_out, not_1_out, not_2_out, not_3_out, not_4_out, or_1_out;

  not not_1 (not_1_out, Input_1);
  not not_2 (not_2_out, Input_2);
  not not_3 (not_3_out, Input_3);
  not not_4 (not_4_out, Input_4);
  and and_1 (and_1_out, not_1_out, not_2_out, not_3_out);
  and and_2 (and_2_out, Input_1, Input_2, not_3_out, not_4_out);
  and and_3 (and_3_out, not_1_out, Input_2, Input_3, Input_4);
  or or_1 (or_1_out, and_1_out, and_2_out, and_3_out);
  not not_5 (Output_1, or_1_out);
endmodule

module gen_impulsion_delay (
  input  Entree,
  input  CLK,
  input  E,
  output Sortie
);

  wire d_ff_1_q, d_ff_2_q;

  D_Flip_Flop #(.trigger("falling")) d_ff_1 (.D(Entree), .clk(CLK), .Q(d_ff_1_q), .reset(E));  // open: Qn, preset
  D_Flip_Flop #(.trigger("falling")) d_ff_2 (.D(d_ff_1_q), .clk(CLK), .Q(d_ff_2_q), .reset(E));  // open: Qn, preset
  and and_1 (Sortie, d_ff_1_q, ~d_ff_2_q, CLK);  // AND_Gate
endmodule

module gen_impulsion_longue (
  input  Entree,
  input  CLK,
  input  E,
  output Output_1
);

  wire d_ff_1_q, d_ff_2_q, d_ff_3_q;

  D_Flip_Flop #(.trigger("falling")) d_ff_1 (.D(Entree), .clk(CLK), .Q(d_ff_1_q), .reset(E));  // open: Qn, preset
  D_Flip_Flop #(.trigger("falling")) d_ff_2 (.D(d_ff_1_q), .clk(CLK), .Q(d_ff_2_q), .reset(E));  // open: Qn, preset
  D_Flip_Flop #(.trigger("falling")) d_ff_3 (.D(d_ff_2_q), .clk(CLK), .Q(d_ff_3_q));  // open: Qn, preset, reset
  and and_1 (Output_1, d_ff_1_q, ~d_ff_3_q);  // AND_Gate
endmodule
