// Logisim project clock_512_10_hz.circ as structural Verilog: 1 circuit, main circuit main
module main (
  input  CLK,
  input  E,
  output CLK1024Hz,
  output CLK512Hz,
  output CLK10Hz
);

  wire and_1_out, and_2_out, if51th_out, if52th_out, multiplexer_1_out, or_1_out, or_2_out, or_3_out,
       or_4_out, or_5_out, or_6_out, or_7_out, or_8_out, or_9_out, t_ff_2_q, t_ff_3_q, t_ff_4_q, t_ff_5_q,
       t_ff_6_q, t_ff_7_q, t_ff_8_q, t_ff_9_q;

  T_Flip_Flop t_ff_1 (.T(1'b1), .clk(CLK), .Q(CLK512Hz), .reset(or_1_out));  // open: Qn, preset
  or or_1 (or_1_out, E, multiplexer_1_out);
  T_Flip_Flop t_ff_2 (.T(1'b1), .clk(multiplexer_1_out), .Q(t_ff_2_q), .reset(or_2_out));  // open: Qn, preset
  or or_2 (or_2_out, E, and_2_out);
  T_Flip_Flop t_ff_3 (.T(1'b1), .clk(CLK512Hz), .Q(t_ff_3_q), .reset(or_3_out));  // open: Qn, preset
  or or_3 (or_3_out, E, multiplexer_1_out);
  T_Flip_Flop t_ff_4 (.T(1'b1), .clk(t_ff_2_q), .Q(t_ff_4_q), .reset(or_4_out));  // open: Qn, preset
  or or_4 (or_4_out, E, and_2_out);
  T_Flip_Flop t_ff_5 (.T(1'b1), .clk(t_ff_3_q), .Q(t_ff_5_q), .reset(or_5_out));  // open: Qn, preset
  and if51th (if51th_out, CLK512Hz, ~t_ff_3_q, t_ff_5_q, t_ff_7_q, ~t_ff_8_q, ~t_ff_9_q);  // AND_Gate
  T_Flip_Flop t_ff_6 (.T(1'b1), .clk(t_ff_4_q), .Q(t_ff_6_q), .reset(or_6_out));  // open: Qn, preset
  or or_5 (or_5_out, E, multiplexer_1_out);
  or or_6 (or_6_out, E, and_2_out);
  T_Flip_Flop t_ff_7 (.T(1'b1), .clk(t_ff_5_q), .Q(t_ff_7_q), .reset(or_7_out));  // open: Qn, preset
  or or_7 (or_7_out, E, multiplexer_1_out);
  and if52th (if52th_out, ~CLK512Hz, ~t_ff_3_q, t_ff_5_q, t_ff_7_q, ~t_ff_8_q, ~t_ff_9_q);  // AND_Gate
  T_Flip_Flop t_ff_8 (.T(1'b1), .clk(t_ff_7_q), .Q(t_ff_8_q), .reset(or_8_out));  // open: Qn, preset
  or or_8 (or_8_out, E, multiplexer_1_out);
  and and_1 (and_1_out, ~t_ff_2_q, ~t_ff_4_q, t_ff_6_q);  // AND_Gate
  T_Flip_Flop t_ff_9 (.T(1'b1), .clk(t_ff_8_q), .Q(t_ff_9_q), .reset(or_9_out));  // open: Qn, preset
  or or_9 (or_9_out, E, multiplexer_1_out);
  Multiplexer #(.enable("false")) multiplexer_1 (
    .in0(if51th_out), .in1(if52th_out), .out(multiplexer_1_out), .sel(and_1_out));
  and and_2 (and_2_out, and_1_out, if52th_out, multiplexer_1_out);
  T_Flip_Flop t_ff_10 (.T(1'b1), .clk(multiplexer_1_out), .Q(CLK10Hz), .reset(E));  // open: Qn, preset

  assign CLK1024Hz = CLK;
endmodule
