// Logisim project convertisseur_temps.circ as structural Verilog: 1 circuit, main circuit main
module main (
  input  [22:0] timestamp,
  output [2:0] jour_semaine,
  output [4:0] heure,
  output [5:0] minutes,
  output [5:0] secondes,
  output [3:0] diziemes
);

  wire [9:4] divider_4_rem;
  wire [9:6] divider_4_out;
  wire [15:0] divider_3_rem;
  wire [15:6] divider_3_out;
  wire [19:0] divider_2_rem;
  wire [19:5] divider_2_out;
  wire [22:0] divider_1_rem;
  wire [22:3] divider_1_out;

  Divider #(.width(23)) divider_1 (
    .a(timestamp), .b(23'hd2f00), .out({divider_1_out, jour_semaine}), .rem(divider_1_rem));  // open: upper
  Divider #(.width(20)) divider_2 (
    .a(divider_1_rem[19:0]), .b(20'h8ca0), .out({divider_2_out, heure}), .rem(divider_2_rem));  // open: upper
  Divider #(.width(16)) divider_3 (
    .a(divider_2_rem[15:0]), .b(16'h258), .out({divider_3_out, minutes}), .rem(divider_3_rem));  // open: upper
  Divider #(.width(10)) divider_4 (
    .a(divider_3_rem[9:0]), .b(10'ha), .out({divider_4_out, secondes}), .rem({divider_4_rem, diziemes}));  // open: upper
endmodule
