// Logisim project diviseur_.circ as structural Verilog: 1 circuit, main circuit main
module main (
  input  [22:0] dividende,
  input  [5:0] diviseur,
  output [22:0] quotient,
  output [5:0] reste
);

  wire subtractor_1_bout, subtractor_2_bout, subtractor_3_bout, subtractor_4_bout, subtractor_5_bout,
       subtractor_6_bout, subtractor_7_bout, subtractor_8_bout, subtractor_9_bout, subtractor_10_bout,
       subtractor_11_bout, subtractor_12_bout, subtractor_13_bout, subtractor_14_bout, subtractor_15_bout,
       subtractor_16_bout, subtractor_17_bout, subtractor_18_bout, subtractor_19_bout, subtractor_20_bout,
       subtractor_21_bout, subtractor_22_bout, subtractor_23_bout;
  wire [5:0] multiplexer_2_out, multiplexer_4_out, multiplexer_6_out, multiplexer_8_out, multiplexer_10_out,
       multiplexer_12_out, multiplexer_14_out, multiplexer_16_out, multiplexer_18_out, multiplexer_20_out,
       multiplexer_22_out, subtractor_1_out, subtractor_2_out, subtractor_3_out, subtractor_4_out,
       subtractor_5_out, subtractor_6_out, subtractor_7_out, subtractor_8_out, subtractor_9_out,
       subtractor_10_out, subtractor_11_out, subtractor_12_out, subtractor_13_out, subtractor_14_out,
       subtractor_15_out, subtractor_16_out, subtractor_17_out, subtractor_18_out, subtractor_19_out,
       subtractor_20_out, subtractor_21_out, subtractor_22_out, subtractor_23_out;
  wire [5:1] multiplexer_1_out, multiplexer_3_out, multiplexer_5_out, multiplexer_7_out, multiplexer_9_out,
       multiplexer_11_out, multiplexer_13_out, multiplexer_15_out, multiplexer_17_out, multiplexer_19_out,
       multiplexer_21_out;
  wire [5:5] multiplexer_1_out_2, multiplexer_3_out_2, multiplexer_5_out_2, multiplexer_7_out_2,
       multiplexer_9_out_2, multiplexer_11_out_2, multiplexer_13_out_2, multiplexer_15_out_2,
       multiplexer_17_out_2, multiplexer_19_out_2, multiplexer_21_out_2;

  Subtractor #(.width(6)) subtractor_1 (
    .a({{5{1'b0}}, dividende[22]}), .b(diviseur), .out(subtractor_1_out), .bout(subtractor_1_bout));  // open: bin
  not not_1 (quotient[22], subtractor_1_bout);
  Subtractor #(.width(6)) subtractor_2 (
    .a({multiplexer_1_out, dividende[21]}), .b(diviseur), .out(subtractor_2_out), .bout(subtractor_2_bout));  // open: bin
  not not_2 (quotient[21], subtractor_2_bout);
  Subtractor #(.width(6)) subtractor_3 (
    .a({multiplexer_2_out[4:0], dividende[20]}), .b(diviseur), .out(subtractor_3_out),
    .bout(subtractor_3_bout));  // open: bin
  not not_3 (quotient[20], subtractor_3_bout);
  Subtractor #(.width(6)) subtractor_4 (
    .a({multiplexer_3_out, dividende[19]}), .b(diviseur), .out(subtractor_4_out), .bout(subtractor_4_bout));  // open: bin
  not not_4 (quotient[19], subtractor_4_bout);
  Subtractor #(.width(6)) subtractor_5 (
    .a({multiplexer_4_out[4:0], dividende[18]}), .b(diviseur), .out(subtractor_5_out),
    .bout(subtractor_5_bout));  // open: bin
  not not_5 (quotient[18], subtractor_5_bout);
  Subtractor #(.width(6)) subtractor_6 (
    .a({multiplexer_5_out, dividende[17]}), .b(diviseur), .out(subtractor_6_out), .bout(subtractor_6_bout));  // open: bin
  not not_6 (quotient[17], subtractor_6_bout);
  Subtractor #(.width(6)) subtractor_7 (
    .a({multiplexer_6_out[4:0], dividende[16]}), .b(diviseur), .out(subtractor_7_out),
    .bout(subtractor_7_bout));  // open: bin
  not not_7 (quotient[16], subtractor_7_bout);
  Subtractor #(.width(6)) subtractor_8 (
    .a({multiplexer_7_out, dividende[15]}), .b(diviseur), .out(subtractor_8_out), .bout(subtractor_8_bout));  // open: bin
  not not_8 (quotient[15], subtractor_8_bout);
  Subtractor #(.width(6)) subtractor_9 (
    .a({multiplexer_8_out[4:0], dividende[14]}), .b(diviseur), .out(subtractor_9_out),
    .bout(subtractor_9_bout));  // open: bin
  not not_9 (quotient[14], subtractor_9_bout);
  Subtractor #(.width(6)) subtractor_10 (
    .a({multiplexer_9_out, dividende[13]}), .b(diviseur), .out(subtractor_10_out), .bout(subtractor_10_bout));  // open: bin
  not not_10 (quotient[13], subtractor_10_bout);
  Subtractor #(.width(6)) subtractor_11 (
    .a({multiplexer_10_out[4:0], dividende[12]}), .b(diviseur), .out(subtractor_11_out),
    .bout(subtractor_11_bout));  // open: bin
  not not_11 (quotient[12], subtractor_11_bout);
  Subtractor #(.width(6)) subtractor_12 (
    .a({multiplexer_11_out, dividende[11]}), .b(diviseur), .out(subtractor_12_out), .bout(subtractor_12_bout));  // open: bin
  not not_12 (quotient[11], subtractor_12_bout);
  Subtractor #(.width(6)) subtractor_13 (
    .a({multiplexer_12_out[4:0], dividende[10]}), .b(diviseur), .out(subtractor_13_out),
    .bout(subtractor_13_bout));  // open: bin
  not not_13 (quotient[10], subtractor_13_bout);
  Subtractor #(.width(6)) subtractor_14 (
    .a({multiplexer_13_out, dividende[9]}), .b(diviseur), .out(subtractor_14_out), .bout(subtractor_14_bout));  // open: bin
  not not_14 (quotient[9], subtractor_14_bout);
  Subtractor #(.width(6)) subtractor_15 (
    .a({multiplexer_14_out[4:0], dividende[8]}), .b(diviseur), .out(subtractor_15_out),
    .bout(subtractor_15_bout));  // open: bin
  not not_15 (quotient[8], subtractor_15_bout);
  Subtractor #(.width(6)) subtractor_16 (
    .a({multiplexer_15_out, dividende[7]}), .b(diviseur), .out(subtractor_16_out), .bout(subtractor_16_bout));  // open: bin
  not not_16 (quotient[7], subtractor_16_bout);
  Subtractor #(.width(6)) subtractor_17 (
    .a({multiplexer_16_out[4:0], dividende[6]}), .b(diviseur), .out(subtractor_17_out),
    .bout(subtractor_17_bout));  // open: bin
  not not_17 (quotient[6], subtractor_17_bout);
  Subtractor #(.width(6)) subtractor_18 (
    .a({multiplexer_17_out, dividende[5]}), .b(diviseur), .out(subtractor_18_out), .bout(subtractor_18_bout));  // open: bin
  not not_18 (quotient[5], subtractor_18_bout);
  Subtractor #(.width(6)) subtractor_19 (
    .a({multiplexer_18_out[4:0], dividende[4]}), .b(diviseur), .out(subtractor_19_out),
    .bout(subtractor_19_bout));  // open: bin
  not not_19 (quotient[4], subtractor_19_bout);
  Subtractor #(.width(6)) subtractor_20 (
    .a({multiplexer_19_out, dividende[3]}), .b(diviseur), .out(subtractor_20_out), .bout(subtractor_20_bout));  // open: bin
  not not_20 (quotient[3], subtractor_20_bout);
  Subtractor #(.width(6)) subtractor_21 (
    .a({multiplexer_20_out[4:0], dividende[2]}), .b(diviseur), .out(subtractor_21_out),
    .bout(subtractor_21_bout));  // open: bin
  not not_21 (quotient[2], subtractor_21_bout);
  Subtractor #(.width(6)) subtractor_22 (
    .a({multiplexer_21_out, dividende[1]}), .b(diviseur), .out(subtractor_22_out), .bout(subtractor_22_bout));  // open: bin
  not not_22 (quotient[1], subtractor_22_bout);
  Subtractor #(.width(6)) subtractor_23 (
    .a({multiplexer_22_out[4:0], dividende[0]}), .b(diviseur), .out(subtractor_23_out),
    .bout(subtractor_23_bout));  // open: bin
  not not_23 (quotient[0], subtractor_23_bout);
  Multiplexer #(.width(6), .enable("false")) multiplexer_1 (
    .in0({{5{1'b0}}, dividende[22]}), .in1(subtractor_1_out),
    .out({multiplexer_1_out_2[5], multiplexer_1_out}), .sel(quotient[22]));
  Multiplexer #(.width(6), .enable("false")) multiplexer_2 (
    .in0({multiplexer_1_out, dividende[21]}), .in1(subtractor_2_out), .out(multiplexer_2_out),
    .sel(quotient[21]));
  Multiplexer #(.width(6), .enable("false")) multiplexer_3 (
    .in0({multiplexer_2_out[4:0], dividende[20]}), .in1(subtractor_3_out),
    .out({multiplexer_3_out_2[5], multiplexer_3_out}), .sel(quotient[20]));
  Multiplexer #(.width(6), .enable("false")) multiplexer_4 (
    .in0({multiplexer_3_out, dividende[19]}), .in1(subtractor_4_out), .out(multiplexer_4_out),
    .sel(quotient[19]));
  Multiplexer #(.width(6), .enable("false")) multiplexer_5 (
    .in0({multiplexer_4_out[4:0], dividende[18]}), .in1(subtractor_5_out),
    .out({multiplexer_5_out_2[5], multiplexer_5_out}), .sel(quotient[18]));
  Multiplexer #(.width(6), .enable("false")) multiplexer_6 (
    .in0({multiplexer_5_out, dividende[17]}), .in1(subtractor_6_out), .out(multiplexer_6_out),
    .sel(quotient[17]));
  Multiplexer #(.width(6), .enable("false")) multiplexer_7 (
    .in0({multiplexer_6_out[4:0], dividende[16]}), .in1(subtractor_7_out),
    .out({multiplexer_7_out_2[5], multiplexer_7_out}), .sel(quotient[16]));
  Multiplexer #(.width(6), .enable("false")) multiplexer_8 (
    .in0({multiplexer_7_out, dividende[15]}), .in1(subtractor_8_out), .out(multiplexer_8_out),
    .sel(quotient[15]));
  Multiplexer #(.width(6), .enable("false")) multiplexer_9 (
    .in0({multiplexer_8_out[4:0], dividende[14]}), .in1(subtractor_9_out),
    .out({multiplexer_9_out_2[5], multiplexer_9_out}), .sel(quotient[14]));
  Multiplexer #(.width(6), .enable("false")) multiplexer_10 (
    .in0({multiplexer_9_out, dividende[13]}), .in1(subtractor_10_out), .out(multiplexer_10_out),
    .sel(quotient[13]));
  Multiplexer #(.width(6), .enable("false")) multiplexer_11 (
    .in0({multiplexer_10_out[4:0], dividende[12]}), .in1(subtractor_11_out),
    .out({multiplexer_11_out_2[5], multiplexer_11_out}), .sel(quotient[12]));
  Multiplexer #(.width(6), .enable("false")) multiplexer_12 (
    .in0({multiplexer_11_out, dividende[11]}), .in1(subtractor_12_out), .out(multiplexer_12_out),
    .sel(quotient[11]));
  Multiplexer #(.width(6), .enable("false")) multiplexer_13 (
    .in0({multiplexer_12_out[4:0], dividende[10]}), .in1(subtractor_13_out),
    .out({multiplexer_13_out_2[5], multiplexer_13_out}), .sel(quotient[10]));
  Multiplexer #(.width(6), .enable("false")) multiplexer_14 (
    .in0({multiplexer_13_out, dividende[9]}), .in1(subtractor_14_out), .out(multiplexer_14_out),
    .sel(quotient[9]));
  Multiplexer #(.width(6), .enable("false")) multiplexer_15 (
    .in0({multiplexer_14_out[4:0], dividende[8]}), .in1(subtractor_15_out),
    .out({multiplexer_15_out_2[5], multiplexer_15_out}), .sel(quotient[8]));
  Multiplexer #(.width(6), .enable("false")) multiplexer_16 (
    .in0({multiplexer_15_out, dividende[7]}), .in1(subtractor_16_out), .out(multiplexer_16_out),
    .sel(quotient[7]));
  Multiplexer #(.width(6), .enable("false")) multiplexer_17 (
    .in0({multiplexer_16_out[4:0], dividende[6]}), .in1(subtractor_17_out),
    .out({multiplexer_17_out_2[5], multiplexer_17_out}), .sel(quotient[6]));
  Multiplexer #(.width(6), .enable("false")) multiplexer_18 (
    .in0({multiplexer_17_out, dividende[5]}), .in1(subtractor_18_out), .out(multiplexer_18_out),
    .sel(quotient[5]));
  Multiplexer #(.width(6), .enable("false")) multiplexer_19 (
    .in0({multiplexer_18_out[4:0], dividende[4]}), .in1(subtractor_19_out),
    .out({multiplexer_19_out_2[5], multiplexer_19_out}), .sel(quotient[4]));
  Multiplexer #(.width(6), .enable("false")) multiplexer_20 (
    .in0({multiplexer_19_out, dividende[3]}), .in1(subtractor_20_out), .out(multiplexer_20_out),
    .sel(quotient[3]));
  Multiplexer #(.width(6), .enable("false")) multiplexer_21 (
    .in0({multiplexer_20_out[4:0], dividende[2]}), .in1(subtractor_21_out),
    .out({multiplexer_21_out_2[5], multiplexer_21_out}), .sel(quotient[2]));
  Multiplexer #(.width(6), .enable("false")) multiplexer_22 (
    .in0({multiplexer_21_out, dividende[1]}), .in1(subtractor_22_out), .out(multiplexer_22_out),
    .sel(quotient[1]));
  Multiplexer #(.width(6), .enable("false")) multiplexer_23 (
    .in0({multiplexer_22_out[4:0], dividende[0]}), .in1(subtractor_23_out), .out(reste), .sel(quotient[0]));
endmodule
