// Logisim project timer_.circ as structural Verilog: 13 circuits, main circuit main
module main (
  input  [3:0] boutons,
  input  [2:0] etat,
  input  [22:0] temps,
  output [7:0] Seg0,
  output [7:0] Seg1,
  output [7:0] Seg2,
  output [7:0] Seg3,
  output [7:0] Seg4,
  output [7:0] Seg5,
  output sonne
);

  wire actif_q, and_1_out, and_2_out, and_3_out, and_5_out, and_8_out, and_9_out, and_10_out, and_12_out,
       comparator_1_eq, comparator_2_eq, d_ff_1_q, d_ff_2_q, d_ff_3_q, d_ff_4_q, not_1_out, subtractor_1_bout;
  wire [1:0] or_1_out;
  wire [2:0] regle;
  wire [22:0] adder_1_out, adder_2_out, duree_q, fin_q, multiplexer_1_out, multiplexer_2_out,
       multiplexer_3_out, subtractor_1_out, subtractor_2_out, temps_prevu_q;

  Comparator #(.width(3), .mode("unsigned")) comparator_1 (.a(etat), .b(3'b011), .eq(comparator_1_eq));  // open: gt, lt
  D_Flip_Flop d_ff_1 (.D(1'b1), .clk(and_1_out), .Q(d_ff_1_q), .reset(and_3_out));  // open: Qn, preset
  and and_1 (and_1_out, boutons[1], ~actif_q, comparator_1_eq);  // AND_Gate
  and and_2 (and_2_out, boutons[2], ~d_ff_1_q, comparator_1_eq);  // AND_Gate
  and and_3 (and_3_out, d_ff_1_q, boutons[1], comparator_1_eq, ~and_1_out);  // AND_Gate
  T_Flip_Flop actif (.T(comparator_1_eq), .clk(and_2_out), .Q(actif_q));  // open: Qn, reset, preset
  and and_4 (regle[0], d_ff_1_q, ~d_ff_2_q);  // AND_Gate
  D_Flip_Flop d_ff_2 (.D(d_ff_1_q), .clk(boutons[2]), .Q(d_ff_2_q), .reset(d_ff_4_q));  // open: Qn, preset
  Register #(.width(23)) duree (.D(temps_prevu_q), .clk(and_3_out), .Q(duree_q));  // open: en, clr
  and and_5 (and_5_out, boutons[2], actif_q);
  and and_6 (regle[1], d_ff_2_q, ~d_ff_3_q);  // AND_Gate
  D_Flip_Flop d_ff_3 (.D(d_ff_2_q), .clk(boutons[2]), .Q(d_ff_3_q), .reset(d_ff_4_q));  // open: Qn, preset
  Register #(.width(23)) debut (.D(temps), .clk(and_5_out));  // open: en, Q, clr
  and and_7 (regle[2], d_ff_3_q, ~d_ff_4_q);  // AND_Gate
  D_Flip_Flop d_ff_4 (.D(d_ff_3_q), .clk(boutons[2]), .Q(d_ff_4_q), .reset(d_ff_4_q));  // open: Qn, preset
  Adder #(.width(23)) adder_1 (.a(duree_q), .b(temps), .out(adder_1_out));  // open: cin, cout
  Subtractor #(.width(23)) subtractor_1 (
    .a(adder_1_out), .b(23'h5c4900), .out(subtractor_1_out), .bout(subtractor_1_bout));  // open: bin
  Register #(.width(23)) fin (.D(multiplexer_1_out), .clk(and_5_out), .Q(fin_q));  // open: en, clr
  Multiplexer #(.width(23), .enable("false")) multiplexer_1 (
    .in0(subtractor_1_out), .in1(adder_1_out), .out(multiplexer_1_out), .sel(subtractor_1_bout));
  and and_8 (and_8_out, regle[0], boutons[0]);
  and and_9 (and_9_out, regle[1], boutons[0]);
  and and_10 (and_10_out, regle[2], boutons[0]);
  Comparator #(.width(23), .mode("unsigned")) comparator_2 (
    .a(fin_q), .b(temps), .eq(comparator_2_eq));  // open: gt, lt
  or or_1 (or_1_out[0], and_8_out, and_10_out);
  or or_2 (or_1_out[1], and_9_out, and_10_out);
  and and_11 (sonne, comparator_2_eq, actif_q);
  Multiplexer #(.select(2), .width(23), .enable("false")) multiplexer_2 (
    .in0({23{1'b0}}), .in1(23'h8ca0), .in2(23'h1770), .in3(23'h258), .out(multiplexer_2_out), .sel(or_1_out));
  Subtractor #(.width(23)) subtractor_2 (.a(fin_q), .b(temps), .out(subtractor_2_out));  // open: bin, bout
  Adder #(.width(23)) adder_2 (.a(multiplexer_2_out), .b(temps_prevu_q), .out(adder_2_out));  // open: cin, cout
  not not_1 (not_1_out, boutons[0]);
  Multiplexer #(.width(23), .enable("false")) multiplexer_3 (
    .in0(duree_q), .in1(subtractor_2_out), .out(multiplexer_3_out), .sel(actif_q));
  Register #(.width(23)) temps_prevu (
    .D(adder_2_out), .clk(not_1_out), .Q(temps_prevu_q), .clr(and_12_out));  // open: en
  and and_12 (and_12_out, d_ff_1_q, and_1_out);
  T_affiche t_affiche_1 (
    .regle(regle), .sous_systeme(d_ff_1_q), .temps_set(adder_2_out), .temps_restant(multiplexer_3_out),
    .clignotement(temps[2]), .Seg0(Seg0), .Seg1(Seg1), .Seg2(Seg2), .Seg3(Seg3), .Seg4(Seg4), .Seg5(Seg5));
endmodule

module T_affiche (
  input  [2:0] regle,
  input  sous_systeme,
  input  [22:0] temps_set,
  input  [22:0] temps_restant,
  input  clignotement,
  output [7:0] Seg0,
  output [7:0] Seg1,
  output [7:0] Seg2,
  output [7:0] Seg3,
  output [7:0] Seg4,
  output [7:0] Seg5
);

  wire nand_1_out, nand_2_out, nand_3_out, not_1_out;
  wire [3:0] conv_unit_dizaines_1_dizaines, conv_unit_dizaines_1_unites, conv_unit_dizaines_2_dizaines,
       conv_unit_dizaines_2_unites, conv_unit_dizaines_3_dizaines, conv_unit_dizaines_3_unites;
  wire [4:0] conv_temps_1_heures;
  wire [5:0] conv_temps_1_minutes, conv_temps_1_secondes;
  wire [7:0] chiffre_7seg_1_sortie, chiffre_7seg_2_sortie, chiffre_7seg_3_sortie, chiffre_7seg_4_sortie,
       chiffre_7seg_5_sortie, chiffre_7seg_6_sortie;
  wire [22:0] multiplexer_1_out;

  Multiplexer #(.width(23), .enable("false")) multiplexer_1 (
    .in0(temps_restant), .in1(temps_set), .out(multiplexer_1_out), .sel(sous_systeme));
  Conv_temps conv_temps_1 (
    .Temps(multiplexer_1_out), .Heures(conv_temps_1_heures), .Minutes(conv_temps_1_minutes),
    .Secondes(conv_temps_1_secondes));  // open: Jours, dixiemes
  conv_unit_dizaines conv_unit_dizaines_1 (
    .entree({conv_temps_1_heures, 1'b0}), .Dizaines(conv_unit_dizaines_1_dizaines),
    .Unites(conv_unit_dizaines_1_unites));
  conv_unit_dizaines conv_unit_dizaines_2 (
    .entree(conv_temps_1_minutes), .Dizaines(conv_unit_dizaines_2_dizaines),
    .Unites(conv_unit_dizaines_2_unites));
  conv_unit_dizaines conv_unit_dizaines_3 (
    .entree(conv_temps_1_secondes), .Dizaines(conv_unit_dizaines_3_dizaines),
    .Unites(conv_unit_dizaines_3_unites));
  not not_1 (not_1_out, sous_systeme);
  Chiffre_7seg chiffre_7seg_1 (.Entree(conv_unit_dizaines_1_dizaines), .Point(1'b0), .Sortie(chiffre_7seg_1_sortie));
  Chiffre_7seg chiffre_7seg_2 (.Entree(conv_unit_dizaines_1_unites), .Point(1'b1), .Sortie(chiffre_7seg_2_sortie));
  Chiffre_7seg chiffre_7seg_3 (.Entree(conv_unit_dizaines_2_dizaines), .Point(1'b0), .Sortie(chiffre_7seg_3_sortie));
  Chiffre_7seg chiffre_7seg_4 (.Entree(conv_unit_dizaines_2_unites), .Point(1'b1), .Sortie(chiffre_7seg_4_sortie));
  Chiffre_7seg chiffre_7seg_5 (.Entree(conv_unit_dizaines_3_dizaines), .Point(1'b0), .Sortie(chiffre_7seg_5_sortie));
  Chiffre_7seg chiffre_7seg_6 (.Entree(conv_unit_dizaines_3_unites), .Point(1'b0), .Sortie(chiffre_7seg_6_sortie));
  nand nand_1 (nand_1_out, sous_systeme, regle[0], clignotement);
  nand nand_2 (nand_2_out, sous_systeme, regle[1], clignotement);
  nand nand_3 (nand_3_out, sous_systeme, regle[2], clignotement);
  Multiplexer #(.width(8), .enable("false")) multiplexer_2 (
    .in0({8{1'b0}}), .in1(chiffre_7seg_1_sortie), .out(Seg0), .sel(nand_1_out));
  Multiplexer #(.width(8), .enable("false")) multiplexer_3 (
    .in0({8{1'b0}}), .in1(chiffre_7seg_2_sortie), .out(Seg1), .sel(nand_1_out));
  Multiplexer #(.width(8), .enable("false")) multiplexer_4 (
    .in0({8{1'b0}}), .in1(chiffre_7seg_3_sortie), .out(Seg2), .sel(nand_2_out));
  Multiplexer #(.width(8), .enable("false")) multiplexer_5 (
    .in0({8{1'b0}}), .in1(chiffre_7seg_4_sortie), .out(Seg3), .sel(nand_3_out));
  Multiplexer #(.width(8), .enable("false")) multiplexer_6 (
    .in0({8{1'b0}}), .in1(chiffre_7seg_5_sortie), .out(Seg4), .sel(not_1_out));
  Multiplexer #(.width(8), .enable("false")) multiplexer_7 (
    .in0({8{1'b0}}), .in1(chiffre_7seg_6_sortie), .out(Seg5), .sel(not_1_out));
endmodule

module Conv_temps (
  input  [22:0] Temps,
  output [2:0] Jours,
  output [4:0] Heures,
  output [5:0] Minutes,
  output [5:0] Secondes,
  output [3:0] dixiemes
);

  wire [22:0] diviseur_1_reste, diviseur_2_reste, diviseur_3_reste;
  wire [22:3] diviseur_1_quotient;
  wire [22:4] diviseur_4_reste;
  wire [22:5] diviseur_2_quotient;
  wire [22:6] diviseur_3_quotient, diviseur_4_quotient;

  diviseur diviseur_1 (
    .dividende(Temps), .diviseur(23'hd2f00), .quotient({diviseur_1_quotient, Jours}), .reste(diviseur_1_reste));
  diviseur diviseur_2 (
    .dividende(diviseur_1_reste), .diviseur(23'h8ca0), .quotient({diviseur_2_quotient, Heures}),
    .reste(diviseur_2_reste));
  diviseur diviseur_3 (
    .dividende(diviseur_2_reste), .diviseur(23'h258), .quotient({diviseur_3_quotient, Minutes}),
    .reste(diviseur_3_reste));
  diviseur diviseur_4 (
    .dividende(diviseur_3_reste), .diviseur(23'ha), .quotient({diviseur_4_quotient, Secondes}),
    .reste({diviseur_4_reste, dixiemes}));
endmodule

module Chiffre_7seg (
  input  [3:0] Entree,
  input  Point,
  output [7:0] Sortie
);

  Dec_b dec_b_1 (.in_1(Entree[3]), .in_2(Entree[2]), .in_3(Entree[1]), .in_4(Entree[0]), .out_5(Sortie[0]));
  Dec_a dec_a_1 (.in_1(Entree[3]), .in_2(Entree[2]), .in_3(Entree[1]), .in_4(Entree[0]), .out_5(Sortie[1]));
  Dec_f dec_f_1 (.in_1(Entree[3]), .in_2(Entree[2]), .in_3(Entree[1]), .in_4(Entree[0]), .out_5(Sortie[2]));
  Dec_g dec_g_1 (.in_1(Entree[3]), .in_2(Entree[2]), .in_3(Entree[1]), .in_4(Entree[0]), .out_5(Sortie[3]));
  Dec_c dec_c_1 (.in_1(Entree[3]), .in_2(Entree[2]), .in_3(Entree[1]), .in_4(Entree[0]), .out_5(Sortie[5]));
  Dec_d dec_d_1 (.in_1(Entree[3]), .in_2(Entree[2]), .in_3(Entree[1]), .in_4(Entree[0]), .out_5(Sortie[6]));
  Dec_e dec_e_1 (.in_1(Entree[3]), .in_2(Entree[2]), .in_3(Entree[1]), .in_4(Entree[0]), .out_5(Sortie[7]));

  assign Sortie[4] = Point;
endmodule

module Dec_a (
  input  in_1,
  input  in_2,
  input  in_3,
  input  in_4,
  output out_5
);

  wire and_1_out, and_2_out, and_3_out, and_4_out, not_1_out, not_2_out, not_3_out, not_4_out, or_1_out;

  not not_1 (not_1_out, in_1);
  not not_2 (not_2_out, in_2);
  not not_3 (not_3_out, in_3);
  not not_4 (not_4_out, in_4);
  and and_1 (and_1_out, not_1_out, not_2_out, not_3_out, in_4);
  and and_2 (and_2_out, not_1_out, in_2, not_3_out, not_4_out);
  and and_3 (and_3_out, in_1, not_2_out, in_3, in_4);
  and and_4 (and_4_out, in_1, in_2, not_3_out, in_4);
  or or_1 (or_1_out, and_1_out, and_2_out, and_3_out, and_4_out);
  not not_5 (out_5, or_1_out);
endmodule

module Dec_b (
  input  in_1,
  input  in_2,
  input  in_3,
  input  in_4,
  output out_5
);

  wire and_1_out, and_2_out, and_3_out, and_4_out, and_5_out, not_1_out, not_2_out, not_3_out, not_4_out;

  not not_1 (not_1_out, in_1);
  not not_2 (not_2_out, in_2);
  not not_3 (not_3_out, in_3);
  not not_4 (not_4_out, in_4);
  and and_1 (and_1_out, not_1_out, not_2_out);
  and and_2 (and_2_out, not_2_out, not_4_out);
  and and_3 (and_3_out, not_1_out, not_3_out, not_4_out);
  and and_4 (and_4_out, not_1_out, in_3, in_4);
  and and_5 (and_5_out, in_1, not_3_out, in_4);
  or or_1 (out_5, and_1_out, and_2_out, and_3_out, and_4_out, and_5_out);
endmodule

module Dec_c (
  input  in_1,
  input  in_2,
  input  in_3,
  input  in_4,
  output out_5
);

  wire and_1_out, and_2_out, and_3_out, not_1_out, not_2_out, not_3_out, not_4_out, or_1_out;

  not not_1 (not_1_out, in_1);
  not not_2 (not_2_out, in_2);
  not not_3 (not_3_out, in_3);
  not not_4 (not_4_out, in_4);
  and and_1 (and_1_out, in_1, in_2, not_4_out);
  and and_2 (and_2_out, in_1, in_2, in_3);
  and and_3 (and_3_out, not_1_out, not_2_out, in_3, not_4_out);
  or or_1 (or_1_out, and_1_out, and_2_out, and_3_out);
  not not_5 (out_5, or_1_out);
endmodule

module Dec_d (
  input  in_1,
  input  in_2,
  input  in_3,
  input  in_4,
  output out_5
);

  wire and_1_out, and_2_out, and_3_out, and_4_out, and_5_out, not_1_out, not_2_out, not_3_out, not_4_out;

  not not_1 (not_1_out, in_1);
  not not_2 (not_2_out, in_2);
  not not_3 (not_3_out, in_3);
  not not_4 (not_4_out, in_4);
  and and_1 (and_1_out, in_1, not_3_out);
  and and_2 (and_2_out, in_2, in_3, not_4_out);
  and and_3 (and_3_out, not_2_out, in_3, in_4);
  and and_4 (and_4_out, not_1_out, not_2_out, not_4_out);
  and and_5 (and_5_out, in_2, not_3_out, in_4);
  or or_1 (out_5, and_1_out, and_2_out, and_3_out, and_4_out, and_5_out);
endmodule

module Dec_e (
  input  in_1,
  input  in_2,
  input  in_3,
  input  in_4,
  output out_5
);

  wire and_1_out, and_2_out, and_3_out, and_4_out, not_1_out, not_2_out, not_3_out, not_4_out;

  not not_1 (not_1_out, in_1);
  not not_2 (not_2_out, in_2);
  not not_3 (not_3_out, in_3);
  not not_4 (not_4_out, in_4);
  and and_1 (and_1_out, in_1, in_2);
  and and_2 (and_2_out, in_1, in_3);
  and and_3 (and_3_out, not_2_out, not_4_out);
  and and_4 (and_4_out, in_3, not_4_out);
  or or_1 (out_5, and_1_out, and_2_out, and_3_out, and_4_out);
endmodule

module Dec_f (
  input  in_1,
  input  in_2,
  input  in_3,
  input  in_4,
  output out_5
);

  wire and_1_out, and_2_out, and_3_out, and_4_out, not_1_out, not_2_out, not_3_out, not_4_out, or_1_out;

  not not_1 (not_1_out, in_1);
  not not_2 (not_2_out, in_2);
  not not_3 (not_3_out, in_3);
  not not_4 (not_4_out, in_4);
  and and_1 (and_1_out, in_1, in_2, not_3_out, in_4);
  and and_2 (and_2_out, not_1_out, in_3, in_4);
  and and_3 (and_3_out, not_1_out, not_2_out, in_3);
  and and_4 (and_4_out, not_1_out, not_2_out, in_4);
  or or_1 (or_1_out, and_1_out, and_2_out, and_3_out, and_4_out);
  not not_5 (out_5, or_1_out);
endmodule

module Dec_g (
  input  in_1,
  input  in_2,
  input  in_3,
  input  in_4,
  output out_5
);

  wire and_1_out, and_2_out, and_3_out, not_1_out, not_2_out, not_3_out, not_4_out, or_1_out;

  not not_1 (not_1_out, in_1);
  not not_2 (not_2_out, in_2);
  not not_3 (not_3_out, in_3);
  not not_4 (not_4_out, in_4);
  and and_1 (and_1_out, not_1_out, not_2_out, not_3_out);
  and and_2 (and_2_out, in_1, in_2, not_3_out, not_4_out);
  and and_3 (and_3_out, not_1_out, in_2, in_3, in_4);
  or or_1 (or_1_out, and_1_out, and_2_out, and_3_out);
  not not_5 (out_5, or_1_out);
endmodule

module conv_unit_dizaines (
  input  [5:0] entree,
  output [3:0] Dizaines,
  output [3:0] Unites
);

  wire [22:4] diviseur_1_quotient, diviseur_1_reste;

  diviseur diviseur_1 (
    .dividende({{17{1'b0}}, entree}), .diviseur(23'ha), .quotient({diviseur_1_quotient, Dizaines}),
    .reste({diviseur_1_reste, Unites}));
endmodule

module diviseur (
  input  [22:0] dividende,
  input  [22:0] diviseur,
  output [22:0] quotient,
  output [22:0] reste
);

  wire subtractor_1_bout, subtractor_2_bout, subtractor_3_bout, subtractor_4_bout, subtractor_5_bout,
       subtractor_6_bout, subtractor_7_bout, subtractor_8_bout, subtractor_9_bout, subtractor_10_bout,
       subtractor_11_bout, subtractor_12_bout, subtractor_13_bout, subtractor_14_bout, subtractor_15_bout,
       subtractor_16_bout, subtractor_17_bout, subtractor_18_bout, subtractor_19_bout, subtractor_20_bout,
       subtractor_21_bout, subtractor_22_bout, subtractor_23_bout;
  wire [22:0] multiplexer_2_out, multiplexer_4_out, multiplexer_6_out, multiplexer_8_out, multiplexer_10_out,
       multiplexer_12_out, multiplexer_14_out, multiplexer_16_out, multiplexer_18_out, multiplexer_20_out,
       multiplexer_22_out, subtractor_1_out, subtractor_2_out, subtractor_3_out, subtractor_4_out,
       subtractor_5_out, subtractor_6_out, subtractor_7_out, subtractor_8_out, subtractor_9_out,
       subtractor_10_out, subtractor_11_out, subtractor_12_out, subtractor_13_out, subtractor_14_out,
       subtractor_15_out, subtractor_16_out, subtractor_17_out, subtractor_18_out, subtractor_19_out,
       subtractor_20_out, subtractor_21_out, subtractor_22_out, subtractor_23_out;
  wire [22:1] multiplexer_1_out, multiplexer_3_out, multiplexer_5_out, multiplexer_7_out, multiplexer_9_out,
       multiplexer_11_out, multiplexer_13_out, multiplexer_15_out, multiplexer_17_out, multiplexer_19_out,
       multiplexer_21_out;
  wire [22:22] multiplexer_1_out_2, multiplexer_3_out_2, multiplexer_5_out_2, multiplexer_7_out_2,
       multiplexer_9_out_2, multiplexer_11_out_2, multiplexer_13_out_2, multiplexer_15_out_2,
       multiplexer_17_out_2, multiplexer_19_out_2, multiplexer_21_out_2;

  Subtractor #(.width(23)) subtractor_1 (
    .a({{22{1'b0}}, dividende[22]}), .b(diviseur), .out(subtractor_1_out), .bout(subtractor_1_bout));  // open: bin
  not not_1 (quotient[22], subtractor_1_bout);
  Subtractor #(.width(23)) subtractor_2 (
    .a({multiplexer_1_out, dividende[21]}), .b(diviseur), .out(subtractor_2_out), .bout(subtractor_2_bout));  // open: bin
  not not_2 (quotient[21], subtractor_2_bout);
  Subtractor #(.width(23)) subtractor_3 (
    .a({multiplexer_2_out[21:0], dividende[20]}), .b(diviseur), .out(subtractor_3_out),
    .bout(subtractor_3_bout));  // open: bin
  not not_3 (quotient[20], subtractor_3_bout);
  Subtractor #(.width(23)) subtractor_4 (
    .a({multiplexer_3_out, dividende[19]}), .b(diviseur), .out(subtractor_4_out), .bout(subtractor_4_bout));  // open: bin
  not not_4 (quotient[19], subtractor_4_bout);
  Subtractor #(.width(23)) subtractor_5 (
    .a({multiplexer_4_out[21:0], dividende[18]}), .b(diviseur), .out(subtractor_5_out),
    .bout(subtractor_5_bout));  // open: bin
  not not_5 (quotient[18], subtractor_5_bout);
  Subtractor #(.width(23)) subtractor_6 (
    .a({multiplexer_5_out, dividende[17]}), .b(diviseur), .out(subtractor_6_out), .bout(subtractor_6_bout));  // open: bin
  not not_6 (quotient[17], subtractor_6_bout);
  Subtractor #(.width(23)) subtractor_7 (
    .a({multiplexer_6_out[21:0], dividende[16]}), .b(diviseur), .out(subtractor_7_out),
    .bout(subtractor_7_bout));  // open: bin
  not not_7 (quotient[16], subtractor_7_bout);
  Subtractor #(.width(23)) subtractor_8 (
    .a({multiplexer_7_out, dividende[15]}), .b(diviseur), .out(subtractor_8_out), .bout(subtractor_8_bout));  // open: bin
  not not_8 (quotient[15], subtractor_8_bout);
  Subtractor #(.width(23)) subtractor_9 (
    .a({multiplexer_8_out[21:0], dividende[14]}), .b(diviseur), .out(subtractor_9_out),
    .bout(subtractor_9_bout));  // open: bin
  not not_9 (quotient[14], subtractor_9_bout);
  Subtractor #(.width(23)) subtractor_10 (
    .a({multiplexer_9_out, dividende[13]}), .b(diviseur), .out(subtractor_10_out), .bout(subtractor_10_bout));  // open: bin
  not not_10 (quotient[13], subtractor_10_bout);
  Subtractor #(.width(23)) subtractor_11 (
    .a({multiplexer_10_out[21:0], dividende[12]}), .b(diviseur), .out(subtractor_11_out),
    .bout(subtractor_11_bout));  // open: bin
  not not_11 (quotient[12], subtractor_11_bout);
  Subtractor #(.width(23)) subtractor_12 (
    .a({multiplexer_11_out, dividende[11]}), .b(diviseur), .out(subtractor_12_out), .bout(subtractor_12_bout));  // open: bin
  not not_12 (quotient[11], subtractor_12_bout);
  Subtractor #(.width(23)) subtractor_13 (
    .a({multiplexer_12_out[21:0], dividende[10]}), .b(diviseur), .out(subtractor_13_out),
    .bout(subtractor_13_bout));  // open: bin
  not not_13 (quotient[10], subtractor_13_bout);
  Subtractor #(.width(23)) subtractor_14 (
    .a({multiplexer_13_out, dividende[9]}), .b(diviseur), .out(subtractor_14_out), .bout(subtractor_14_bout));  // open: bin
  not not_14 (quotient[9], subtractor_14_bout);
  Subtractor #(.width(23)) subtractor_15 (
    .a({multiplexer_14_out[21:0], dividende[8]}), .b(diviseur), .out(subtractor_15_out),
    .bout(subtractor_15_bout));  // open: bin
  not not_15 (quotient[8], subtractor_15_bout);
  Subtractor #(.width(23)) subtractor_16 (
    .a({multiplexer_15_out, dividende[7]}), .b(diviseur), .out(subtractor_16_out), .bout(subtractor_16_bout));  // open: bin
  not not_16 (quotient[7], subtractor_16_bout);
  Subtractor #(.width(23)) subtractor_17 (
    .a({multiplexer_16_out[21:0], dividende[6]}), .b(diviseur), .out(subtractor_17_out),
    .bout(subtractor_17_bout));  // open: bin
  not not_17 (quotient[6], subtractor_17_bout);
  Subtractor #(.width(23)) subtractor_18 (
    .a({multiplexer_17_out, dividende[5]}), .b(diviseur), .out(subtractor_18_out), .bout(subtractor_18_bout));  // open: bin
  not not_18 (quotient[5], subtractor_18_bout);
  Subtractor #(.width(23)) subtractor_19 (
    .a({multiplexer_18_out[21:0], dividende[4]}), .b(diviseur), .out(subtractor_19_out),
    .bout(subtractor_19_bout));  // open: bin
  not not_19 (quotient[4], subtractor_19_bout);
  Subtractor #(.width(23)) subtractor_20 (
    .a({multiplexer_19_out, dividende[3]}), .b(diviseur), .out(subtractor_20_out), .bout(subtractor_20_bout));  // open: bin
  not not_20 (quotient[3], subtractor_20_bout);
  Subtractor #(.width(23)) subtractor_21 (
    .a({multiplexer_20_out[21:0], dividende[2]}), .b(diviseur), .out(subtractor_21_out),
    .bout(subtractor_21_bout));  // open: bin
  not not_21 (quotient[2], subtractor_21_bout);
  Subtractor #(.width(23)) subtractor_22 (
    .a({multiplexer_21_out, dividende[1]}), .b(diviseur), .out(subtractor_22_out), .bout(subtractor_22_bout));  // open: bin
  not not_22 (quotient[1], subtractor_22_bout);
  Subtractor #(.width(23)) subtractor_23 (
    .a({multiplexer_22_out[21:0], dividende[0]}), .b(diviseur), .out(subtractor_23_out),
    .bout(subtractor_23_bout));  // open: bin
  not not_23 (quotient[0], subtractor_23_bout);
  Multiplexer #(.width(23), .enable("false")) multiplexer_1 (
    .in0({{22{1'b0}}, dividende[22]}), .in1(subtractor_1_out),
    .out({multiplexer_1_out_2[22], multiplexer_1_out}), .sel(quotient[22]));
  Multiplexer #(.width(23), .enable("false")) multiplexer_2 (
    .in0({multiplexer_1_out, dividende[21]}), .in1(subtractor_2_out), .out(multiplexer_2_out),
    .sel(quotient[21]));
  Multiplexer #(.width(23), .enable("false")) multiplexer_3 (
    .in0({multiplexer_2_out[21:0], dividende[20]}), .in1(subtractor_3_out),
    .out({multiplexer_3_out_2[22], multiplexer_3_out}), .sel(quotient[20]));
  Multiplexer #(.width(23), .enable("false")) multiplexer_4 (
    .in0({multiplexer_3_out, dividende[19]}), .in1(subtractor_4_out), .out(multiplexer_4_out),
    .sel(quotient[19]));
  Multiplexer #(.width(23), .enable("false")) multiplexer_5 (
    .in0({multiplexer_4_out[21:0], dividende[18]}), .in1(subtractor_5_out),
    .out({multiplexer_5_out_2[22], multiplexer_5_out}), .sel(quotient[18]));
  Multiplexer #(.width(23), .enable("false")) multiplexer_6 (
    .in0({multiplexer_5_out, dividende[17]}), .in1(subtractor_6_out), .out(multiplexer_6_out),
    .sel(quotient[17]));
  Multiplexer #(.width(23), .enable("false")) multiplexer_7 (
    .in0({multiplexer_6_out[21:0], dividende[16]}), .in1(subtractor_7_out),
    .out({multiplexer_7_out_2[22], multiplexer_7_out}), .sel(quotient[16]));
  Multiplexer #(.width(23), .enable("false")) multiplexer_8 (
    .in0({multiplexer_7_out, dividende[15]}), .in1(subtractor_8_out), .out(multiplexer_8_out),
    .sel(quotient[15]));
  Multiplexer #(.width(23), .enable("false")) multiplexer_9 (
    .in0({multiplexer_8_out[21:0], dividende[14]}), .in1(subtractor_9_out),
    .out({multiplexer_9_out_2[22], multiplexer_9_out}), .sel(quotient[14]));
  Multiplexer #(.width(23), .enable("false")) multiplexer_10 (
    .in0({multiplexer_9_out, dividende[13]}), .in1(subtractor_10_out), .out(multiplexer_10_out),
    .sel(quotient[13]));
  Multiplexer #(.width(23), .enable("false")) multiplexer_11 (
    .in0({multiplexer_10_out[21:0], dividende[12]}), .in1(subtractor_11_out),
    .out({multiplexer_11_out_2[22], multiplexer_11_out}), .sel(quotient[12]));
  Multiplexer #(.width(23), .enable("false")) multiplexer_12 (
    .in0({multiplexer_11_out, dividende[11]}), .in1(subtractor_12_out), .out(multiplexer_12_out),
    .sel(quotient[11]));
  Multiplexer #(.width(23), .enable("false")) multiplexer_13 (
    .in0({multiplexer_12_out[21:0], dividende[10]}), .in1(subtractor_13_out),
    .out({multiplexer_13_out_2[22], multiplexer_13_out}), .sel(quotient[10]));
  Multiplexer #(.width(23), .enable("false")) multiplexer_14 (
    .in0({multiplexer_13_out, dividende[9]}), .in1(subtractor_14_out), .out(multiplexer_14_out),
    .sel(quotient[9]));
  Multiplexer #(.width(23), .enable("false")) multiplexer_15 (
    .in0({multiplexer_14_out[21:0], dividende[8]}), .in1(subtractor_15_out),
    .out({multiplexer_15_out_2[22], multiplexer_15_out}), .sel(quotient[8]));
  Multiplexer #(.width(23), .enable("false")) multiplexer_16 (
    .in0({multiplexer_15_out, dividende[7]}), .in1(subtractor_16_out), .out(multiplexer_16_out),
    .sel(quotient[7]));
  Multiplexer #(.width(23), .enable("false")) multiplexer_17 (
    .in0({multiplexer_16_out[21:0], dividende[6]}), .in1(subtractor_17_out),
    .out({multiplexer_17_out_2[22], multiplexer_17_out}), .sel(quotient[6]));
  Multiplexer #(.width(23), .enable("false")) multiplexer_18 (
    .in0({multiplexer_17_out, dividende[5]}), .in1(subtractor_18_out), .out(multiplexer_18_out),
    .sel(quotient[5]));
  Multiplexer #(.width(23), .enable("false")) multiplexer_19 (
    .in0({multiplexer_18_out[21:0], dividende[4]}), .in1(subtractor_19_out),
    .out({multiplexer_19_out_2[22], multiplexer_19_out}), .sel(quotient[4]));
  Multiplexer #(.width(23), .enable("false")) multiplexer_20 (
    .in0({multiplexer_19_out, dividende[3]}), .in1(subtractor_20_out), .out(multiplexer_20_out),
    .sel(quotient[3]));
  Multiplexer #(.width(23), .enable("false")) multiplexer_21 (
    .in0({multiplexer_20_out[21:0], dividende[2]}), .in1(subtractor_21_out),
    .out({multiplexer_21_out_2[22], multiplexer_21_out}), .sel(quotient[2]));
  Multiplexer #(.width(23), .enable("false")) multiplexer_22 (
    .in0({multiplexer_21_out, dividende[1]}), .in1(subtractor_22_out), .out(multiplexer_22_out),
    .sel(quotient[1]));
  Multiplexer #(.width(23), .enable("false")) multiplexer_23 (
    .in0({multiplexer_22_out[21:0], dividende[0]}), .in1(subtractor_23_out), .out(reste), .sel(quotient[0]));
endmodule
